// Logisim project 16BitComputer.circ as structural Verilog: 15 circuits, main circuit main
module main (
  input  in_1,
  input  in_2
);

  wire alu_1_carryout, button_1_out, button_2_out, button_3_out, button_4_out, control_1_aluincrement,
       control_1_clr, control_1_counterenable, control_1_hlt, control_1_notain, control_1_notaout,
       control_1_notbin, control_1_notclr, control_1_notcounterout, control_1_notequationout,
       control_1_notflagsin, control_1_notinstructionin, control_1_notinstructionout, control_1_notjump,
       control_1_notmemoryin, control_1_notramout, control_1_outputin, control_1_ramin, control_1_rtcout,
       dipswitch_1_sw1, dipswitch_1_sw2, dipswitch_1_sw3, dipswitch_1_sw4, dipswitch_1_sw5, dipswitch_1_sw6,
       dipswitch_1_sw7, dipswitch_1_sw8, dipswitch_1_sw9, dipswitch_1_sw10, dipswitch_1_sw11,
       dipswitch_1_sw12, dipswitch_1_sw13, dipswitch_1_sw14, dipswitch_1_sw15, dipswitch_1_sw16,
       dipswitch_2_sw1, dipswitch_2_sw2, dipswitch_2_sw3, dipswitch_2_sw4, dipswitch_2_sw5, dipswitch_2_sw6,
       dipswitch_2_sw7, dipswitch_2_sw8, myclock_1_clk, myclock_1_notclk, registerflags_1_carryflag,
       registerflags_1_zeroflag, registermemoryaddress_1_programmingmode;
  wire [3:0] control_1_alucontrol;
  wire [7:0] registerinstructions_1_instructionout4_7, registermemoryaddress_1_adressout;
  wire [15:0] alu_1_aluout, outputshift_1_out_5, outputshift_1_out_6, outputshift_1_out_7,
       outputshift_1_out_8, outputshift_1_out_9, outputshift_1_out_10, outputshift_1_out_11,
       outputshift_1_out_12, outputshift_1_out_13, outputshift_1_out_14, outputshift_1_out_15,
       outputshift_1_out_16, outputshift_1_out_17, outputshift_1_out_18, outputshift_1_out_19,
       outputshift_1_out_20, registera_1_aout, registerb_1_bout, rtc_1_busout;

  Button button_1 (.out(button_1_out));
  Button button_2 (.out(button_2_out));
  DipSwitch #(.number(16)) dipswitch_1 (
    .sw1(dipswitch_1_sw1), .sw2(dipswitch_1_sw2), .sw3(dipswitch_1_sw3), .sw4(dipswitch_1_sw4),
    .sw5(dipswitch_1_sw5), .sw6(dipswitch_1_sw6), .sw7(dipswitch_1_sw7), .sw8(dipswitch_1_sw8),
    .sw9(dipswitch_1_sw9), .sw10(dipswitch_1_sw10), .sw11(dipswitch_1_sw11), .sw12(dipswitch_1_sw12),
    .sw13(dipswitch_1_sw13), .sw14(dipswitch_1_sw14), .sw15(dipswitch_1_sw15), .sw16(dipswitch_1_sw16));
  Button button_3 (.out(button_3_out));
  DipSwitch dipswitch_2 (
    .sw1(dipswitch_2_sw1), .sw2(dipswitch_2_sw2), .sw3(dipswitch_2_sw3), .sw4(dipswitch_2_sw4),
    .sw5(dipswitch_2_sw5), .sw6(dipswitch_2_sw6), .sw7(dipswitch_2_sw7), .sw8(dipswitch_2_sw8));
  RTC rtc_1 (
    .BusOut(rtc_1_busout), .CLK(myclock_1_clk), .RTCReset(button_1_out), .CLR(control_1_clr),
    .RTCOut(control_1_rtcout));
  MyClock myclock_1 (
    .NotCLK(myclock_1_notclk), .CLK(myclock_1_clk), .CLKSwitch(in_1), .CLKPush(button_3_out),
    .HLT(control_1_hlt));
  RegisterMemoryAddress registermemoryaddress_1 (
    .ProgrammingMode(registermemoryaddress_1_programmingmode), .AdressOut(registermemoryaddress_1_adressout),
    .BusIn(rtc_1_busout), .CLK(myclock_1_clk), .CLR(control_1_clr), .NotMemoryIn(control_1_notmemoryin),
    .Dip0In(dipswitch_2_sw8), .Dip1In(dipswitch_2_sw7), .Dip2In(dipswitch_2_sw6), .Dip3In(dipswitch_2_sw5),
    .Dip4In(dipswitch_2_sw4), .Dip5In(dipswitch_2_sw3), .Dip6In(dipswitch_2_sw2), .Dip7In(dipswitch_2_sw1),
    .ProgrammingSwitch(in_2));
  RAMModule rammodule_1 (
    .BusOut(rtc_1_busout), .ClockPush(button_2_out), .RAMIn(control_1_ramin), .CLK(myclock_1_clk),
    .ProgMode(registermemoryaddress_1_programmingmode), .Dip0In(dipswitch_1_sw16), .Dip1In(dipswitch_1_sw15),
    .Dip2In(dipswitch_1_sw14), .Dip3In(dipswitch_1_sw13), .Dip4In(dipswitch_1_sw12),
    .Dip5In(dipswitch_1_sw11), .Dip6In(dipswitch_1_sw10), .Dip7In(dipswitch_1_sw9), .Dip8In(dipswitch_1_sw8),
    .Dip9In(dipswitch_1_sw7), .Dip10In(dipswitch_1_sw6), .Dip11In(dipswitch_1_sw5),
    .Dip12In(dipswitch_1_sw4), .Dip13In(dipswitch_1_sw3), .Dip14In(dipswitch_1_sw2),
    .Dip15In(dipswitch_1_sw1), .BusIn(rtc_1_busout), .AddressIn(registermemoryaddress_1_adressout),
    .NotRAMOut(control_1_notramout));
  RegisterInstructions registerinstructions_1 (
    .BusOut(rtc_1_busout), .InstructionOut4_7(registerinstructions_1_instructionout4_7),
    .BusIn(rtc_1_busout), .CLK(myclock_1_clk), .CLR(control_1_clr),
    .NotInstructionIn(control_1_notinstructionin), .NotInstructionOut(control_1_notinstructionout));
  Button button_4 (.out(button_4_out));
  RegisterOutput registeroutput_1 (
    .BusIn(rtc_1_busout), .OutputIn(control_1_outputin), .CLK(myclock_1_clk), .NotCLR(control_1_notclr));
  LedBar #(.matrixcols(16)) ledbar_1 (
    .led0(rtc_1_busout[15]), .led1(rtc_1_busout[14]), .led2(rtc_1_busout[13]), .led3(rtc_1_busout[12]),
    .led4(rtc_1_busout[11]), .led5(rtc_1_busout[10]), .led6(rtc_1_busout[9]), .led7(rtc_1_busout[8]),
    .led8(rtc_1_busout[7]), .led9(rtc_1_busout[6]), .led10(rtc_1_busout[5]), .led11(rtc_1_busout[4]),
    .led12(rtc_1_busout[3]), .led13(rtc_1_busout[2]), .led14(rtc_1_busout[1]), .led15(rtc_1_busout[0]));
  ProgramCounter programcounter_1 (
    .BusOut(rtc_1_busout), .BusIn(rtc_1_busout), .NotJump(control_1_notjump), .CLK(myclock_1_clk),
    .NotCLR(control_1_notclr), .CounterEnable(control_1_counterenable),
    .NotCounterOut(control_1_notcounterout));
  RegisterA registera_1 (
    .AOut(registera_1_aout), .BusOut(rtc_1_busout), .BusIn(rtc_1_busout), .CLK(myclock_1_clk),
    .CLR(control_1_clr), .NotAIn(control_1_notain), .NotAOut(control_1_notaout));
  ALU alu_1 (
    .CarryOut(alu_1_carryout), .ALUOut(alu_1_aluout), .BusOut(rtc_1_busout), .AIn(registera_1_aout),
    .BIn(registerb_1_bout), .Increment(control_1_aluincrement), .ALUControl(control_1_alucontrol),
    .NotEOut(control_1_notequationout));
  RegisterB registerb_1 (
    .BOut(registerb_1_bout), .BusOut(rtc_1_busout), .BusIn(rtc_1_busout), .CLK(myclock_1_clk),
    .CLR(control_1_clr), .NotBIn(control_1_notbin), .NotBOut(1'b1));
  Control control_1 (
    .NotAOut(control_1_notaout), .NotAIn(control_1_notain), .NotInstructionIn(control_1_notinstructionin),
    .NotInstructionOut(control_1_notinstructionout), .NotRAMOut(control_1_notramout),
    .RAMIn(control_1_ramin), .NotMemoryIn(control_1_notmemoryin), .HLT(control_1_hlt),
    .RTCOut(control_1_rtcout), .NotFlagsIn(control_1_notflagsin), .NotJump(control_1_notjump),
    .NotCounterOut(control_1_notcounterout), .CounterEnable(control_1_counterenable),
    .OutputIn(control_1_outputin), .NotBIn(control_1_notbin), .ALUIncrement(control_1_aluincrement),
    .NotEquationOut(control_1_notequationout), .ALUControl(control_1_alucontrol), .CLR(control_1_clr),
    .NotCLR(control_1_notclr), .NotCLK(myclock_1_notclk), .PushReset(button_4_out),
    .InstructionIn(registerinstructions_1_instructionout4_7), .CarryFlag(registerflags_1_carryflag),
    .ZeroFlag(registerflags_1_zeroflag));  // open: NIU0, NIU1, NIU2, NIU3, NIU4, NIU5, NIU6, NIU7, NIU8, NIU9, NIU10
  RegisterFlags registerflags_1 (
    .ZeroFlag(registerflags_1_zeroflag), .CarryFlag(registerflags_1_carryflag), .CarryIn(alu_1_carryout),
    .CLK(myclock_1_clk), .CLR(control_1_clr), .NotFlagsIn(control_1_notflagsin), .ALUIn(alu_1_aluout));
  OutputShift outputshift_1 (
    .out_5(outputshift_1_out_5), .out_6(outputshift_1_out_6), .out_7(outputshift_1_out_7),
    .out_8(outputshift_1_out_8), .out_9(outputshift_1_out_9), .out_10(outputshift_1_out_10),
    .out_11(outputshift_1_out_11), .out_12(outputshift_1_out_12), .out_13(outputshift_1_out_13),
    .out_14(outputshift_1_out_14), .out_15(outputshift_1_out_15), .out_16(outputshift_1_out_16),
    .out_17(outputshift_1_out_17), .out_18(outputshift_1_out_18), .out_19(outputshift_1_out_19),
    .out_20(outputshift_1_out_20), .BusIn(rtc_1_busout), .CLK(myclock_1_clk), .CLR(control_1_clr),
    .OutputIn(control_1_outputin));
  Dec16Bit dec16bit_1 (.DataIn(outputshift_1_out_5));
  Dec16Bit dec16bit_2 (.DataIn(outputshift_1_out_6));
  Dec16Bit dec16bit_3 (.DataIn(outputshift_1_out_7));
  Dec16Bit dec16bit_4 (.DataIn(outputshift_1_out_8));
  Dec16Bit dec16bit_5 (.DataIn(outputshift_1_out_9));
  Dec16Bit dec16bit_6 (.DataIn(outputshift_1_out_10));
  Dec16Bit dec16bit_7 (.DataIn(outputshift_1_out_11));
  Dec16Bit dec16bit_8 (.DataIn(outputshift_1_out_12));
  Dec16Bit dec16bit_9 (.DataIn(outputshift_1_out_13));
  Dec16Bit dec16bit_10 (.DataIn(outputshift_1_out_14));
  Dec16Bit dec16bit_11 (.DataIn(outputshift_1_out_15));
  Dec16Bit dec16bit_12 (.DataIn(outputshift_1_out_16));
  Dec16Bit dec16bit_13 (.DataIn(outputshift_1_out_17));
  Dec16Bit dec16bit_14 (.DataIn(outputshift_1_out_18));
  Dec16Bit dec16bit_15 (.DataIn(outputshift_1_out_19));
  Dec16Bit dec16bit_16 (.DataIn(outputshift_1_out_20));
endmodule

module MyClock (
  input  CLKSwitch,
  input  CLKPush,
  input  HLT,
  output NotCLK,
  output CLK
);

  wire and_1_out, and_2_out, clock_1_out, not_1_out, not_2_out, or_1_out;

  Clock clock_1 (.out(clock_1_out));
  not not_1 (not_1_out, CLKSwitch);
  and and_1 (and_1_out, clock_1_out, CLKSwitch);
  LED led_1 (.in(CLKSwitch));
  LED led_2 (.in(not_1_out));
  and and_2 (and_2_out, not_1_out, CLKPush);
  or or_1 (or_1_out, and_1_out, and_2_out);
  not not_2 (not_2_out, HLT);
  and and_3 (CLK, or_1_out, not_2_out);
  not not_3 (NotCLK, CLK);
  LED led_3 (.in(CLK));
endmodule

module RegisterA (
  input  [15:0] BusIn,
  input  CLK,
  input  CLR,
  input  NotAIn,
  input  NotAOut,
  output [15:0] AOut,
  output [15:0] BusOut
);

  wire not_1_out, not_2_out;
  wire [15:0] divider_1_out, divider_1_rem;

  Register #(.width(16)) register_1 (.D(BusIn), .en(not_1_out), .clk(CLK), .Q(AOut), .clr(CLR));
  not not_1 (not_1_out, NotAIn);
  assign BusOut = not_2_out ? AOut : 16'bz;  // Controlled_Buffer controlled_buffer_1
  not not_2 (not_2_out, NotAOut);
  // Probe on AOut
  // Probe on 16'h3e8
  Divider #(.width(16)) divider_1 (.a(AOut), .b(16'h3e8), .out(divider_1_out), .rem(divider_1_rem));  // open: upper
  // Probe on divider_1_out
  // Probe on divider_1_rem
  // Binary_to_BCD_converter #(.binvalue(8)) binary_to_bcd_converter_1: pin names not known; wires that end beside it: divider_1_out[7:0]
  _7_Segment_Display u_7_segment_display_1 ();  // open: g, f, a, b, e, d, c, dp
  _7_Segment_Display u_7_segment_display_2 ();  // open: g, f, a, b, e, d, c, dp
  // BCD_to_7_Segment_decoder bcd_to_7_segment_decoder_1: pin names not known
  // BCD_to_7_Segment_decoder bcd_to_7_segment_decoder_2: pin names not known
  // Binary_to_BCD_converter #(.binvalue(10)) binary_to_bcd_converter_2: pin names not known; wires that end beside it: divider_1_rem[9:0]
  _7_Segment_Display u_7_segment_display_3 ();  // open: g, f, a, b, e, d, c, dp
  // BCD_to_7_Segment_decoder bcd_to_7_segment_decoder_3: pin names not known
  _7_Segment_Display u_7_segment_display_4 ();  // open: g, f, a, b, e, d, c, dp
  _7_Segment_Display u_7_segment_display_5 ();  // open: g, f, a, b, e, d, c, dp
  // BCD_to_7_Segment_decoder bcd_to_7_segment_decoder_4: pin names not known
  // BCD_to_7_Segment_decoder bcd_to_7_segment_decoder_5: pin names not known
endmodule

module RegisterB (
  input  [15:0] BusIn,
  input  CLK,
  input  CLR,
  input  NotBIn,
  input  NotBOut,
  output [15:0] BOut,
  output [15:0] BusOut
);

  wire not_1_out, not_2_out;
  wire [15:0] divider_1_out, divider_1_rem;

  Register #(.width(16)) register_1 (.D(BusIn), .en(not_1_out), .clk(CLK), .Q(BOut), .clr(CLR));
  not not_1 (not_1_out, NotBIn);
  assign BusOut = not_2_out ? BOut : 16'bz;  // Controlled_Buffer controlled_buffer_1
  not not_2 (not_2_out, NotBOut);
  // Probe on BOut
  // Probe on 16'h3e8
  Divider #(.width(16)) divider_1 (.a(BOut), .b(16'h3e8), .out(divider_1_out), .rem(divider_1_rem));  // open: upper
  // Probe on divider_1_out
  // Probe on divider_1_rem
  // Binary_to_BCD_converter #(.binvalue(8)) binary_to_bcd_converter_1: pin names not known; wires that end beside it: divider_1_out[7:0]
  _7_Segment_Display u_7_segment_display_1 ();  // open: g, f, a, b, e, d, c, dp
  // BCD_to_7_Segment_decoder bcd_to_7_segment_decoder_1: pin names not known
  _7_Segment_Display u_7_segment_display_2 ();  // open: g, f, a, b, e, d, c, dp
  // BCD_to_7_Segment_decoder bcd_to_7_segment_decoder_2: pin names not known
  _7_Segment_Display u_7_segment_display_3 ();  // open: g, f, a, b, e, d, c, dp
  // BCD_to_7_Segment_decoder bcd_to_7_segment_decoder_3: pin names not known
  // Binary_to_BCD_converter #(.binvalue(10)) binary_to_bcd_converter_2: pin names not known; wires that end beside it: divider_1_rem[9:0]
  _7_Segment_Display u_7_segment_display_4 ();  // open: g, f, a, b, e, d, c, dp
  // BCD_to_7_Segment_decoder bcd_to_7_segment_decoder_4: pin names not known
  _7_Segment_Display u_7_segment_display_5 ();  // open: g, f, a, b, e, d, c, dp
  // BCD_to_7_Segment_decoder bcd_to_7_segment_decoder_5: pin names not known
endmodule

module RegisterInstructions (
  input  [15:0] BusIn,
  input  CLK,
  input  CLR,
  input  NotInstructionIn,
  input  NotInstructionOut,
  output [7:0] InstructionOut4_7,
  output [15:0] BusOut
);

  wire not_1_out, not_2_out;
  wire [7:0] register_1_q;

  Register #(.width(16)) register_1 (
    .D(BusIn), .en(not_1_out), .clk(CLK), .Q({InstructionOut4_7, register_1_q}), .clr(CLR));
  not not_1 (not_1_out, NotInstructionIn);
  Hex_Digit_Display hex_digit_display_1 (.value(InstructionOut4_7[7:4]));  // open: dp
  Hex_Digit_Display hex_digit_display_2 (.value(InstructionOut4_7[3:0]));  // open: dp
  Hex_Digit_Display hex_digit_display_3 (.value(register_1_q[7:4]));  // open: dp
  assign BusOut = not_2_out ? {{8{1'b0}}, register_1_q} : 16'bz;  // Controlled_Buffer controlled_buffer_1
  not not_2 (not_2_out, NotInstructionOut);
  Hex_Digit_Display hex_digit_display_4 (.value(register_1_q[3:0]));  // open: dp
endmodule

module ALU (
  input  Increment,
  input  [3:0] ALUControl,
  input  [15:0] AIn,
  input  NotEOut,
  input  [15:0] BIn,
  output CarryOut,
  output [15:0] BusOut,
  output [15:0] ALUOut
);

  wire adder_1_cout, adder_2_cout, adder_3_cout, adder_4_cout, and_2_out, multiplexer_1_out,
       multiplexer_2_out, not_4_out;
  wire [4:0] bitadder_1_out;
  wire [15:0] adder_1_out, adder_2_out, adder_3_out, adder_4_out, and_1_out, bit_extender_1_out,
       divider_1_out, divider_1_rem, divider_2_out, divider_2_rem, multiplexer_3_out, multiplexer_5_out,
       multiplier_1_cout, multiplier_1_out, not_1_out, not_2_out, not_3_out, or_1_out, shifter_1_out,
       shifter_2_out, shifter_3_out, shifter_4_out, shifter_5_out, xor_1_out;

  assign not_1_out = ~BIn;  // NOT_Gate not_1, 16 bits wide
  assign bit_extender_1_out = {{13{ALUControl[2]}}, ALUControl[2:0]};  // Bit_Extender bit_extender_1
  Adder #(.width(16)) adder_1 (.a(AIn), .b(BIn), .out(adder_1_out), .cout(adder_1_cout));  // open: cin
  Adder #(.width(16)) adder_2 (.a(AIn), .b(not_1_out), .out(adder_2_out), .cin(1'b1), .cout(adder_2_cout));
  Multiplier #(.width(16)) multiplier_1 (
    .a(AIn), .b(BIn), .out(multiplier_1_out), .cout(multiplier_1_cout));  // open: cin
  Divider #(.width(16)) divider_1 (.a(AIn), .b(BIn), .out(divider_1_out), .rem(divider_1_rem));  // open: upper
  assign and_1_out = AIn & BIn;  // AND_Gate and_1, 16 bits wide
  assign or_1_out = AIn | BIn;  // OR_Gate or_1, 16 bits wide
  assign xor_1_out = AIn ^ BIn;  // XOR_Gate xor_1, 16 bits wide
  assign not_2_out = ~AIn;  // NOT_Gate not_2, 16 bits wide
  Shifter #(.width(16)) shifter_1 (.in(AIn), .\dist (BIn[3:0]), .out(shifter_1_out));
  Shifter #(.shift("lr"), .width(16)) shifter_2 (.in(AIn), .\dist (BIn[3:0]), .out(shifter_2_out));
  Shifter #(.shift("ar"), .width(16)) shifter_3 (.in(AIn), .\dist (BIn[3:0]), .out(shifter_3_out));
  Shifter #(.shift("rl"), .width(16)) shifter_4 (.in(AIn), .\dist (BIn[3:0]), .out(shifter_4_out));
  Shifter #(.shift("rr"), .width(16)) shifter_5 (.in(AIn), .\dist (BIn[3:0]), .out(shifter_5_out));
  BitAdder #(.width(16)) bitadder_1 (.in0(AIn), .out(bitadder_1_out));
  assign not_3_out = ~bit_extender_1_out;  // NOT_Gate not_3, 16 bits wide
  Adder #(.width(16)) adder_3 (.a(AIn), .b(bit_extender_1_out), .out(adder_3_out), .cout(adder_3_cout));  // open: cin
  Multiplexer multiplexer_1 (.in0(adder_3_cout), .in1(adder_4_cout), .out(multiplexer_1_out), .sel(ALUControl[3]));
  Adder #(.width(16)) adder_4 (.a(AIn), .b(not_3_out), .out(adder_4_out), .cin(1'b1), .cout(adder_4_cout));
  Multiplexer multiplexer_2 (.in0(adder_1_cout), .in1(adder_2_cout), .out(multiplexer_2_out), .sel(ALUControl[0]));
  and and_2 (and_2_out, multiplexer_2_out, ~ALUControl[1], ~ALUControl[2], ~ALUControl[3]);  // AND_Gate
  Multiplexer #(.select(4), .width(16)) multiplexer_3 (
    .in0(adder_1_out), .in1(adder_2_out), .in2(multiplier_1_out), .in3(multiplier_1_cout),
    .in4(divider_1_out), .in5(divider_1_rem), .in6(and_1_out), .in7(or_1_out), .in8(xor_1_out),
    .in9(not_2_out), .in10(shifter_1_out), .in11(shifter_2_out), .in12(shifter_3_out), .in13(shifter_4_out),
    .in14(shifter_5_out), .in15({{11{1'b0}}, bitadder_1_out}), .out(multiplexer_3_out), .sel(ALUControl));
  Multiplexer #(.width(16)) multiplexer_4 (
    .in0(multiplexer_3_out), .in1(multiplexer_5_out), .out(ALUOut), .sel(Increment));
  Multiplexer #(.width(16)) multiplexer_5 (
    .in0(adder_3_out), .in1(adder_4_out), .out(multiplexer_5_out), .sel(ALUControl[3]));
  Multiplexer multiplexer_6 (.in0(and_2_out), .in1(multiplexer_1_out), .out(CarryOut), .sel(Increment));
  // Probe on ALUOut
  // Probe on 16'h3e8
  Divider #(.width(16)) divider_2 (.a(ALUOut), .b(16'h3e8), .out(divider_2_out), .rem(divider_2_rem));  // open: upper
  // Probe on divider_2_out
  // Probe on divider_2_rem
  assign BusOut = not_4_out ? ALUOut : 16'bz;  // Controlled_Buffer controlled_buffer_1
  not not_4 (not_4_out, NotEOut);
  // Binary_to_BCD_converter #(.binvalue(8)) binary_to_bcd_converter_1: pin names not known; wires that end beside it: divider_2_out[7:0]
  _7_Segment_Display u_7_segment_display_1 ();  // open: g, f, a, b, e, d, c, dp
  // BCD_to_7_Segment_decoder bcd_to_7_segment_decoder_1: pin names not known
  _7_Segment_Display u_7_segment_display_2 ();  // open: g, f, a, b, e, d, c, dp
  // BCD_to_7_Segment_decoder bcd_to_7_segment_decoder_2: pin names not known
  _7_Segment_Display u_7_segment_display_3 ();  // open: g, f, a, b, e, d, c, dp
  // BCD_to_7_Segment_decoder bcd_to_7_segment_decoder_3: pin names not known
  // Binary_to_BCD_converter #(.binvalue(10)) binary_to_bcd_converter_2: pin names not known; wires that end beside it: divider_2_rem[9:0]
  _7_Segment_Display u_7_segment_display_4 ();  // open: g, f, a, b, e, d, c, dp
  // BCD_to_7_Segment_decoder bcd_to_7_segment_decoder_4: pin names not known
  _7_Segment_Display u_7_segment_display_5 ();  // open: g, f, a, b, e, d, c, dp
  // BCD_to_7_Segment_decoder bcd_to_7_segment_decoder_5: pin names not known
endmodule

module RegisterFlags (
  input  [15:0] ALUIn,
  input  CarryIn,
  input  CLK,
  input  CLR,
  input  NotFlagsIn,
  output ZeroFlag,
  output CarryFlag
);

  wire not_1_out;
  wire [0:0] nor_1_out;

  nor nor_1 (nor_1_out[0], ALUIn[0], ALUIn[1], ALUIn[2], ALUIn[3], ALUIn[4], ALUIn[5], ALUIn[6], ALUIn[7], ALUIn[8], ALUIn[9], ALUIn[10], ALUIn[11], ALUIn[12], ALUIn[13], ALUIn[14], ALUIn[15]);
  not not_1 (not_1_out, NotFlagsIn);
  Register #(.width(2)) register_1 (
    .D({CarryIn, nor_1_out[0]}), .en(not_1_out), .clk(CLK), .Q({CarryFlag, ZeroFlag}), .clr(CLR));
  LED led_1 (.in(ZeroFlag));
  LED led_2 (.in(CarryFlag));
endmodule

module RegisterMemoryAddress (
  input  [15:0] BusIn,
  input  CLK,
  input  CLR,
  input  NotMemoryIn,
  input  Dip0In,
  input  Dip1In,
  input  Dip2In,
  input  Dip3In,
  input  Dip4In,
  input  Dip5In,
  input  ProgrammingSwitch,
  input  Dip6In,
  input  Dip7In,
  output [7:0] AdressOut,
  output ProgrammingMode
);

  wire not_1_out, not_2_out;
  wire [7:0] register_1_q;

  Register register_1 (.D(BusIn[7:0]), .en(not_1_out), .clk(CLK), .Q(register_1_q), .clr(CLR));
  not not_1 (not_1_out, NotMemoryIn);
  LED led_1 (.in(AdressOut[0]));
  LED led_2 (.in(AdressOut[1]));
  LED led_3 (.in(AdressOut[2]));
  LED led_4 (.in(AdressOut[3]));
  LED led_5 (.in(AdressOut[4]));
  LED led_6 (.in(AdressOut[5]));
  LED led_7 (.in(AdressOut[6]));
  LED led_8 (.in(AdressOut[7]));
  Multiplexer #(.width(8)) multiplexer_1 (
    .in0(register_1_q), .in1({Dip7In, Dip6In, Dip5In, Dip4In, Dip3In, Dip2In, Dip1In, Dip0In}),
    .out(AdressOut), .sel(ProgrammingSwitch));
  LED led_9 (.in(ProgrammingSwitch));
  not not_2 (not_2_out, ProgrammingSwitch);
  LED led_10 (.in(not_2_out));
  _7_Segment_Display u_7_segment_display_1 ();  // open: g, f, a, b, e, d, c, dp
  // BCD_to_7_Segment_decoder bcd_to_7_segment_decoder_1: pin names not known
  // Binary_to_BCD_converter #(.binvalue(8)) binary_to_bcd_converter_1: pin names not known; wires that end beside it: AdressOut
  Hex_Digit_Display hex_digit_display_1 (.value(AdressOut[7:4]));  // open: dp
  Hex_Digit_Display hex_digit_display_2 (.value(AdressOut[3:0]));  // open: dp
  _7_Segment_Display u_7_segment_display_2 ();  // open: g, f, a, b, e, d, c, dp
  // BCD_to_7_Segment_decoder bcd_to_7_segment_decoder_2: pin names not known
  _7_Segment_Display u_7_segment_display_3 ();  // open: g, f, a, b, e, d, c, dp
  // BCD_to_7_Segment_decoder bcd_to_7_segment_decoder_3: pin names not known

  assign ProgrammingMode = ProgrammingSwitch;
endmodule

module RAMModule (
  input  [7:0] AddressIn,
  input  NotRAMOut,
  input  ClockPush,
  input  RAMIn,
  input  CLK,
  input  ProgMode,
  input  Dip0In,
  input  [15:0] BusIn,
  input  Dip1In,
  input  Dip2In,
  input  Dip3In,
  input  Dip4In,
  input  Dip5In,
  input  Dip6In,
  input  Dip7In,
  input  Dip8In,
  input  Dip9In,
  input  Dip10In,
  input  Dip11In,
  input  Dip12In,
  input  Dip13In,
  input  Dip14In,
  input  Dip15In,
  output [15:0] BusOut
);

  wire multiplexer_1_out, nand_1_out, not_1_out, not_2_out, not_3_out, not_4_out;
  wire [3:0] ram_1_dout, ram_1_dout_2, ram_1_dout_3, ram_1_dout_4;
  wire [15:0] multiplexer_2_out, multiplexer_3_out;

  not not_1 (not_1_out, ClockPush);
  nand nand_1 (nand_1_out, RAMIn, CLK);
  not not_2 (not_2_out, ProgMode);
  not not_3 (not_3_out, multiplexer_1_out);
  Multiplexer multiplexer_1 (.in0(not_1_out), .in1(nand_1_out), .out(multiplexer_1_out), .sel(not_2_out));
  Multiplexer #(.width(16)) multiplexer_2 (
    .in0({Dip15In, Dip14In, Dip13In, Dip12In, Dip11In, Dip10In, Dip9In, Dip8In, Dip7In, Dip6In, Dip5In, Dip4In, Dip3In, Dip2In, Dip1In, Dip0In}),
    .in1(BusIn), .out(multiplexer_2_out), .sel(not_2_out));
  RAM #(.dataWidth(16), .trigger("high"), .\type ("nonvolatile")) ram_1 (
    .addr(AddressIn), .we(not_3_out), .oe(1'b1), .din(multiplexer_2_out),
    .dout({ram_1_dout_4, ram_1_dout_3, ram_1_dout_2, ram_1_dout}));
  Hex_Digit_Display hex_digit_display_1 (.value(ram_1_dout_4));  // open: dp
  Hex_Digit_Display hex_digit_display_2 (.value(ram_1_dout_3));  // open: dp
  Hex_Digit_Display hex_digit_display_3 (.value(ram_1_dout_2));  // open: dp
  Hex_Digit_Display hex_digit_display_4 (.value(multiplexer_3_out[15:12]));  // open: dp
  Hex_Digit_Display hex_digit_display_5 (.value(multiplexer_3_out[11:8]));  // open: dp
  Multiplexer #(.width(16)) multiplexer_3 (
    .in0({Dip15In, Dip14In, Dip13In, Dip12In, Dip11In, Dip10In, Dip9In, Dip8In, Dip7In, Dip6In, Dip5In, Dip4In, Dip3In, Dip2In, Dip1In, Dip0In}),
    .in1({ram_1_dout_4, ram_1_dout_3, ram_1_dout_2, ram_1_dout}), .out(multiplexer_3_out), .sel(not_2_out));
  not not_4 (not_4_out, NotRAMOut);
  assign BusOut = not_4_out ? {ram_1_dout_4, ram_1_dout_3, ram_1_dout_2, ram_1_dout} : 16'bz;  // Controlled_Buffer controlled_buffer_1
  Hex_Digit_Display hex_digit_display_6 (.value(ram_1_dout));  // open: dp
  LED led_1 (.in(ram_1_dout[0]));
  LED led_2 (.in(ram_1_dout[1]));
  LED led_3 (.in(ram_1_dout[2]));
  LED led_4 (.in(ram_1_dout[3]));
  LED led_5 (.in(ram_1_dout_2[0]));
  LED led_6 (.in(ram_1_dout_2[1]));
  LED led_7 (.in(ram_1_dout_2[2]));
  LED led_8 (.in(ram_1_dout_2[3]));
  LED led_9 (.in(ram_1_dout_3[0]));
  LED led_10 (.in(ram_1_dout_3[1]));
  LED led_11 (.in(ram_1_dout_3[2]));
  LED led_12 (.in(ram_1_dout_3[3]));
  LED led_13 (.in(ram_1_dout_4[0]));
  LED led_14 (.in(ram_1_dout_4[1]));
  LED led_15 (.in(ram_1_dout_4[2]));
  LED led_16 (.in(ram_1_dout_4[3]));
  Hex_Digit_Display hex_digit_display_7 (.value(multiplexer_3_out[7:4]));  // open: dp
  Hex_Digit_Display hex_digit_display_8 (.value(multiplexer_3_out[3:0]));  // open: dp
endmodule

module RegisterOutput (
  input  [15:0] BusIn,
  input  OutputIn,
  input  CLK,
  input  NotCLR
);

  wire and_1_out, not_1_out;
  wire [15:0] divider_1_out, divider_1_rem, register_1_q;

  Register #(.width(16)) register_1 (.D(BusIn), .en(1'b1), .clk(and_1_out), .Q(register_1_q), .clr(not_1_out));
  and and_1 (and_1_out, OutputIn, CLK);
  not not_1 (not_1_out, NotCLR);
  // Probe on register_1_q
  // Probe on 16'h3e8
  Divider #(.width(16)) divider_1 (
    .a(register_1_q), .b(16'h3e8), .out(divider_1_out), .rem(divider_1_rem));  // open: upper
  // Probe on divider_1_out
  // Probe on divider_1_rem
  // Binary_to_BCD_converter #(.binvalue(8)) binary_to_bcd_converter_1: pin names not known; wires that end beside it: divider_1_out[7:0]
  _7_Segment_Display u_7_segment_display_1 ();  // open: g, f, a, b, e, d, c, dp
  _7_Segment_Display u_7_segment_display_2 ();  // open: g, f, a, b, e, d, c, dp
  // BCD_to_7_Segment_decoder bcd_to_7_segment_decoder_1: pin names not known
  // BCD_to_7_Segment_decoder bcd_to_7_segment_decoder_2: pin names not known
  // Binary_to_BCD_converter #(.binvalue(10)) binary_to_bcd_converter_2: pin names not known; wires that end beside it: divider_1_rem[9:0]
  _7_Segment_Display u_7_segment_display_3 ();  // open: g, f, a, b, e, d, c, dp
  // BCD_to_7_Segment_decoder bcd_to_7_segment_decoder_3: pin names not known
  _7_Segment_Display u_7_segment_display_4 ();  // open: g, f, a, b, e, d, c, dp
  _7_Segment_Display u_7_segment_display_5 ();  // open: g, f, a, b, e, d, c, dp
  // BCD_to_7_Segment_decoder bcd_to_7_segment_decoder_4: pin names not known
  // BCD_to_7_Segment_decoder bcd_to_7_segment_decoder_5: pin names not known
endmodule

module ProgramCounter (
  input  [15:0] BusIn,
  input  NotJump,
  input  CLK,
  input  NotCLR,
  input  CounterEnable,
  input  NotCounterOut,
  output [15:0] BusOut
);

  wire not_1_out, not_2_out, not_3_out;
  wire [7:0] counter_1_q;

  not not_1 (not_1_out, NotJump);
  not not_2 (not_2_out, NotCLR);
  Counter counter_1 (
    .clr(not_2_out), .load(not_1_out), .up(1'b1), .count(CounterEnable), .clk(CLK), .D(BusIn[7:0]),
    .Q(counter_1_q));  // open: carry
  LED led_1 (.in(counter_1_q[0]));
  LED led_2 (.in(counter_1_q[1]));
  LED led_3 (.in(counter_1_q[2]));
  LED led_4 (.in(counter_1_q[3]));
  LED led_5 (.in(counter_1_q[4]));
  LED led_6 (.in(counter_1_q[5]));
  LED led_7 (.in(counter_1_q[6]));
  LED led_8 (.in(counter_1_q[7]));
  Hex_Digit_Display hex_digit_display_1 (.value(counter_1_q[7:4]));  // open: dp
  assign BusOut = not_3_out ? {{8{1'b0}}, counter_1_q} : 16'bz;  // Controlled_Buffer controlled_buffer_1
  not not_3 (not_3_out, NotCounterOut);
  _7_Segment_Display u_7_segment_display_1 ();  // open: g, f, a, b, e, d, c, dp
  // BCD_to_7_Segment_decoder bcd_to_7_segment_decoder_1: pin names not known
  // Binary_to_BCD_converter #(.binvalue(8)) binary_to_bcd_converter_1: pin names not known; wires that end beside it: counter_1_q
  Hex_Digit_Display hex_digit_display_2 (.value(counter_1_q[3:0]));  // open: dp
  _7_Segment_Display u_7_segment_display_2 ();  // open: g, f, a, b, e, d, c, dp
  // BCD_to_7_Segment_decoder bcd_to_7_segment_decoder_2: pin names not known
  _7_Segment_Display u_7_segment_display_3 ();  // open: g, f, a, b, e, d, c, dp
  // BCD_to_7_Segment_decoder bcd_to_7_segment_decoder_3: pin names not known
endmodule

module Control (
  input  [7:0] InstructionIn,
  input  NotCLK,
  input  CarryFlag,
  input  ZeroFlag,
  input  PushReset,
  output NIU0,
  output NIU1,
  output NIU2,
  output NIU3,
  output NIU4,
  output NIU5,
  output NIU6,
  output NIU7,
  output NIU8,
  output NIU9,
  output NIU10,
  output RTCOut,
  output CLR,
  output NotFlagsIn,
  output NotCLR,
  output NotJump,
  output NotCounterOut,
  output CounterEnable,
  output OutputIn,
  output NotBIn,
  output ALUIncrement,
  output NotEquationOut,
  output [3:0] ALUControl,
  output NotAOut,
  output NotAIn,
  output NotInstructionIn,
  output NotInstructionOut,
  output NotRAMOut,
  output RAMIn,
  output NotMemoryIn,
  output HLT
);

  wire decoder_1_out0, decoder_1_out1, decoder_1_out2, decoder_1_out3, decoder_1_out4, decoder_1_out5,
       nand_1_out, not_1_out;
  wire [2:0] counter_1_q_2;
  wire [3:3] counter_1_q;
  wire [30:12] rom_1_data;

  Counter #(.max('hf), .width(4)) counter_1 (
    .clr(not_1_out), .load(1'b0), .up(1'b1), .count(1'b1), .clk(NotCLK), .Q({counter_1_q[3], counter_1_q_2}));  // open: D, carry
  not not_1 (not_1_out, nand_1_out);
  LED led_1 (.in(decoder_1_out0));
  LED led_2 (.in(decoder_1_out1));
  LED led_3 (.in(decoder_1_out2));
  nand nand_1 (nand_1_out, decoder_1_out5, NotCLR);
  LED led_4 (.in(decoder_1_out3));
  LED led_5 (.in(decoder_1_out4));
  not not_2 (NotCLR, PushReset);
  _7_Segment_Display u_7_segment_display_1 ();  // open: g, f, a, b, e, d, c, dp
  // BCD_to_7_Segment_decoder bcd_to_7_segment_decoder_1: pin names not known; wires that end beside it: {counter_1_q[3], counter_1_q_2}
  Decoder #(.select(3)) decoder_1 (
    .out0(decoder_1_out0), .out1(decoder_1_out1), .out2(decoder_1_out2), .out3(decoder_1_out3),
    .out4(decoder_1_out4), .out5(decoder_1_out5), .sel(counter_1_q_2), .en(1'b1));  // open: out6, out7
  not not_3 (CLR, NotCLR);
  LED led_6 (.in(counter_1_q_2[0]));
  LED led_7 (.in(counter_1_q_2[1]));
  LED led_8 (.in(counter_1_q_2[2]));
  ROM #(.addrWidth(16), .dataWidth(32)) rom_1 (
    .addr({2'b00, ZeroFlag, CarryFlag, InstructionIn, 1'b0, counter_1_q_2}),
    .data({HLT, rom_1_data[30], RAMIn, rom_1_data[28:24], ALUControl, rom_1_data[19], ALUIncrement, rom_1_data[17], OutputIn, CounterEnable, rom_1_data[14:12], RTCOut, NIU10, NIU9, NIU8, NIU7, NIU6, NIU5, NIU4, NIU3, NIU2, NIU1, NIU0}));
  LED led_9 (.in(NIU0));
  LED led_10 (.in(NIU1));
  LED led_11 (.in(NIU2));
  LED led_12 (.in(NIU3));
  LED led_13 (.in(NIU4));
  LED led_14 (.in(NIU5));
  LED led_15 (.in(NIU6));
  LED led_16 (.in(NIU7));
  LED led_17 (.in(NIU8));
  LED led_18 (.in(NIU9));
  LED led_19 (.in(NIU10));
  LED led_20 (.in(RTCOut));
  LED led_21 (.in(rom_1_data[12]));
  LED led_22 (.in(rom_1_data[13]));
  LED led_23 (.in(rom_1_data[14]));
  LED led_24 (.in(CounterEnable));
  LED led_25 (.in(OutputIn));
  LED led_26 (.in(rom_1_data[17]));
  LED led_27 (.in(ALUIncrement));
  LED led_28 (.in(rom_1_data[19]));
  LED led_29 (.in(ALUControl[0]));
  LED led_30 (.in(ALUControl[1]));
  LED led_31 (.in(ALUControl[2]));
  LED led_32 (.in(ALUControl[3]));
  LED led_33 (.in(rom_1_data[24]));
  LED led_34 (.in(rom_1_data[25]));
  LED led_35 (.in(rom_1_data[26]));
  LED led_36 (.in(rom_1_data[27]));
  LED led_37 (.in(rom_1_data[28]));
  LED led_38 (.in(RAMIn));
  LED led_39 (.in(rom_1_data[30]));
  LED led_40 (.in(HLT));
  not not_4 (NotFlagsIn, rom_1_data[12]);
  not not_5 (NotJump, rom_1_data[13]);
  not not_6 (NotCounterOut, rom_1_data[14]);
  not not_7 (NotBIn, rom_1_data[17]);
  not not_8 (NotEquationOut, rom_1_data[19]);
  not not_9 (NotAOut, rom_1_data[24]);
  not not_10 (NotAIn, rom_1_data[25]);
  not not_11 (NotInstructionIn, rom_1_data[26]);
  not not_12 (NotInstructionOut, rom_1_data[27]);
  not not_13 (NotRAMOut, rom_1_data[28]);
  not not_14 (NotMemoryIn, rom_1_data[30]);

  // Notes on the sheet:
  //   contents of rom_1 (hex, n*v repeats v):
  //   40004000 14008000 14*0 40004000 14008000 48000000 12000000 12*0 40004000 14008000 48000000 10020000
  //   2081000 11*0 40004000 14008000 48000000 10020000 2181000 11*0 40004000 14008000 48000000 21000000
  //   12*0 40004000 14008000 a000000 13*0 40004000 14008000 8002000 13*0 40004000 14008000 14*0 40004000
  //   14008000 14*0 40004000 14008000 48000000 12000000 201c1000 11*0 40004000 14008000 48000000 12000000
  //   209c1000 11*0 40004000 14008000 a000000 13*0 40004000 14008000 48000000 20000800 12*0 40004000
  //   14008000 48000000 10020000 101000 11*0 40004000 14008000 1010000 13*0 40004000 14008000 80000000
  //   13*0 40004000 14008000 48000000 10020000 2081000 11*0 40004000 14008000 48000000 10020000 2181000
  //   11*0 40004000 14008000 48000000 10020000 2281000 11*0 40004000 14008000 48000000 10020000 2381000
  //   11*0 40004000 14008000 48000000 10020000 2481000 11*0 40004000 14008000 48000000 10020000 2581000
  //   11*0 40004000 14008000 48000000 10020000 2681000 11*0 40004000 14008000 48000000 10020000 2781000
  //   11*0 40004000 14008000 48000000 10020000 2881000 11*0 40004000 14008000 48000000 10020000 2981000
  //   11*0 40004000 14008000 48000000 10020000 2a81000 11*0 40004000 14008000 48000000 10020000 2b81000
  //   11*0 40004000 14008000 48000000 10020000 2c81000 11*0 40004000 14008000 48000000 10020000 2d81000
  //   11*0 40004000 14008000 48000000 10020000 2e81000 11*0 40004000 14008000 48000000 10020000 2f81000
  //   3595*0 40004000 14008000 14*0 40004000 14008000 48000000 12000000 12*0 40004000 14008000 48000000
  //   10020000 2081000 11*0 40004000 14008000 48000000 10020000 2181000 11*0 40004000 14008000 48000000
  //   21000000 12*0 40004000 14008000 a000000 13*0 40004000 14008000 8002000 13*0 40004000 14008000
  //   8002000 13*0 40004000 14008000 14*0 40004000 14008000 48000000 12000000 201c1000 11*0 40004000
  //   14008000 48000000 12000000 209c1000 11*0 40004000 14008000 a000000 13*0 40004000 14008000 48000000
  //   20000800 12*0 40004000 14008000 48000000 10020000 101000 11*0 40004000 14008000 1010000 13*0
  //   40004000 14008000 80000000 13*0 40004000 14008000 48000000 10020000 2081000 11*0 40004000 14008000
  //   48000000 10020000 2181000 11*0 40004000 14008000 48000000 10020000 2281000 11*0 40004000 14008000
  //   48000000 10020000 2381000 11*0 40004000 14008000 48000000 10020000 2481000 11*0 40004000 14008000
  //   48000000 10020000 2581000 11*0 40004000 14008000 48000000 10020000 2681000 11*0 40004000 14008000
  //   48000000 10020000 2781000 11*0 40004000 14008000 48000000 10020000 2881000 11*0 40004000 14008000
  //   48000000 10020000 2981000 11*0 40004000 14008000 48000000 10020000 2a81000 11*0 40004000 14008000
  //   48000000 10020000 2b81000 11*0 40004000 14008000 48000000 10020000 2c81000 11*0 40004000 14008000
  //   48000000 10020000 2d81000 11*0 40004000 14008000 48000000 10020000 2e81000 11*0 40004000 14008000
  //   48000000 10020000 2f81000 3595*0 40004000 14008000 14*0 40004000 14008000 48000000 12000000 12*0
  //   40004000 14008000 48000000 10020000 2081000 11*0 40004000 14008000 48000000 10020000 2181000 11*0
  //   40004000 14008000 48000000 21000000 12*0 40004000 14008000 a000000 13*0 40004000 14008000 8002000
  //   13*0 40004000 14008000 14*0 40004000 14008000 8002000 13*0 40004000 14008000 48000000 12000000
  //   201c1000 11*0 40004000 14008000 48000000 12000000 209c1000 11*0 40004000 14008000 a000000 13*0
  //   40004000 14008000 48000000 20000800 12*0 40004000 14008000 48000000 10020000 101000 11*0 40004000
  //   14008000 1010000 13*0 40004000 14008000 80000000 13*0 40004000 14008000 48000000 10020000 2081000
  //   11*0 40004000 14008000 48000000 10020000 2181000 11*0 40004000 14008000 48000000 10020000 2281000
  //   11*0 40004000 14008000 48000000 10020000 2381000 11*0 40004000 14008000 48000000 10020000 2481000
  //   11*0 40004000 14008000 48000000 10020000 2581000 11*0 40004000 14008000 48000000 10020000 2681000
  //   11*0 40004000 14008000 48000000 10020000 2781000 11*0 40004000 14008000 48000000 10020000 2881000
  //   11*0 40004000 14008000 48000000 10020000 2981000 11*0 40004000 14008000 48000000 10020000 2a81000
  //   11*0 40004000 14008000 48000000 10020000 2b81000 11*0 40004000 14008000 48000000 10020000 2c8100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
endmodule

module RTC (
  input  CLK,
  input  RTCReset,
  input  RTCOut,
  input  CLR,
  output [15:0] BusOut
);

  wire or_1_out;
  wire [15:0] counter_1_q, divider_1_out, divider_1_rem;

  or or_1 (or_1_out, RTCReset, CLR);
  Counter #(.max('hffff), .width(16)) counter_1 (
    .clr(or_1_out), .load(1'b0), .up(1'b1), .count(1'b1), .clk(CLK), .Q(counter_1_q));  // open: D, carry
  assign BusOut = RTCOut ? counter_1_q : 16'bz;  // Controlled_Buffer controlled_buffer_1
  // Probe on counter_1_q
  // Probe on 16'h3e8
  Divider #(.width(16)) divider_1 (
    .a(counter_1_q), .b(16'h3e8), .out(divider_1_out), .rem(divider_1_rem));  // open: upper
  // Probe on divider_1_out
  // Probe on divider_1_rem
  _7_Segment_Display u_7_segment_display_1 ();  // open: g, f, a, b, e, d, c, dp
  // BCD_to_7_Segment_decoder bcd_to_7_segment_decoder_1: pin names not known
  // Binary_to_BCD_converter #(.binvalue(8)) binary_to_bcd_converter_1: pin names not known; wires that end beside it: divider_1_out[7:0]
  _7_Segment_Display u_7_segment_display_2 ();  // open: g, f, a, b, e, d, c, dp
  // BCD_to_7_Segment_decoder bcd_to_7_segment_decoder_2: pin names not known
  // Binary_to_BCD_converter #(.binvalue(10)) binary_to_bcd_converter_2: pin names not known; wires that end beside it: divider_1_rem[9:0]
  _7_Segment_Display u_7_segment_display_3 ();  // open: g, f, a, b, e, d, c, dp
  _7_Segment_Display u_7_segment_display_4 ();  // open: g, f, a, b, e, d, c, dp
  // BCD_to_7_Segment_decoder bcd_to_7_segment_decoder_3: pin names not known
  // BCD_to_7_Segment_decoder bcd_to_7_segment_decoder_4: pin names not known
  _7_Segment_Display u_7_segment_display_5 ();  // open: g, f, a, b, e, d, c, dp
  // BCD_to_7_Segment_decoder bcd_to_7_segment_decoder_5: pin names not known
endmodule

module OutputShift (
  input  [15:0] BusIn,
  input  CLK,
  input  CLR,
  input  OutputIn,
  output [15:0] out_5,
  output [15:0] out_6,
  output [15:0] out_7,
  output [15:0] out_8,
  output [15:0] out_9,
  output [15:0] out_10,
  output [15:0] out_11,
  output [15:0] out_12,
  output [15:0] out_13,
  output [15:0] out_14,
  output [15:0] out_15,
  output [15:0] out_16,
  output [15:0] out_17,
  output [15:0] out_18,
  output [15:0] out_19,
  output [15:0] out_20
);

  // Shift_Register #(.length(16), .width(16)) shift_register_1: pin names not known; wires that end beside it: CLR, OutputIn, CLK, BusIn, out_5, out_6, out_7, out_8, out_9, out_10, out_11, out_12, out_13, out_14, out_15, out_16
endmodule

module Dec16Bit (
  input  [15:0] DataIn
);

  wire [15:0] divider_1_out, divider_1_rem;

  // Probe on DataIn
  // Probe on 16'h3e8
  Divider #(.width(16)) divider_1 (.a(DataIn), .b(16'h3e8), .out(divider_1_out), .rem(divider_1_rem));  // open: upper
  // Probe on divider_1_out
  // Probe on divider_1_rem
  _7_Segment_Display u_7_segment_display_1 ();  // open: g, f, a, b, e, d, c, dp
  // BCD_to_7_Segment_decoder bcd_to_7_segment_decoder_1: pin names not known
  // Binary_to_BCD_converter #(.binvalue(8)) binary_to_bcd_converter_1: pin names not known; wires that end beside it: divider_1_out[7:0]
  _7_Segment_Display u_7_segment_display_2 ();  // open: g, f, a, b, e, d, c, dp
  // BCD_to_7_Segment_decoder bcd_to_7_segment_decoder_2: pin names not known
  _7_Segment_Display u_7_segment_display_3 ();  // open: g, f, a, b, e, d, c, dp
  // BCD_to_7_Segment_decoder bcd_to_7_segment_decoder_3: pin names not known
  // Binary_to_BCD_converter #(.binvalue(10)) binary_to_bcd_converter_2: pin names not known; wires that end beside it: divider_1_rem[9:0]
  _7_Segment_Display u_7_segment_display_4 ();  // open: g, f, a, b, e, d, c, dp
  // BCD_to_7_Segment_decoder bcd_to_7_segment_decoder_4: pin names not known
  _7_Segment_Display u_7_segment_display_5 ();  // open: g, f, a, b, e, d, c, dp
  // BCD_to_7_Segment_decoder bcd_to_7_segment_decoder_5: pin names not known
endmodule
