// Logisim project 32BitComputer.circ as structural Verilog: 17 circuits, main circuit main
module main (
  input  in_1,
  input  in_2
);

  wire alu_1_carryout, button_1_out, button_2_out, button_3_out, button_4_out, CLK, CLR, control_1_alufloat,
       control_1_aluincrement, control_1_counterenable, control_1_hlt, control_1_notain, control_1_notaout,
       control_1_notbin, control_1_notclr, control_1_notcounterout, control_1_notequationout,
       control_1_notflagsin, control_1_notinstructionin, control_1_notinstructionout, control_1_notjump,
       control_1_notmemoryin, control_1_notramout, control_1_outputin, control_1_ramin, control_1_rtcout,
       dipswitch_1_sw1, dipswitch_1_sw2, dipswitch_1_sw3, dipswitch_1_sw4, dipswitch_1_sw5, dipswitch_1_sw6,
       dipswitch_1_sw7, dipswitch_1_sw8, dipswitch_1_sw9, dipswitch_1_sw10, dipswitch_1_sw11,
       dipswitch_1_sw12, dipswitch_1_sw13, dipswitch_1_sw14, dipswitch_1_sw15, dipswitch_1_sw16,
       dipswitch_1_sw17, dipswitch_1_sw18, dipswitch_1_sw19, dipswitch_1_sw20, dipswitch_1_sw21,
       dipswitch_1_sw22, dipswitch_1_sw23, dipswitch_1_sw24, dipswitch_1_sw25, dipswitch_1_sw26,
       dipswitch_1_sw27, dipswitch_1_sw28, dipswitch_1_sw29, dipswitch_1_sw30, dipswitch_1_sw31,
       dipswitch_1_sw32, dipswitch_2_sw1, dipswitch_2_sw2, dipswitch_2_sw3, dipswitch_2_sw4, dipswitch_2_sw5,
       dipswitch_2_sw6, dipswitch_2_sw7, dipswitch_2_sw8, dipswitch_2_sw9, dipswitch_2_sw10,
       dipswitch_2_sw11, dipswitch_2_sw12, dipswitch_2_sw13, dipswitch_2_sw14, dipswitch_2_sw15,
       dipswitch_2_sw16, dipswitch_2_sw17, dipswitch_2_sw18, dipswitch_2_sw19, dipswitch_2_sw20,
       dipswitch_2_sw21, dipswitch_2_sw22, dipswitch_2_sw23, dipswitch_2_sw24, myclock_1_notclk,
       registerflags_1_carryflag, registerflags_1_zeroflag, registermemoryaddress_1_programmingmode;
  wire [3:0] control_1_alucontrol;
  wire [6:0] rtc_1_busout;
  wire [7:0] registerinstructions_1_instructionout4_7;
  wire [23:0] registermemoryaddress_1_adressout;
  wire [24:0] rtc_1_busout_2;
  wire [31:0] alu_1_aludisp, alu_1_aluout, OutDisp, outputshift_1_out_5, outputshift_1_out_6,
       outputshift_1_out_7, outputshift_1_out_8, outputshift_1_out_9, outputshift_1_out_10,
       outputshift_1_out_11, outputshift_1_out_12, outputshift_1_out_13, outputshift_1_out_14,
       outputshift_1_out_15, outputshift_1_out_16, outputshift_1_out_17, outputshift_1_out_18,
       outputshift_1_out_19, outputshift_1_out_20, registera_1_adisp, registera_1_aout, registerb_1_bdisp,
       registerb_1_bout;

  // Probe on OutDisp
  DisplayFloat displayfloat_1 (.in_1(OutDisp));
  // Probe on OutDisp
  Button button_1 (.out(button_1_out));
  DipSwitch #(.number(32)) dipswitch_1 (
    .sw1(dipswitch_1_sw1), .sw2(dipswitch_1_sw2), .sw3(dipswitch_1_sw3), .sw4(dipswitch_1_sw4),
    .sw5(dipswitch_1_sw5), .sw6(dipswitch_1_sw6), .sw7(dipswitch_1_sw7), .sw8(dipswitch_1_sw8),
    .sw9(dipswitch_1_sw9), .sw10(dipswitch_1_sw10), .sw11(dipswitch_1_sw11), .sw12(dipswitch_1_sw12),
    .sw13(dipswitch_1_sw13), .sw14(dipswitch_1_sw14), .sw15(dipswitch_1_sw15), .sw16(dipswitch_1_sw16),
    .sw17(dipswitch_1_sw17), .sw18(dipswitch_1_sw18), .sw19(dipswitch_1_sw19), .sw20(dipswitch_1_sw20),
    .sw21(dipswitch_1_sw21), .sw22(dipswitch_1_sw22), .sw23(dipswitch_1_sw23), .sw24(dipswitch_1_sw24),
    .sw25(dipswitch_1_sw25), .sw26(dipswitch_1_sw26), .sw27(dipswitch_1_sw27), .sw28(dipswitch_1_sw28),
    .sw29(dipswitch_1_sw29), .sw30(dipswitch_1_sw30), .sw31(dipswitch_1_sw31), .sw32(dipswitch_1_sw32));
  DipSwitch #(.number(24)) dipswitch_2 (
    .sw1(dipswitch_2_sw1), .sw2(dipswitch_2_sw2), .sw3(dipswitch_2_sw3), .sw4(dipswitch_2_sw4),
    .sw5(dipswitch_2_sw5), .sw6(dipswitch_2_sw6), .sw7(dipswitch_2_sw7), .sw8(dipswitch_2_sw8),
    .sw9(dipswitch_2_sw9), .sw10(dipswitch_2_sw10), .sw11(dipswitch_2_sw11), .sw12(dipswitch_2_sw12),
    .sw13(dipswitch_2_sw13), .sw14(dipswitch_2_sw14), .sw15(dipswitch_2_sw15), .sw16(dipswitch_2_sw16),
    .sw17(dipswitch_2_sw17), .sw18(dipswitch_2_sw18), .sw19(dipswitch_2_sw19), .sw20(dipswitch_2_sw20),
    .sw21(dipswitch_2_sw21), .sw22(dipswitch_2_sw22), .sw23(dipswitch_2_sw23), .sw24(dipswitch_2_sw24));
  Button button_2 (.out(button_2_out));
  Button button_3 (.out(button_3_out));
  RTC rtc_1 (
    .BusOut({rtc_1_busout_2, rtc_1_busout}), .CLK(CLK), .RTCReset(button_2_out), .CLR(CLR),
    .RTCOut(control_1_rtcout));
  MyClock myclock_1 (
    .NotCLK(myclock_1_notclk), .CLK(CLK), .CLKSwitch(in_1), .CLKPush(button_3_out), .HLT(control_1_hlt));
  RegisterMemoryAddress registermemoryaddress_1 (
    .ProgrammingMode(registermemoryaddress_1_programmingmode), .AdressOut(registermemoryaddress_1_adressout),
    .Dip18In(dipswitch_2_sw6), .Dip19In(dipswitch_2_sw5), .Dip20In(dipswitch_2_sw4),
    .Dip21In(dipswitch_2_sw3), .Dip22In(dipswitch_2_sw2), .Dip23In(dipswitch_2_sw1),
    .BusIn({rtc_1_busout_2, rtc_1_busout}), .CLK(CLK), .CLR(CLR), .NotMemoryIn(control_1_notmemoryin),
    .Dip0In(dipswitch_2_sw24), .Dip1In(dipswitch_2_sw23), .Dip2In(dipswitch_2_sw22),
    .Dip3In(dipswitch_2_sw21), .Dip4In(dipswitch_2_sw20), .Dip5In(dipswitch_2_sw19),
    .Dip6In(dipswitch_2_sw18), .Dip7In(dipswitch_2_sw17), .Dip8In(dipswitch_2_sw16),
    .Dip9In(dipswitch_2_sw15), .Dip10In(dipswitch_2_sw14), .Dip11In(dipswitch_2_sw13),
    .Dip12In(dipswitch_2_sw12), .Dip13In(dipswitch_2_sw11), .Dip14In(dipswitch_2_sw10),
    .Dip15In(dipswitch_2_sw9), .Dip16In(dipswitch_2_sw8), .Dip17In(dipswitch_2_sw7), .ProgrammingSwitch(in_2));
  RAMModule rammodule_1 (
    .BusOut({rtc_1_busout_2, rtc_1_busout}), .ClockPush(button_1_out), .RAMIn(control_1_ramin), .CLK(CLK),
    .ProgMode(registermemoryaddress_1_programmingmode), .Dip0In(dipswitch_1_sw32), .Dip1In(dipswitch_1_sw31),
    .Dip2In(dipswitch_1_sw30), .Dip3In(dipswitch_1_sw29), .Dip4In(dipswitch_1_sw28),
    .Dip5In(dipswitch_1_sw27), .Dip6In(dipswitch_1_sw26), .Dip7In(dipswitch_1_sw25),
    .Dip8In(dipswitch_1_sw24), .Dip9In(dipswitch_1_sw23), .Dip10In(dipswitch_1_sw22),
    .Dip11In(dipswitch_1_sw21), .Dip12In(dipswitch_1_sw20), .Dip13In(dipswitch_1_sw19),
    .Dip14In(dipswitch_1_sw18), .Dip15In(dipswitch_1_sw17), .Dip16In(dipswitch_1_sw16),
    .Dip17In(dipswitch_1_sw15), .Dip18In(dipswitch_1_sw14), .Dip19In(dipswitch_1_sw13),
    .Dip20In(dipswitch_1_sw12), .Dip21In(dipswitch_1_sw11), .Dip22In(dipswitch_1_sw10),
    .Dip23In(dipswitch_1_sw9), .Dip24In(dipswitch_1_sw8), .Dip25In(dipswitch_1_sw7),
    .Dip26In(dipswitch_1_sw6), .Dip27In(dipswitch_1_sw5), .Dip28In(dipswitch_1_sw4),
    .Dip29In(dipswitch_1_sw3), .Dip30In(dipswitch_1_sw2), .Dip31In(dipswitch_1_sw1),
    .BusIn({rtc_1_busout_2, rtc_1_busout}), .AddressIn(registermemoryaddress_1_adressout),
    .NotRAMOut(control_1_notramout));
  RegisterInstructions registerinstructions_1 (
    .BusOut({rtc_1_busout_2, rtc_1_busout}), .InstructionOut4_7(registerinstructions_1_instructionout4_7),
    .BusIn({rtc_1_busout_2, rtc_1_busout}), .CLK(CLK), .CLR(CLR),
    .NotInstructionIn(control_1_notinstructionin), .NotInstructionOut(control_1_notinstructionout));
  Button button_4 (.out(button_4_out));
  LedBar #(.matrixcols(32)) ledbar_1 (
    .led0(rtc_1_busout_2[24]), .led1(rtc_1_busout_2[23]), .led2(rtc_1_busout_2[22]),
    .led3(rtc_1_busout_2[21]), .led4(rtc_1_busout_2[20]), .led5(rtc_1_busout_2[19]),
    .led6(rtc_1_busout_2[18]), .led7(rtc_1_busout_2[17]), .led8(rtc_1_busout_2[16]),
    .led9(rtc_1_busout_2[15]), .led10(rtc_1_busout_2[14]), .led11(rtc_1_busout_2[13]),
    .led12(rtc_1_busout_2[12]), .led13(rtc_1_busout_2[11]), .led14(rtc_1_busout_2[10]),
    .led15(rtc_1_busout_2[9]), .led16(rtc_1_busout_2[8]), .led17(rtc_1_busout_2[7]),
    .led18(rtc_1_busout_2[6]), .led19(rtc_1_busout_2[5]), .led20(rtc_1_busout_2[4]),
    .led21(rtc_1_busout_2[3]), .led22(rtc_1_busout_2[2]), .led23(rtc_1_busout_2[1]),
    .led24(rtc_1_busout_2[0]), .led25(rtc_1_busout[6]), .led26(rtc_1_busout[5]), .led27(rtc_1_busout[4]),
    .led28(rtc_1_busout[3]), .led29(rtc_1_busout[2]), .led30(rtc_1_busout[1]), .led31(rtc_1_busout[0]));
  ProgramCounter programcounter_1 (
    .BusOut({rtc_1_busout_2, rtc_1_busout}), .BusIn({rtc_1_busout_2, rtc_1_busout}),
    .NotJump(control_1_notjump), .CLK(CLK), .NotCLR(control_1_notclr),
    .CounterEnable(control_1_counterenable), .NotCounterOut(control_1_notcounterout));
  RegisterOutput registeroutput_1 (
    .OutDisp(OutDisp), .BusIn({rtc_1_busout_2, rtc_1_busout}), .OutputIn(control_1_outputin), .CLK(CLK),
    .NotCLR(control_1_notclr));
  RegisterA registera_1 (
    .ADisp(registera_1_adisp), .AOut(registera_1_aout), .BusOut({rtc_1_busout_2, rtc_1_busout}),
    .BusIn({rtc_1_busout_2, rtc_1_busout}), .CLK(CLK), .CLR(CLR), .NotAIn(control_1_notain),
    .NotAOut(control_1_notaout));
  ALU alu_1 (
    .CarryOut(alu_1_carryout), .ALUOut(alu_1_aluout), .ALUDisp(alu_1_aludisp),
    .BusOut({rtc_1_busout_2, rtc_1_busout}), .AIn(registera_1_aout), .BIn(registerb_1_bout),
    .Floating(control_1_alufloat), .Increment(control_1_aluincrement), .ALUControl(control_1_alucontrol),
    .NotEOut(control_1_notequationout));
  RegisterB registerb_1 (
    .BDisp(registerb_1_bdisp), .BOut(registerb_1_bout), .BusOut({rtc_1_busout_2, rtc_1_busout}),
    .BusIn({rtc_1_busout_2, rtc_1_busout}), .CLK(CLK), .CLR(CLR), .NotBIn(control_1_notbin), .NotBOut(1'b1));
  DisplayFloat displayfloat_2 (.in_1(registera_1_adisp));
  DisplayFloat displayfloat_3 (.in_1(alu_1_aludisp));
  Control control_1 (
    .NotAOut(control_1_notaout), .NotAIn(control_1_notain), .NotInstructionIn(control_1_notinstructionin),
    .NotInstructionOut(control_1_notinstructionout), .NotRAMOut(control_1_notramout),
    .RAMIn(control_1_ramin), .NotMemoryIn(control_1_notmemoryin), .HLT(control_1_hlt),
    .ALUFloat(control_1_alufloat), .RTCOut(control_1_rtcout), .NotFlagsIn(control_1_notflagsin),
    .NotJump(control_1_notjump), .NotCounterOut(control_1_notcounterout),
    .CounterEnable(control_1_counterenable), .OutputIn(control_1_outputin), .NotBIn(control_1_notbin),
    .ALUIncrement(control_1_aluincrement), .NotEquationOut(control_1_notequationout),
    .ALUControl(control_1_alucontrol), .CLR(CLR), .NotCLR(control_1_notclr), .NotCLK(myclock_1_notclk),
    .PushReset(button_4_out), .InstructionIn(registerinstructions_1_instructionout4_7),
    .CarryFlag(registerflags_1_carryflag), .ZeroFlag(registerflags_1_zeroflag));  // open: NIU0, NIU1, NIU2, NIU3, NIU4, NIU5, NIU6, NIU7, NIU8, NIU9
  DisplayFloat displayfloat_4 (.in_1(registerb_1_bdisp));
  RegisterFlags registerflags_1 (
    .ZeroFlag(registerflags_1_zeroflag), .CarryFlag(registerflags_1_carryflag), .CarryIn(alu_1_carryout),
    .CLK(CLK), .CLR(CLR), .NotFlagsIn(control_1_notflagsin), .ALUIn(alu_1_aluout));
  OutputShift outputshift_1 (
    .out_5(outputshift_1_out_5), .out_6(outputshift_1_out_6), .out_7(outputshift_1_out_7),
    .out_8(outputshift_1_out_8), .out_9(outputshift_1_out_9), .out_10(outputshift_1_out_10),
    .out_11(outputshift_1_out_11), .out_12(outputshift_1_out_12), .out_13(outputshift_1_out_13),
    .out_14(outputshift_1_out_14), .out_15(outputshift_1_out_15), .out_16(outputshift_1_out_16),
    .out_17(outputshift_1_out_17), .out_18(outputshift_1_out_18), .out_19(outputshift_1_out_19),
    .out_20(outputshift_1_out_20), .BusIn({rtc_1_busout_2, rtc_1_busout}), .CLK(CLK), .CLR(CLR),
    .OutputIn(control_1_outputin));
  Dec32Bit dec32bit_1 (.DataIn(outputshift_1_out_5));
  Dec32Bit dec32bit_2 (.DataIn(outputshift_1_out_6));
  Dec32Bit dec32bit_3 (.DataIn(outputshift_1_out_7));
  Dec32Bit dec32bit_4 (.DataIn(outputshift_1_out_8));
  Dec32Bit dec32bit_5 (.DataIn(outputshift_1_out_9));
  Dec32Bit dec32bit_6 (.DataIn(outputshift_1_out_10));
  Dec32Bit dec32bit_7 (.DataIn(outputshift_1_out_11));
  Dec32Bit dec32bit_8 (.DataIn(outputshift_1_out_12));
  Dec32Bit dec32bit_9 (.DataIn(outputshift_1_out_13));
  Dec32Bit dec32bit_10 (.DataIn(outputshift_1_out_14));
  Dec32Bit dec32bit_11 (.DataIn(outputshift_1_out_15));
  Dec32Bit dec32bit_12 (.DataIn(outputshift_1_out_16));
  Dec32Bit dec32bit_13 (.DataIn(outputshift_1_out_17));
  Dec32Bit dec32bit_14 (.DataIn(outputshift_1_out_18));
  Dec32Bit dec32bit_15 (.DataIn(outputshift_1_out_19));
  Dec32Bit dec32bit_16 (.DataIn(outputshift_1_out_20));
  DisplayFloat displayfloat_5 (.in_1(outputshift_1_out_5));
  DisplayFloat displayfloat_6 (.in_1(outputshift_1_out_6));
  DisplayFloat displayfloat_7 (.in_1(outputshift_1_out_7));
  DisplayFloat displayfloat_8 (.in_1(outputshift_1_out_8));
  DisplayFloat displayfloat_9 (.in_1(outputshift_1_out_9));
  DisplayFloat displayfloat_10 (.in_1(outputshift_1_out_10));
  DisplayFloat displayfloat_11 (.in_1(outputshift_1_out_11));
  DisplayFloat displayfloat_12 (.in_1(outputshift_1_out_12));
  DisplayFloat displayfloat_13 (.in_1(outputshift_1_out_13));
  DisplayFloat displayfloat_14 (.in_1(outputshift_1_out_14));
  DisplayFloat displayfloat_15 (.in_1(outputshift_1_out_15));
  DisplayFloat displayfloat_16 (.in_1(outputshift_1_out_16));
  DisplayFloat displayfloat_17 (.in_1(outputshift_1_out_17));
  DisplayFloat displayfloat_18 (.in_1(outputshift_1_out_18));
  DisplayFloat displayfloat_19 (.in_1(outputshift_1_out_19));
  DisplayFloat displayfloat_20 (.in_1(outputshift_1_out_20));
  // Probe on rtc_1_busout
  TTY tty_1 (.data(rtc_1_busout), .clk(CLK), .we(control_1_outputin), .clr(CLR));
endmodule

module MyClock (
  input  CLKSwitch,
  input  CLKPush,
  input  HLT,
  output NotCLK,
  output CLK
);

  wire and_1_out, and_2_out, clock_1_out, not_1_out, not_2_out, or_1_out;

  Clock clock_1 (.out(clock_1_out));
  not not_1 (not_1_out, CLKSwitch);
  and and_1 (and_1_out, clock_1_out, CLKSwitch);
  LED led_1 (.in(CLKSwitch));
  LED led_2 (.in(not_1_out));
  and and_2 (and_2_out, not_1_out, CLKPush);
  or or_1 (or_1_out, and_1_out, and_2_out);
  not not_2 (not_2_out, HLT);
  and and_3 (CLK, or_1_out, not_2_out);
  not not_3 (NotCLK, CLK);
  LED led_3 (.in(CLK));
endmodule

module RegisterA (
  input  [31:0] BusIn,
  input  CLK,
  input  CLR,
  input  NotAIn,
  input  NotAOut,
  output [31:0] ADisp,
  output [31:0] AOut,
  output [31:0] BusOut
);

  wire not_1_out, not_2_out;

  Register #(.width(32)) register_1 (.D(BusIn), .en(not_1_out), .clk(CLK), .Q(ADisp), .clr(CLR));
  not not_1 (not_1_out, NotAIn);
  Hex_Digit_Display hex_digit_display_1 (.value(ADisp[31:28]));  // open: dp
  assign BusOut = not_2_out ? ADisp : 32'bz;  // Controlled_Buffer controlled_buffer_1
  not not_2 (not_2_out, NotAOut);
  Hex_Digit_Display hex_digit_display_2 (.value(ADisp[27:24]));  // open: dp
  Hex_Digit_Display hex_digit_display_3 (.value(ADisp[23:20]));  // open: dp
  Hex_Digit_Display hex_digit_display_4 (.value(ADisp[19:16]));  // open: dp
  Hex_Digit_Display hex_digit_display_5 (.value(ADisp[15:12]));  // open: dp
  Hex_Digit_Display hex_digit_display_6 (.value(ADisp[11:8]));  // open: dp
  Hex_Digit_Display hex_digit_display_7 (.value(ADisp[7:4]));  // open: dp
  Hex_Digit_Display hex_digit_display_8 (.value(ADisp[3:0]));  // open: dp

  assign AOut = ADisp;
endmodule

module RegisterB (
  input  [31:0] BusIn,
  input  CLK,
  input  CLR,
  input  NotBIn,
  input  NotBOut,
  output [31:0] BDisp,
  output [31:0] BOut,
  output [31:0] BusOut
);

  wire not_1_out, not_2_out;

  Register #(.width(32)) register_1 (.D(BusIn), .en(not_1_out), .clk(CLK), .Q(BDisp), .clr(CLR));
  not not_1 (not_1_out, NotBIn);
  assign BusOut = not_2_out ? BDisp : 32'bz;  // Controlled_Buffer controlled_buffer_1
  not not_2 (not_2_out, NotBOut);
  Hex_Digit_Display hex_digit_display_1 (.value(BDisp[31:28]));  // open: dp
  Hex_Digit_Display hex_digit_display_2 (.value(BDisp[27:24]));  // open: dp
  Hex_Digit_Display hex_digit_display_3 (.value(BDisp[23:20]));  // open: dp
  Hex_Digit_Display hex_digit_display_4 (.value(BDisp[19:16]));  // open: dp
  Hex_Digit_Display hex_digit_display_5 (.value(BDisp[15:12]));  // open: dp
  Hex_Digit_Display hex_digit_display_6 (.value(BDisp[11:8]));  // open: dp
  Hex_Digit_Display hex_digit_display_7 (.value(BDisp[7:4]));  // open: dp
  Hex_Digit_Display hex_digit_display_8 (.value(BDisp[3:0]));  // open: dp

  assign BOut = BDisp;
endmodule

module RegisterInstructions (
  input  [31:0] BusIn,
  input  CLK,
  input  CLR,
  input  NotInstructionIn,
  input  NotInstructionOut,
  output [7:0] InstructionOut4_7,
  output [31:0] BusOut
);

  wire not_1_out, not_2_out;
  wire [23:0] register_1_q;

  Register #(.width(32)) register_1 (
    .D(BusIn), .en(not_1_out), .clk(CLK), .Q({InstructionOut4_7, register_1_q}), .clr(CLR));
  not not_1 (not_1_out, NotInstructionIn);
  Hex_Digit_Display hex_digit_display_1 (.value(InstructionOut4_7[7:4]));  // open: dp
  Hex_Digit_Display hex_digit_display_2 (.value(InstructionOut4_7[3:0]));  // open: dp
  Hex_Digit_Display hex_digit_display_3 (.value(register_1_q[23:20]));  // open: dp
  assign BusOut = not_2_out ? {{8{1'b0}}, register_1_q} : 32'bz;  // Controlled_Buffer controlled_buffer_1
  not not_2 (not_2_out, NotInstructionOut);
  Hex_Digit_Display hex_digit_display_4 (.value(register_1_q[19:16]));  // open: dp
  Hex_Digit_Display hex_digit_display_5 (.value(register_1_q[15:12]));  // open: dp
  Hex_Digit_Display hex_digit_display_6 (.value(register_1_q[11:8]));  // open: dp
  Hex_Digit_Display hex_digit_display_7 (.value(register_1_q[7:4]));  // open: dp
  Hex_Digit_Display hex_digit_display_8 (.value(register_1_q[3:0]));  // open: dp
endmodule

module ALU (
  input  Floating,
  input  Increment,
  input  [3:0] ALUControl,
  input  [31:0] AIn,
  input  NotEOut,
  input  [31:0] BIn,
  output CarryOut,
  output [31:0] BusOut,
  output [31:0] ALUOut,
  output [31:0] ALUDisp
);

  wire adder_1_cout, adder_2_cout, adder_3_cout, adder_4_cout, and_2_out, multiplexer_1_out,
       multiplexer_3_out, not_4_out;
  wire [5:0] bitadder_1_out;
  wire [31:0] adder_1_out, adder_2_out, adder_3_out, adder_4_out, and_1_out, bit_extender_1_out,
       divider_1_out, divider_1_rem, fpadder_1_out, fpadder_2_out, fpdivider_1_out, fpmultiplier_1_out,
       fpmultiplier_2_out, fpnegator_1_p2, fpsubtractor_1_out, fpsubtractor_2_out, fptoint_1_p2,
       inttofp_1_p2, inttofp_2_p2, multiplexer_2_out, multiplexer_4_out, multiplexer_5_out,
       multiplexer_6_out, multiplier_1_cout, multiplier_1_out, not_1_out, not_2_out, not_3_out, or_1_out,
       shifter_1_out, shifter_2_out, shifter_3_out, shifter_4_out, shifter_5_out, sqrt_1_rootout, xor_1_out;

  assign not_1_out = ~BIn;  // NOT_Gate not_1, 32 bits wide
  // IntToFP #(.width(3)) inttofp_1: pin names not known; wires that end beside it: ALUControl[2:0], inttofp_1_p2
  Adder #(.width(32)) adder_1 (.a(AIn), .b(BIn), .out(adder_1_out), .cout(adder_1_cout));  // open: cin
  Adder #(.width(32)) adder_2 (.a(AIn), .b(not_1_out), .out(adder_2_out), .cin(1'b1), .cout(adder_2_cout));
  Multiplier #(.width(32)) multiplier_1 (
    .a(AIn), .b(BIn), .out(multiplier_1_out), .cout(multiplier_1_cout));  // open: cin
  Divider #(.width(32)) divider_1 (.a(AIn), .b(BIn), .out(divider_1_out), .rem(divider_1_rem));  // open: upper
  assign and_1_out = AIn & BIn;  // AND_Gate and_1, 32 bits wide
  assign or_1_out = AIn | BIn;  // OR_Gate or_1, 32 bits wide
  assign xor_1_out = AIn ^ BIn;  // XOR_Gate xor_1, 32 bits wide
  assign not_2_out = ~AIn;  // NOT_Gate not_2, 32 bits wide
  Shifter #(.width(32)) shifter_1 (.in(AIn), .\dist (BIn[4:0]), .out(shifter_1_out));
  Shifter #(.shift("lr"), .width(32)) shifter_2 (.in(AIn), .\dist (BIn[4:0]), .out(shifter_2_out));
  Shifter #(.shift("ar"), .width(32)) shifter_3 (.in(AIn), .\dist (BIn[4:0]), .out(shifter_3_out));
  Shifter #(.shift("rl"), .width(32)) shifter_4 (.in(AIn), .\dist (BIn[4:0]), .out(shifter_4_out));
  Shifter #(.shift("rr"), .width(32)) shifter_5 (.in(AIn), .\dist (BIn[4:0]), .out(shifter_5_out));
  BitAdder #(.width(32)) bitadder_1 (.in0(AIn), .out(bitadder_1_out));
  assign bit_extender_1_out = {{29{ALUControl[2]}}, ALUControl[2:0]};  // Bit_Extender bit_extender_1
  assign not_3_out = ~bit_extender_1_out;  // NOT_Gate not_3, 32 bits wide
  FPAdder fpadder_1 (.a(AIn), .b(BIn), .out(fpadder_1_out));
  FPSubtractor fpsubtractor_1 (.a(AIn), .b(BIn), .out(fpsubtractor_1_out));
  FPMultiplier fpmultiplier_1 (.a(AIn), .b(BIn), .out(fpmultiplier_1_out));
  FPDivider fpdivider_1 (.a(AIn), .b(BIn), .out(fpdivider_1_out));
  // FPNegator fpnegator_1: pin names not known; wires that end beside it: AIn, fpnegator_1_p2
  // FPToInt #(.width(32)) fptoint_1: pin names not known; wires that end beside it: AIn, fptoint_1_p2
  // IntToFP #(.width(32)) inttofp_2: pin names not known; wires that end beside it: AIn, inttofp_2_p2
  FPMultiplier fpmultiplier_2 (.a(AIn), .b(AIn), .out(fpmultiplier_2_out));
  SQRT sqrt_1 (.RootOut(sqrt_1_rootout), .S(AIn));
  Adder #(.width(32)) adder_3 (.a(AIn), .b(bit_extender_1_out), .out(adder_3_out), .cout(adder_3_cout));  // open: cin
  Multiplexer multiplexer_1 (.in0(adder_3_cout), .in1(adder_4_cout), .out(multiplexer_1_out), .sel(ALUControl[3]));
  Adder #(.width(32)) adder_4 (.a(AIn), .b(not_3_out), .out(adder_4_out), .cin(1'b1), .cout(adder_4_cout));
  // Probe on inttofp_2_p2
  FPAdder fpadder_2 (.a(AIn), .b(inttofp_1_p2), .out(fpadder_2_out));
  FPSubtractor fpsubtractor_2 (.a(AIn), .b(inttofp_1_p2), .out(fpsubtractor_2_out));
  Multiplexer #(.width(32)) multiplexer_2 (
    .in0(fpadder_2_out), .in1(fpsubtractor_2_out), .out(multiplexer_2_out), .sel(ALUControl[3]));
  Multiplexer multiplexer_3 (.in0(adder_1_cout), .in1(adder_2_cout), .out(multiplexer_3_out), .sel(ALUControl[0]));
  and and_2 (and_2_out, multiplexer_3_out, ~ALUControl[1], ~ALUControl[2], ~ALUControl[3]);  // AND_Gate
  Multiplexer #(.select(4), .width(32)) multiplexer_4 (
    .in0(adder_1_out), .in1(adder_2_out), .in2(multiplier_1_out), .in3(multiplier_1_cout),
    .in4(divider_1_out), .in5(divider_1_rem), .in6(and_1_out), .in7(or_1_out), .in8(xor_1_out),
    .in9(not_2_out), .in10(shifter_1_out), .in11(shifter_2_out), .in12(shifter_3_out), .in13(shifter_4_out),
    .in14(shifter_5_out), .in15({{26{1'b0}}, bitadder_1_out}), .out(multiplexer_4_out), .sel(ALUControl));
  Multiplexer #(.width(32)) multiplexer_5 (
    .in0(adder_3_out), .in1(adder_4_out), .out(multiplexer_5_out), .sel(ALUControl[3]));
  Multiplexer #(.select(4), .width(32)) multiplexer_6 (
    .in0(fpadder_1_out), .in1(fpsubtractor_1_out), .in2(fpmultiplier_1_out), .in3(fpdivider_1_out),
    .in4(fpnegator_1_p2), .in5(fptoint_1_p2), .in6(inttofp_2_p2), .in7(fpmultiplier_2_out),
    .in8(sqrt_1_rootout), .out(multiplexer_6_out), .sel(ALUControl));  // open: in9, in10, in11, in12, in13, in14, in15
  Multiplexer multiplexer_7 (.in0(and_2_out), .in1(multiplexer_1_out), .out(CarryOut), .sel(Increment));
  Hex_Digit_Display hex_digit_display_1 (.value(ALUDisp[31:28]));  // open: dp
  Multiplexer #(.select(2), .width(32)) multiplexer_8 (
    .in0(multiplexer_4_out), .in1(multiplexer_5_out), .in2(multiplexer_6_out), .in3(multiplexer_2_out),
    .out(ALUDisp), .sel({Floating, Increment}));
  // Probe on ALUDisp
  Hex_Digit_Display hex_digit_display_2 (.value(ALUDisp[27:24]));  // open: dp
  Hex_Digit_Display hex_digit_display_3 (.value(ALUDisp[23:20]));  // open: dp
  Hex_Digit_Display hex_digit_display_4 (.value(ALUDisp[19:16]));  // open: dp
  Hex_Digit_Display hex_digit_display_5 (.value(ALUDisp[15:12]));  // open: dp
  assign BusOut = not_4_out ? ALUDisp : 32'bz;  // Controlled_Buffer controlled_buffer_1
  not not_4 (not_4_out, NotEOut);
  Hex_Digit_Display hex_digit_display_6 (.value(ALUDisp[11:8]));  // open: dp
  Hex_Digit_Display hex_digit_display_7 (.value(ALUDisp[7:4]));  // open: dp
  Hex_Digit_Display hex_digit_display_8 (.value(ALUDisp[3:0]));  // open: dp

  assign ALUOut = ALUDisp;
endmodule

module RegisterFlags (
  input  [31:0] ALUIn,
  input  CarryIn,
  input  CLK,
  input  CLR,
  input  NotFlagsIn,
  output ZeroFlag,
  output CarryFlag
);

  wire not_1_out;
  wire [0:0] nor_1_out;

  nor nor_1 (nor_1_out[0], ALUIn[0], ALUIn[1], ALUIn[2], ALUIn[3], ALUIn[4], ALUIn[5], ALUIn[6], ALUIn[7], ALUIn[8], ALUIn[9], ALUIn[10], ALUIn[11], ALUIn[12], ALUIn[13], ALUIn[14], ALUIn[15], ALUIn[16], ALUIn[17], ALUIn[18], ALUIn[19], ALUIn[20], ALUIn[21], ALUIn[22], ALUIn[23], ALUIn[24], ALUIn[25], ALUIn[26], ALUIn[27], ALUIn[28], ALUIn[29], ALUIn[30], ALUIn[31]);
  Register #(.width(2)) register_1 (
    .D({CarryIn, nor_1_out[0]}), .en(not_1_out), .clk(CLK), .Q({CarryFlag, ZeroFlag}), .clr(CLR));
  not not_1 (not_1_out, NotFlagsIn);
  LED led_1 (.in(ZeroFlag));
  LED led_2 (.in(CarryFlag));
endmodule

module RegisterMemoryAddress (
  input  [31:0] BusIn,
  input  CLK,
  input  CLR,
  input  NotMemoryIn,
  input  Dip0In,
  input  Dip1In,
  input  Dip2In,
  input  Dip3In,
  input  Dip4In,
  input  Dip5In,
  input  ProgrammingSwitch,
  input  Dip6In,
  input  Dip7In,
  input  Dip8In,
  input  Dip9In,
  input  Dip10In,
  input  Dip11In,
  input  Dip12In,
  input  Dip13In,
  input  Dip14In,
  input  Dip15In,
  input  Dip16In,
  input  Dip17In,
  input  Dip18In,
  input  Dip19In,
  input  Dip20In,
  input  Dip21In,
  input  Dip22In,
  input  Dip23In,
  output [23:0] AdressOut,
  output ProgrammingMode
);

  wire not_1_out, not_2_out;
  wire [23:0] register_1_q;

  not not_1 (not_1_out, NotMemoryIn);
  Register #(.width(24)) register_1 (.D(BusIn[23:0]), .en(not_1_out), .clk(CLK), .Q(register_1_q), .clr(CLR));
  Multiplexer #(.width(24)) multiplexer_1 (
    .in0(register_1_q),
    .in1({Dip23In, Dip22In, Dip21In, Dip20In, Dip19In, Dip18In, Dip17In, Dip16In, Dip15In, Dip14In, Dip13In, Dip12In, Dip11In, Dip10In, Dip9In, Dip8In, Dip7In, Dip6In, Dip5In, Dip4In, Dip3In, Dip2In, Dip1In, Dip0In}),
    .out(AdressOut), .sel(ProgrammingSwitch));
  LED led_1 (.in(AdressOut[0]));
  LED led_2 (.in(AdressOut[1]));
  LED led_3 (.in(AdressOut[2]));
  LED led_4 (.in(AdressOut[3]));
  LED led_5 (.in(AdressOut[4]));
  LED led_6 (.in(AdressOut[5]));
  LED led_7 (.in(AdressOut[6]));
  LED led_8 (.in(AdressOut[7]));
  LED led_9 (.in(AdressOut[8]));
  LED led_10 (.in(AdressOut[9]));
  LED led_11 (.in(AdressOut[10]));
  LED led_12 (.in(AdressOut[11]));
  LED led_13 (.in(AdressOut[12]));
  LED led_14 (.in(AdressOut[13]));
  LED led_15 (.in(AdressOut[14]));
  LED led_16 (.in(AdressOut[15]));
  LED led_17 (.in(AdressOut[16]));
  LED led_18 (.in(AdressOut[17]));
  LED led_19 (.in(AdressOut[18]));
  LED led_20 (.in(AdressOut[19]));
  LED led_21 (.in(AdressOut[20]));
  LED led_22 (.in(AdressOut[21]));
  LED led_23 (.in(AdressOut[22]));
  LED led_24 (.in(AdressOut[23]));
  Hex_Digit_Display hex_digit_display_1 (.value(AdressOut[23:20]));  // open: dp
  LED led_25 (.in(ProgrammingSwitch));
  not not_2 (not_2_out, ProgrammingSwitch);
  LED led_26 (.in(not_2_out));
  Hex_Digit_Display hex_digit_display_2 (.value(AdressOut[19:16]));  // open: dp
  Hex_Digit_Display hex_digit_display_3 (.value(AdressOut[15:12]));  // open: dp
  Hex_Digit_Display hex_digit_display_4 (.value(AdressOut[11:8]));  // open: dp
  Hex_Digit_Display hex_digit_display_5 (.value(AdressOut[7:4]));  // open: dp
  Hex_Digit_Display hex_digit_display_6 (.value(AdressOut[3:0]));  // open: dp

  assign ProgrammingMode = ProgrammingSwitch;
endmodule

module RAMModule (
  input  [23:0] AddressIn,
  input  NotRAMOut,
  input  ClockPush,
  input  RAMIn,
  input  CLK,
  input  ProgMode,
  input  Dip0In,
  input  [31:0] BusIn,
  input  Dip1In,
  input  Dip2In,
  input  Dip3In,
  input  Dip4In,
  input  Dip5In,
  input  Dip6In,
  input  Dip7In,
  input  Dip8In,
  input  Dip9In,
  input  Dip10In,
  input  Dip11In,
  input  Dip12In,
  input  Dip13In,
  input  Dip14In,
  input  Dip15In,
  input  Dip16In,
  input  Dip17In,
  input  Dip18In,
  input  Dip19In,
  input  Dip20In,
  input  Dip21In,
  input  Dip22In,
  input  Dip23In,
  input  Dip24In,
  input  Dip25In,
  input  Dip26In,
  input  Dip27In,
  input  Dip28In,
  input  Dip29In,
  input  Dip30In,
  input  Dip31In,
  output [31:0] BusOut
);

  wire multiplexer_1_out, nand_1_out, not_1_out, not_2_out, not_3_out, not_4_out;
  wire [3:0] ram_1_dout, ram_1_dout_2, ram_1_dout_3, ram_1_dout_4, ram_1_dout_5, ram_1_dout_6, ram_1_dout_7,
       ram_1_dout_8;
  wire [31:0] multiplexer_2_out, multiplexer_3_out;

  not not_1 (not_1_out, ClockPush);
  nand nand_1 (nand_1_out, RAMIn, CLK);
  not not_2 (not_2_out, ProgMode);
  not not_3 (not_3_out, multiplexer_1_out);
  Multiplexer multiplexer_1 (.in0(not_1_out), .in1(nand_1_out), .out(multiplexer_1_out), .sel(not_2_out));
  Multiplexer #(.width(32)) multiplexer_2 (
    .in0({Dip31In, Dip30In, Dip29In, Dip28In, Dip27In, Dip26In, Dip25In, Dip24In, Dip23In, Dip22In, Dip21In, Dip20In, Dip19In, Dip18In, Dip17In, Dip16In, Dip15In, Dip14In, Dip13In, Dip12In, Dip11In, Dip10In, Dip9In, Dip8In, Dip7In, Dip6In, Dip5In, Dip4In, Dip3In, Dip2In, Dip1In, Dip0In}),
    .in1(BusIn), .out(multiplexer_2_out), .sel(not_2_out));
  RAM #(.addrWidth(24), .dataWidth(32), .trigger("high"), .\type ("nonvolatile")) ram_1 (
    .addr(AddressIn), .we(not_3_out), .oe(1'b1), .din(multiplexer_2_out),
    .dout({ram_1_dout_8, ram_1_dout_7, ram_1_dout_6, ram_1_dout_5, ram_1_dout_4, ram_1_dout_3, ram_1_dout_2, ram_1_dout}));
  Hex_Digit_Display hex_digit_display_1 (.value(ram_1_dout_8));  // open: dp
  Hex_Digit_Display hex_digit_display_2 (.value(ram_1_dout_7));  // open: dp
  Hex_Digit_Display hex_digit_display_3 (.value(ram_1_dout_6));  // open: dp
  Hex_Digit_Display hex_digit_display_4 (.value(multiplexer_3_out[31:28]));  // open: dp
  Hex_Digit_Display hex_digit_display_5 (.value(multiplexer_3_out[27:24]));  // open: dp
  Multiplexer #(.width(32)) multiplexer_3 (
    .in0({Dip31In, Dip30In, Dip29In, Dip28In, Dip27In, Dip26In, Dip25In, Dip24In, Dip23In, Dip22In, Dip21In, Dip20In, Dip19In, Dip18In, Dip17In, Dip16In, Dip15In, Dip14In, Dip13In, Dip12In, Dip11In, Dip10In, Dip9In, Dip8In, Dip7In, Dip6In, Dip5In, Dip4In, Dip3In, Dip2In, Dip1In, Dip0In}),
    .in1({ram_1_dout_8, ram_1_dout_7, ram_1_dout_6, ram_1_dout_5, ram_1_dout_4, ram_1_dout_3, ram_1_dout_2, ram_1_dout}),
    .out(multiplexer_3_out), .sel(not_2_out));
  Hex_Digit_Display hex_digit_display_6 (.value(ram_1_dout_5));  // open: dp
  Hex_Digit_Display hex_digit_display_7 (.value(ram_1_dout_4));  // open: dp
  Hex_Digit_Display hex_digit_display_8 (.value(multiplexer_3_out[23:20]));  // open: dp
  Hex_Digit_Display hex_digit_display_9 (.value(multiplexer_3_out[19:16]));  // open: dp
  Hex_Digit_Display hex_digit_display_10 (.value(ram_1_dout_3));  // open: dp
  Hex_Digit_Display hex_digit_display_11 (.value(ram_1_dout_2));  // open: dp
  Hex_Digit_Display hex_digit_display_12 (.value(multiplexer_3_out[15:12]));  // open: dp
  Hex_Digit_Display hex_digit_display_13 (.value(multiplexer_3_out[11:8]));  // open: dp
  Hex_Digit_Display hex_digit_display_14 (.value(ram_1_dout));  // open: dp
  Hex_Digit_Display hex_digit_display_15 (.value(multiplexer_3_out[7:4]));  // open: dp
  Hex_Digit_Display hex_digit_display_16 (.value(multiplexer_3_out[3:0]));  // open: dp
  not not_4 (not_4_out, NotRAMOut);
  assign BusOut = not_4_out ? {ram_1_dout_8, ram_1_dout_7, ram_1_dout_6, ram_1_dout_5, ram_1_dout_4, ram_1_dout_3, ram_1_dout_2, ram_1_dout} : 32'bz;  // Controlled_Buffer controlled_buffer_1
  LED led_1 (.in(ram_1_dout[0]));
  LED led_2 (.in(ram_1_dout[1]));
  LED led_3 (.in(ram_1_dout[2]));
  LED led_4 (.in(ram_1_dout[3]));
  LED led_5 (.in(ram_1_dout_2[0]));
  LED led_6 (.in(ram_1_dout_2[1]));
  LED led_7 (.in(ram_1_dout_2[2]));
  LED led_8 (.in(ram_1_dout_2[3]));
  LED led_9 (.in(ram_1_dout_3[0]));
  LED led_10 (.in(ram_1_dout_3[1]));
  LED led_11 (.in(ram_1_dout_3[2]));
  LED led_12 (.in(ram_1_dout_3[3]));
  LED led_13 (.in(ram_1_dout_4[0]));
  LED led_14 (.in(ram_1_dout_4[1]));
  LED led_15 (.in(ram_1_dout_4[2]));
  LED led_16 (.in(ram_1_dout_4[3]));
  LED led_17 (.in(ram_1_dout_5[0]));
  LED led_18 (.in(ram_1_dout_5[1]));
  LED led_19 (.in(ram_1_dout_5[2]));
  LED led_20 (.in(ram_1_dout_5[3]));
  LED led_21 (.in(ram_1_dout_6[0]));
  LED led_22 (.in(ram_1_dout_6[1]));
  LED led_23 (.in(ram_1_dout_6[2]));
  LED led_24 (.in(ram_1_dout_6[3]));
  LED led_25 (.in(ram_1_dout_7[0]));
  LED led_26 (.in(ram_1_dout_7[1]));
  LED led_27 (.in(ram_1_dout_7[2]));
  LED led_28 (.in(ram_1_dout_7[3]));
  LED led_29 (.in(ram_1_dout_8[0]));
  LED led_30 (.in(ram_1_dout_8[1]));
  LED led_31 (.in(ram_1_dout_8[2]));
  LED led_32 (.in(ram_1_dout_8[3]));
endmodule

module RegisterOutput (
  input  [31:0] BusIn,
  input  OutputIn,
  input  CLK,
  input  NotCLR,
  output [31:0] OutDisp
);

  wire and_1_out, not_1_out;

  Register #(.width(32)) register_1 (.D(BusIn), .en(1'b1), .clk(and_1_out), .Q(OutDisp), .clr(not_1_out));
  and and_1 (and_1_out, OutputIn, CLK);
  not not_1 (not_1_out, NotCLR);
endmodule

module ProgramCounter (
  input  [31:0] BusIn,
  input  NotJump,
  input  CLK,
  input  NotCLR,
  input  CounterEnable,
  input  NotCounterOut,
  output [31:0] BusOut
);

  wire not_1_out, not_2_out, not_3_out;
  wire [23:0] counter_1_q;

  not not_1 (not_1_out, NotJump);
  not not_2 (not_2_out, NotCLR);
  Counter #(.max('hffffff), .width(24)) counter_1 (
    .clr(not_2_out), .load(not_1_out), .up(1'b1), .count(CounterEnable), .clk(CLK), .D(BusIn[23:0]),
    .Q(counter_1_q));  // open: carry
  LED led_1 (.in(counter_1_q[0]));
  LED led_2 (.in(counter_1_q[1]));
  LED led_3 (.in(counter_1_q[2]));
  LED led_4 (.in(counter_1_q[3]));
  LED led_5 (.in(counter_1_q[4]));
  LED led_6 (.in(counter_1_q[5]));
  LED led_7 (.in(counter_1_q[6]));
  LED led_8 (.in(counter_1_q[7]));
  LED led_9 (.in(counter_1_q[8]));
  LED led_10 (.in(counter_1_q[9]));
  LED led_11 (.in(counter_1_q[10]));
  LED led_12 (.in(counter_1_q[11]));
  LED led_13 (.in(counter_1_q[12]));
  LED led_14 (.in(counter_1_q[13]));
  LED led_15 (.in(counter_1_q[14]));
  LED led_16 (.in(counter_1_q[15]));
  LED led_17 (.in(counter_1_q[16]));
  LED led_18 (.in(counter_1_q[17]));
  LED led_19 (.in(counter_1_q[18]));
  LED led_20 (.in(counter_1_q[19]));
  LED led_21 (.in(counter_1_q[20]));
  LED led_22 (.in(counter_1_q[21]));
  LED led_23 (.in(counter_1_q[22]));
  LED led_24 (.in(counter_1_q[23]));
  Hex_Digit_Display hex_digit_display_1 (.value(counter_1_q[23:20]));  // open: dp
  assign BusOut = not_3_out ? {{8{1'b0}}, counter_1_q} : 32'bz;  // Controlled_Buffer controlled_buffer_1
  not not_3 (not_3_out, NotCounterOut);
  Hex_Digit_Display hex_digit_display_2 (.value(counter_1_q[19:16]));  // open: dp
  Hex_Digit_Display hex_digit_display_3 (.value(counter_1_q[15:12]));  // open: dp
  Hex_Digit_Display hex_digit_display_4 (.value(counter_1_q[11:8]));  // open: dp
  Hex_Digit_Display hex_digit_display_5 (.value(counter_1_q[7:4]));  // open: dp
  Hex_Digit_Display hex_digit_display_6 (.value(counter_1_q[3:0]));  // open: dp
endmodule

module Control (
  input  [7:0] InstructionIn,
  input  NotCLK,
  input  CarryFlag,
  input  ZeroFlag,
  input  PushReset,
  output NIU0,
  output NIU1,
  output NIU2,
  output NIU3,
  output NIU4,
  output NIU5,
  output NIU6,
  output NIU7,
  output NIU8,
  output NIU9,
  output ALUFloat,
  output RTCOut,
  output CLR,
  output NotFlagsIn,
  output NotCLR,
  output NotJump,
  output NotCounterOut,
  output CounterEnable,
  output OutputIn,
  output NotBIn,
  output ALUIncrement,
  output NotEquationOut,
  output [3:0] ALUControl,
  output NotAOut,
  output NotAIn,
  output NotInstructionIn,
  output NotInstructionOut,
  output NotRAMOut,
  output RAMIn,
  output NotMemoryIn,
  output HLT
);

  wire decoder_1_out0, decoder_1_out1, decoder_1_out2, decoder_1_out3, decoder_1_out4, decoder_1_out5,
       nand_1_out, not_1_out;
  wire [2:0] counter_1_q_2;
  wire [3:3] counter_1_q;
  wire [30:12] rom_1_data;

  Counter #(.max('hf), .width(4)) counter_1 (
    .clr(not_1_out), .load(1'b0), .up(1'b1), .count(1'b1), .clk(NotCLK), .Q({counter_1_q[3], counter_1_q_2}));  // open: D, carry
  not not_1 (not_1_out, nand_1_out);
  LED led_1 (.in(decoder_1_out0));
  LED led_2 (.in(decoder_1_out1));
  LED led_3 (.in(decoder_1_out2));
  nand nand_1 (nand_1_out, decoder_1_out5, NotCLR);
  LED led_4 (.in(decoder_1_out3));
  LED led_5 (.in(decoder_1_out4));
  not not_2 (NotCLR, PushReset);
  _7_Segment_Display u_7_segment_display_1 ();  // open: g, f, a, b, e, d, c, dp
  // BCD_to_7_Segment_decoder bcd_to_7_segment_decoder_1: pin names not known; wires that end beside it: {counter_1_q[3], counter_1_q_2}
  Decoder #(.select(3)) decoder_1 (
    .out0(decoder_1_out0), .out1(decoder_1_out1), .out2(decoder_1_out2), .out3(decoder_1_out3),
    .out4(decoder_1_out4), .out5(decoder_1_out5), .sel(counter_1_q_2), .en(1'b1));  // open: out6, out7
  not not_3 (CLR, NotCLR);
  LED led_6 (.in(counter_1_q_2[0]));
  LED led_7 (.in(counter_1_q_2[1]));
  LED led_8 (.in(counter_1_q_2[2]));
  ROM #(.addrWidth(16), .dataWidth(32)) rom_1 (
    .addr({2'b00, ZeroFlag, CarryFlag, InstructionIn, 1'b0, counter_1_q_2}),
    .data({HLT, rom_1_data[30], RAMIn, rom_1_data[28:24], ALUControl, rom_1_data[19], ALUIncrement, rom_1_data[17], OutputIn, CounterEnable, rom_1_data[14:12], RTCOut, ALUFloat, NIU9, NIU8, NIU7, NIU6, NIU5, NIU4, NIU3, NIU2, NIU1, NIU0}));
  LED led_9 (.in(NIU0));
  LED led_10 (.in(NIU1));
  LED led_11 (.in(NIU2));
  LED led_12 (.in(NIU3));
  LED led_13 (.in(NIU4));
  LED led_14 (.in(NIU5));
  LED led_15 (.in(NIU6));
  LED led_16 (.in(NIU7));
  LED led_17 (.in(NIU8));
  LED led_18 (.in(NIU9));
  LED led_19 (.in(ALUFloat));
  LED led_20 (.in(RTCOut));
  LED led_21 (.in(rom_1_data[12]));
  LED led_22 (.in(rom_1_data[13]));
  LED led_23 (.in(rom_1_data[14]));
  LED led_24 (.in(CounterEnable));
  LED led_25 (.in(OutputIn));
  LED led_26 (.in(rom_1_data[17]));
  LED led_27 (.in(ALUIncrement));
  LED led_28 (.in(rom_1_data[19]));
  LED led_29 (.in(ALUControl[0]));
  LED led_30 (.in(ALUControl[1]));
  LED led_31 (.in(ALUControl[2]));
  LED led_32 (.in(ALUControl[3]));
  LED led_33 (.in(rom_1_data[24]));
  LED led_34 (.in(rom_1_data[25]));
  LED led_35 (.in(rom_1_data[26]));
  LED led_36 (.in(rom_1_data[27]));
  LED led_37 (.in(rom_1_data[28]));
  LED led_38 (.in(RAMIn));
  LED led_39 (.in(rom_1_data[30]));
  LED led_40 (.in(HLT));
  not not_4 (NotFlagsIn, rom_1_data[12]);
  not not_5 (NotJump, rom_1_data[13]);
  not not_6 (NotCounterOut, rom_1_data[14]);
  not not_7 (NotBIn, rom_1_data[17]);
  not not_8 (NotEquationOut, rom_1_data[19]);
  not not_9 (NotAOut, rom_1_data[24]);
  not not_10 (NotAIn, rom_1_data[25]);
  not not_11 (NotInstructionIn, rom_1_data[26]);
  not not_12 (NotInstructionOut, rom_1_data[27]);
  not not_13 (NotRAMOut, rom_1_data[28]);
  not not_14 (NotMemoryIn, rom_1_data[30]);

  // Notes on the sheet:
  //   contents of rom_1 (hex, n*v repeats v):
  //   40004000 14008000 14*0 40004000 14008000 48000000 12000000 12*0 40004000 14008000 41000000 12000000
  //   12*0 40004000 14008000 48000000 50000000 21000000 11*0 40004000 14008000 48000000 21000000 12*0
  //   40004000 14008000 a000000 13*0 40004000 14008000 8002000 13*0 40004000 14008000 14*0 40004000
  //   14008000 14*0 40004000 14008000 48000000 12000000 201c1000 11*0 40004000 14008000 48000000 12000000
  //   209c1000 11*0 40004000 14008000 a000000 13*0 40004000 14008000 48000000 20000800 12*0 40004000
  //   14008000 48000000 10020000 101000 11*0 40004000 14008000 1010000 13*0 40004000 14008000 80000000
  //   13*0 40004000 14008000 48000000 10020000 2081000 11*0 40004000 14008000 48000000 10020000 2181000
  //   11*0 40004000 14008000 48000000 10020000 2281000 11*0 40004000 14008000 48000000 10020000 2381000
  //   11*0 40004000 14008000 48000000 10020000 2481000 11*0 40004000 14008000 48000000 10020000 2581000
  //   11*0 40004000 14008000 48000000 10020000 2681000 11*0 40004000 14008000 48000000 10020000 2781000
  //   11*0 40004000 14008000 48000000 10020000 2881000 11*0 40004000 14008000 0 0 2981000 11*0 40004000
  //   14008000 48000000 10020000 2a81000 11*0 40004000 14008000 48000000 10020000 2b81000 11*0 40004000
  //   14008000 48000000 10020000 2c81000 11*0 40004000 14008000 48000000 10020000 2d81000 11*0 40004000
  //   14008000 48000000 10020000 2e81000 11*0 40004000 14008000 0 0 2f81000 11*0 40004000 14008000
  //   48000000 10020000 2081400 11*0 40004000 14008000 48000000 10020000 2181400 11*0 40004000 14008000
  //   48000000 10020000 2281400 11*0 40004000 14008000 48000000 10020000 2381400 11*0 40004000 14008000 0
  //   0 2481400 11*0 40004000 14008000 0 0 2581400 11*0 40004000 14008000 0 0 2681400 11*0 40004000
  //   14008000 0 0 2781400 11*0 40004000 14008000 0 0 2881400 11*0 40004000 14008000 14*0 40004000
  //   14008000 14*0 40004000 14008000 14*0 40004000 14008000 14*0 40004000 14008000 14*0 40004000 14008000
  //   14*0 40004000 14008000 8020000 101000 3340*0 40004000 14008000 14*0 40004000 14008000 48000000
  //   12000000 12*0 40004000 14008000 41000000 12000000 12*0 40004000 14008000 48000000 50000000 21000000
  //   11*0 40004000 14008000 48000000 21000000 12*0 40004000 14008000 a000000 13*0 40004000 14008000
  //   8002000 13*0 40004000 14008000 8002000 13*0 40004000 14008000 14*0 40004000 14008000 48000000
  //   12000000 201c1000 11*0 40004000 14008000 48000000 12000000 209c1000 11*0 40004000 14008000 a000000
  //   13*0 40004000 14008000 48000000 20000800 12*0 40004000 14008000 48000000 10020000 101000 11*0
  //   40004000 14008000 1010000 13*0 40004000 14008000 80000000 13*0 40004000 14008000 48000000 10020000
  //   2081000 11*0 40004000 14008000 48000000 10020000 2181000 11*0 40004000 14008000 48000000 10020000
  //   2281000 11*0 40004000 14008000 48000000 10020000 2381000 11*0 40004000 14008000 48000000 10020000
  //   2481000 11*0 40004000 14008000 48000000 10020000 2581000 11*0 40004000 14008000 48000000 10020000
  //   2681000 11*0 40004000 14008000 48000000 10020000 2781000 11*0 40004000 14008000 48000000 10020000
  //   2881000 11*0 40004000 14008000 48000000 10020000 2981000 11*0 40004000 14008000 48000000 10020000
  //   2a81000 11*0 40004000 14008000 48000000 10020000 2b81000 11*0 40004000 14008000 48000000 10020000
  //   2c81000 11*0 40004000 14008000 48000000 10020000 2d81000 11*0 40004000 14008000 48000000 10020000
  //   2e81000 11*0 40004000 14008000 48000000 10020000 2f81000 11*0 40004000 14008000 48000000 10020000
  //   2081400 11*0 40004000 14008000 48000000 10020000 2181400 11*0 40004000 14008000 48000000 10020000
  //   2281400 11*0 40004000 14008000 48000000 10020000 2381400 11*0 40004000 14008000 0 0 2481400 11*0
  //   40004000 14008000 0 0 2581400 11*0 40004000 14008000 0 0 2681400 11*0 40004000 14008000 0 0 2781400
  //   11*0 40004000 14008000 0 0 2881400 11*0 40004000 14008000 14*0 40004000 14008000 14*0 40004000
  //   14008000 14*0 40004000 14008000 14*0 40004000 14008000 14*0 40004000 14008000 14*0 40004000 14008000
  //   8020000 101000 3340*0 40004000 14008000 14*0 40004000 14008000 48000000 12000000 12*0 40004000
  //   14008000 41000000 12000000 12*0 40004000 14008000 48000000 50000000 21000000 11*0 40004000 14008000
  //   4800000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
endmodule

module RTC (
  input  CLK,
  input  RTCReset,
  input  RTCOut,
  input  CLR,
  output [31:0] BusOut
);

  wire or_1_out;
  wire [3:0] counter_1_q;
  wire [31:4] counter_1_q_2;

  or or_1 (or_1_out, RTCReset, CLR);
  Counter #(.max('hffffffff), .width(32)) counter_1 (
    .clr(or_1_out), .load(1'b0), .up(1'b1), .count(1'b1), .clk(CLK), .Q({counter_1_q_2, counter_1_q}));  // open: D, carry
  assign BusOut = RTCOut ? {counter_1_q_2, counter_1_q} : 32'bz;  // Controlled_Buffer controlled_buffer_1
  Hex_Digit_Display hex_digit_display_1 (.value(counter_1_q_2[31:28]));  // open: dp
  Hex_Digit_Display hex_digit_display_2 (.value(counter_1_q_2[27:24]));  // open: dp
  Hex_Digit_Display hex_digit_display_3 (.value(counter_1_q_2[23:20]));  // open: dp
  Hex_Digit_Display hex_digit_display_4 (.value(counter_1_q_2[19:16]));  // open: dp
  Hex_Digit_Display hex_digit_display_5 (.value(counter_1_q_2[15:12]));  // open: dp
  Hex_Digit_Display hex_digit_display_6 (.value(counter_1_q_2[11:8]));  // open: dp
  Hex_Digit_Display hex_digit_display_7 (.value(counter_1_q));  // open: dp
  Hex_Digit_Display hex_digit_display_8 (.value(counter_1_q_2[7:4]));  // open: dp
endmodule

module OutputShift (
  input  [31:0] BusIn,
  input  CLK,
  input  CLR,
  input  OutputIn,
  output [31:0] out_5,
  output [31:0] out_6,
  output [31:0] out_7,
  output [31:0] out_8,
  output [31:0] out_9,
  output [31:0] out_10,
  output [31:0] out_11,
  output [31:0] out_12,
  output [31:0] out_13,
  output [31:0] out_14,
  output [31:0] out_15,
  output [31:0] out_16,
  output [31:0] out_17,
  output [31:0] out_18,
  output [31:0] out_19,
  output [31:0] out_20
);

  // Shift_Register #(.length(16), .width(32)) shift_register_1: pin names not known; wires that end beside it: CLR, OutputIn, CLK, BusIn, out_5, out_6, out_7, out_8, out_9, out_10, out_11, out_12, out_13, out_14, out_15, out_16
endmodule

module Dec32Bit (
  input  [31:0] DataIn
);

  wire [31:0] divider_1_out, divider_1_rem, divider_2_out, divider_2_rem, divider_3_out, divider_3_rem;

  // Probe on DataIn
  // Probe on 32'h3e8
  Divider #(.width(32)) divider_1 (
    .a(divider_2_out), .b(32'h3e8), .out(divider_1_out), .rem(divider_1_rem));  // open: upper
  Divider #(.width(32)) divider_2 (
    .a(divider_3_out), .b(32'h3e8), .out(divider_2_out), .rem(divider_2_rem));  // open: upper
  Divider #(.width(32)) divider_3 (.a(DataIn), .b(32'h3e8), .out(divider_3_out), .rem(divider_3_rem));  // open: upper
  // Probe on divider_3_out
  // Probe on divider_3_rem
  _7_Segment_Display u_7_segment_display_1 ();  // open: g, f, a, b, e, d, c, dp
  // BCD_to_7_Segment_decoder bcd_to_7_segment_decoder_1: pin names not known
  _7_Segment_Display u_7_segment_display_2 ();  // open: g, f, a, b, e, d, c, dp
  // BCD_to_7_Segment_decoder bcd_to_7_segment_decoder_2: pin names not known; wires that end beside it: divider_1_out[3:0]
  // Binary_to_BCD_converter #(.binvalue(10)) binary_to_bcd_converter_1: pin names not known; wires that end beside it: divider_1_rem[9:0]
  _7_Segment_Display u_7_segment_display_3 ();  // open: g, f, a, b, e, d, c, dp
  // BCD_to_7_Segment_decoder bcd_to_7_segment_decoder_3: pin names not known
  _7_Segment_Display u_7_segment_display_4 ();  // open: g, f, a, b, e, d, c, dp
  // BCD_to_7_Segment_decoder bcd_to_7_segment_decoder_4: pin names not known
  // Binary_to_BCD_converter #(.binvalue(10)) binary_to_bcd_converter_2: pin names not known; wires that end beside it: divider_2_rem[9:0]
  _7_Segment_Display u_7_segment_display_5 ();  // open: g, f, a, b, e, d, c, dp
  _7_Segment_Display u_7_segment_display_6 ();  // open: g, f, a, b, e, d, c, dp
  // BCD_to_7_Segment_decoder bcd_to_7_segment_decoder_5: pin names not known
  // BCD_to_7_Segment_decoder bcd_to_7_segment_decoder_6: pin names not known
  _7_Segment_Display u_7_segment_display_7 ();  // open: g, f, a, b, e, d, c, dp
  // BCD_to_7_Segment_decoder bcd_to_7_segment_decoder_7: pin names not known
  // Binary_to_BCD_converter #(.binvalue(10)) binary_to_bcd_converter_3: pin names not known; wires that end beside it: divider_3_rem[9:0]
  _7_Segment_Display u_7_segment_display_8 ();  // open: g, f, a, b, e, d, c, dp
  _7_Segment_Display u_7_segment_display_9 ();  // open: g, f, a, b, e, d, c, dp
  // BCD_to_7_Segment_decoder bcd_to_7_segment_decoder_8: pin names not known
  // BCD_to_7_Segment_decoder bcd_to_7_segment_decoder_9: pin names not known
  _7_Segment_Display u_7_segment_display_10 ();  // open: g, f, a, b, e, d, c, dp
  // BCD_to_7_Segment_decoder bcd_to_7_segment_decoder_10: pin names not known
endmodule

module DisplayFloat (
  input  [31:0] in_1
);

  wire bcd_to_7_segment_decoder_26_p1, binary_to_bcd_converter_2_p1, binary_to_bcd_converter_4_p2,
       binary_to_bcd_converter_6_p2, fpcomparator_1_p3, fpcomparator_1_p4, fpcomparator_2_p1, inttofp_4_p2,
       or_1_out, or_2_out, or_3_out, or_4_out, or_5_out, or_6_out, or_7_out, or_8_out, or_9_out, or_10_out,
       or_11_out, or_12_out, or_13_out, or_14_out, or_15_out, or_16_out, or_17_out, or_18_out, or_19_out,
       or_20_out, or_21_out, or_22_out, or_23_out, or_24_out, or_25_out;
  wire [3:0] binary_to_bcd_converter_1_p2, binary_to_bcd_converter_1_p3, binary_to_bcd_converter_2_p2,
       binary_to_bcd_converter_3_p1, binary_to_bcd_converter_3_p4, binary_to_bcd_converter_3_p5,
       binary_to_bcd_converter_4_p1, binary_to_bcd_converter_4_p3, binary_to_bcd_converter_5_p1,
       binary_to_bcd_converter_5_p3, binary_to_bcd_converter_6_p1, binary_to_bcd_converter_6_p3,
       binary_to_bcd_converter_7_p1, binary_to_bcd_converter_7_p2, binary_to_bcd_converter_7_p4,
       binary_to_bcd_converter_7_p5, binary_to_bcd_converter_8_p1, binary_to_bcd_converter_8_p3,
       binary_to_bcd_converter_8_p4, binary_to_bcd_converter_9_p1, binary_to_bcd_converter_9_p3,
       binary_to_bcd_converter_9_p4, bit_extender_1_out, inttofp_2_p1, inttofp_5_p1;
  wire [9:0] binary_to_bcd_converter_1_p1, binary_to_bcd_converter_3_p2, binary_to_bcd_converter_5_p2,
       binary_to_bcd_converter_7_p3, binary_to_bcd_converter_8_p2, binary_to_bcd_converter_9_p2;
  wire [31:0] fpmultiplier_1_out, fpmultiplier_2_out, fpmultiplier_3_out, fpmultiplier_4_out,
       fpmultiplier_5_out, fpnegator_1_p2, fpsubtractor_1_out, fpsubtractor_2_out, fpsubtractor_3_out,
       inttofp_1_p2, inttofp_2_p2, inttofp_3_p2, inttofp_5_p2, inttofp_6_p2, multiplexer_1_out;
  wire [63:0] divider_1_out, divider_1_rem, divider_2_out, divider_2_rem, divider_3_out, divider_3_rem,
       divider_4_out, divider_4_rem, divider_5_out, divider_5_rem, divider_6_out, divider_6_rem,
       fptoint_3_p2, multiplexer_2_out;

  // Probe on in_1
  _7_Segment_Display u_7_segment_display_1 (.g(fpcomparator_1_p4));  // open: f, a, b, e, d, c, dp
  _7_Segment_Display u_7_segment_display_2 (.dp(fpcomparator_2_p1));  // open: g, f, a, b, e, d, c
  // BCD_to_7_Segment_decoder bcd_to_7_segment_decoder_1: pin names not known
  Bit_Extender #(.in_width(64), .out_width(4)) bit_extender_1 (.in(divider_1_out), .out(bit_extender_1_out));
  // FPNegator fpnegator_1: pin names not known; wires that end beside it: in_1, fpnegator_1_p2
  // FPComparator fpcomparator_1: pin names not known; wires that end beside it: in_1, {32{1'b0}}, fpcomparator_1_p3, fpcomparator_1_p4
  // IntToFP #(.width(12)) inttofp_1: pin names not known; wires that end beside it: 12'h3e8, inttofp_1_p2
  Controlled_Buffer #(.width(4)) controlled_buffer_1 (.in(bit_extender_1_out), .en(or_1_out));  // open: out
  or or_1 (or_1_out, bit_extender_1_out[0], bit_extender_1_out[1], bit_extender_1_out[2], bit_extender_1_out[3]);
  // Binary_to_BCD_converter #(.binvalue(10)) binary_to_bcd_converter_1: pin names not known; wires that end beside it: binary_to_bcd_converter_1_p1, binary_to_bcd_converter_1_p2, binary_to_bcd_converter_1_p3
  // Probe on multiplexer_1_out
  Multiplexer #(.width(32)) multiplexer_1 (
    .in0(fpnegator_1_p2), .in1(in_1), .out(multiplexer_1_out), .sel(fpcomparator_1_p3));
  // Binary_to_BCD_converter #(.binvalue(11)) binary_to_bcd_converter_2: pin names not known; wires that end beside it: binary_to_bcd_converter_2_p1, binary_to_bcd_converter_2_p2
  _7_Segment_Display u_7_segment_display_3 (.dp(fpcomparator_2_p1));  // open: g, f, a, b, e, d, c
  // BCD_to_7_Segment_decoder bcd_to_7_segment_decoder_2: pin names not known
  Controlled_Buffer #(.width(4)) controlled_buffer_2 (.in(binary_to_bcd_converter_1_p2), .en(or_2_out));  // open: out
  or or_2 (or_2_out, binary_to_bcd_converter_1_p2[0], binary_to_bcd_converter_1_p2[1], binary_to_bcd_converter_1_p2[2], binary_to_bcd_converter_1_p2[3], or_1_out);
  Divider #(.width(64)) divider_1 (
    .a(divider_2_out), .b(64'h3e8), .out(divider_1_out), .rem(divider_1_rem));  // open: upper
  _7_Segment_Display u_7_segment_display_4 ();  // open: g, f, a, b, e, d, c, dp
  // BCD_to_7_Segment_decoder bcd_to_7_segment_decoder_3: pin names not known
  Controlled_Buffer #(.width(4)) controlled_buffer_3 (.in(binary_to_bcd_converter_2_p2), .en(or_3_out));  // open: out
  or or_3 (or_3_out, binary_to_bcd_converter_2_p2[0], binary_to_bcd_converter_2_p2[1], binary_to_bcd_converter_2_p2[2], binary_to_bcd_converter_2_p2[3], or_5_out);
  FPMultiplier fpmultiplier_1 (.a(fpsubtractor_3_out), .b(inttofp_1_p2), .out(fpmultiplier_1_out));
  // FPToInt #(.mode("floor"), .width(11)) fptoint_1: pin names not known; wires that end beside it: fpmultiplier_1_out, binary_to_bcd_converter_2_p1
  _7_Segment_Display u_7_segment_display_5 (.dp(fpcomparator_2_p1));  // open: g, f, a, b, e, d, c
  _7_Segment_Display u_7_segment_display_6 (.dp(fpcomparator_2_p1));  // open: g, f, a, b, e, d, c
  // BCD_to_7_Segment_decoder bcd_to_7_segment_decoder_4: pin names not known
  // BCD_to_7_Segment_decoder bcd_to_7_segment_decoder_5: pin names not known
  Controlled_Buffer #(.width(4)) controlled_buffer_4 (.in(binary_to_bcd_converter_1_p3), .en(or_4_out));  // open: out
  or or_4 (or_4_out, binary_to_bcd_converter_1_p3[0], binary_to_bcd_converter_1_p3[1], binary_to_bcd_converter_1_p3[2], binary_to_bcd_converter_1_p3[3], or_2_out);
  Bit_Extender #(.in_width(64), .out_width(10)) bit_extender_2 (.in(divider_1_rem), .out(binary_to_bcd_converter_1_p1));
  _7_Segment_Display u_7_segment_display_7 ();  // open: g, f, a, b, e, d, c, dp
  _7_Segment_Display u_7_segment_display_8 ();  // open: g, f, a, b, e, d, c, dp
  // BCD_to_7_Segment_decoder bcd_to_7_segment_decoder_6: pin names not known
  // BCD_to_7_Segment_decoder bcd_to_7_segment_decoder_7: pin names not known
  Controlled_Buffer #(.width(4)) controlled_buffer_5 (.in(inttofp_2_p1), .en(or_5_out));  // open: out
  Controlled_Buffer #(.width(4)) controlled_buffer_6 (.in(binary_to_bcd_converter_4_p1), .en(or_7_out));  // open: out
  or or_5 (or_5_out, inttofp_2_p1[0], inttofp_2_p1[1], inttofp_2_p1[2], inttofp_2_p1[3], or_7_out);
  // IntToFP #(.width(11)) inttofp_2: pin names not known; wires that end beside it: inttofp_2_p1, inttofp_2_p2, inttofp_2_p2
  Controlled_Buffer #(.width(4)) controlled_buffer_7 (.in(binary_to_bcd_converter_3_p1), .en(or_6_out));  // open: out
  or or_6 (or_6_out, binary_to_bcd_converter_3_p1[0], binary_to_bcd_converter_3_p1[1], binary_to_bcd_converter_3_p1[2], binary_to_bcd_converter_3_p1[3], or_4_out);
  // Binary_to_BCD_converter #(.binvalue(10)) binary_to_bcd_converter_3: pin names not known; wires that end beside it: binary_to_bcd_converter_3_p1, binary_to_bcd_converter_3_p2, {64{1'b1}}, binary_to_bcd_converter_3_p4, binary_to_bcd_converter_3_p5
  // IntToFP #(.width(12)) inttofp_3: pin names not known; wires that end beside it: 12'h3e8, inttofp_3_p2
  or or_7 (or_7_out, binary_to_bcd_converter_4_p1[0], binary_to_bcd_converter_4_p1[1], binary_to_bcd_converter_4_p1[2], binary_to_bcd_converter_4_p1[3], or_9_out);
  // Binary_to_BCD_converter #(.binvalue(11)) binary_to_bcd_converter_4: pin names not known; wires that end beside it: binary_to_bcd_converter_4_p1, binary_to_bcd_converter_4_p2, binary_to_bcd_converter_4_p3
  FPSubtractor fpsubtractor_1 (.a(fpmultiplier_1_out), .b(inttofp_2_p2), .out(fpsubtractor_1_out));
  // Probe on fpsubtractor_1_out
  _7_Segment_Display u_7_segment_display_9 (.dp(fpcomparator_2_p1));  // open: g, f, a, b, e, d, c
  // BCD_to_7_Segment_decoder bcd_to_7_segment_decoder_8: pin names not known
  Controlled_Buffer #(.width(4)) controlled_buffer_8 (.in(binary_to_bcd_converter_3_p4), .en(or_8_out));  // open: out
  or or_8 (or_8_out, binary_to_bcd_converter_3_p4[0], binary_to_bcd_converter_3_p4[1], binary_to_bcd_converter_3_p4[2], binary_to_bcd_converter_3_p4[3], or_6_out);
  Divider #(.width(64)) divider_2 (
    .a(divider_3_out), .b(64'h3e8), .out(divider_2_out), .rem(divider_2_rem));  // open: upper
  // IntToFP #(.mode("unsigned"), .width(64)) inttofp_4: pin names not known; wires that end beside it: 64'h7fffffffffffffff, inttofp_4_p2, multiplexer_1_out, inttofp_4_p2
  // Probe on inttofp_4_p2
  _7_Segment_Display u_7_segment_display_10 ();  // open: g, f, a, b, e, d, c, dp
  // BCD_to_7_Segment_decoder bcd_to_7_segment_decoder_9: pin names not known
  Controlled_Buffer #(.width(4)) controlled_buffer_9 (.in(binary_to_bcd_converter_4_p3), .en(or_9_out));  // open: out
  or or_9 (or_9_out, binary_to_bcd_converter_4_p3[0], binary_to_bcd_converter_4_p3[1], binary_to_bcd_converter_4_p3[2], binary_to_bcd_converter_4_p3[3], or_11_out);
  FPMultiplier fpmultiplier_2 (.a(fpsubtractor_1_out), .b(inttofp_1_p2), .out(fpmultiplier_2_out));
  // FPToInt #(.mode("floor"), .width(11)) fptoint_2: pin names not known; wires that end beside it: fpmultiplier_2_out, fpmultiplier_2_out
  // Probe on binary_to_bcd_converter_4_p2
  _7_Segment_Display u_7_segment_display_11 (.dp(fpcomparator_2_p1));  // open: g, f, a, b, e, d, c
  _7_Segment_Display u_7_segment_display_12 (.dp(fpcomparator_2_p1));  // open: g, f, a, b, e, d, c
  // BCD_to_7_Segment_decoder bcd_to_7_segment_decoder_10: pin names not known
  // BCD_to_7_Segment_decoder bcd_to_7_segment_decoder_11: pin names not known
  Controlled_Buffer #(.width(4)) controlled_buffer_10 (.in(binary_to_bcd_converter_3_p5), .en(or_10_out));  // open: out
  or or_10 (or_10_out, binary_to_bcd_converter_3_p5[0], binary_to_bcd_converter_3_p5[1], binary_to_bcd_converter_3_p5[2], binary_to_bcd_converter_3_p5[3], or_8_out);
  Bit_Extender #(.in_width(64), .out_width(10)) bit_extender_3 (.in(divider_2_rem), .out(binary_to_bcd_converter_3_p2));
  // Probe on fptoint_3_p2
  // FPToInt #(.mode("floor"), .width(64)) fptoint_3: pin names not known; wires that end beside it: multiplexer_1_out, fptoint_3_p2
  // FPComparator fpcomparator_2: pin names not known; wires that end beside it: fpcomparator_2_p1
  _7_Segment_Display u_7_segment_display_13 ();  // open: g, f, a, b, e, d, c, dp
  _7_Segment_Display u_7_segment_display_14 ();  // open: g, f, a, b, e, d, c, dp
  // BCD_to_7_Segment_decoder bcd_to_7_segment_decoder_12: pin names not known
  // BCD_to_7_Segment_decoder bcd_to_7_segment_decoder_13: pin names not known
  Controlled_Buffer #(.width(4)) controlled_buffer_11 (.in(inttofp_5_p1), .en(or_11_out));  // open: out
  Controlled_Buffer #(.width(4)) controlled_buffer_12 (.in(binary_to_bcd_converter_6_p1), .en(or_13_out));  // open: out
  or or_11 (or_11_out, inttofp_5_p1[0], inttofp_5_p1[1], inttofp_5_p1[2], inttofp_5_p1[3], or_13_out);
  // IntToFP #(.width(11)) inttofp_5: pin names not known; wires that end beside it: inttofp_5_p1, inttofp_5_p2, inttofp_5_p2
  Controlled_Buffer #(.width(4)) controlled_buffer_13 (.in(binary_to_bcd_converter_5_p1), .en(or_12_out));  // open: out
  or or_12 (or_12_out, binary_to_bcd_converter_5_p1[0], binary_to_bcd_converter_5_p1[1], binary_to_bcd_converter_5_p1[2], binary_to_bcd_converter_5_p1[3], or_10_out);
  // Binary_to_BCD_converter #(.binvalue(10)) binary_to_bcd_converter_5: pin names not known; wires that end beside it: binary_to_bcd_converter_5_p1, binary_to_bcd_converter_5_p2, binary_to_bcd_converter_5_p3
  Multiplexer #(.width(64)) multiplexer_2 (
    .in0(fptoint_3_p2), .in1({64{1'b0}}), .out(multiplexer_2_out), .sel(fpcomparator_2_p1));
  // IntToFP #(.width(64)) inttofp_6: pin names not known; wires that end beside it: fptoint_3_p2, inttofp_6_p2
  or or_13 (or_13_out, binary_to_bcd_converter_6_p1[0], binary_to_bcd_converter_6_p1[1], binary_to_bcd_converter_6_p1[2], binary_to_bcd_converter_6_p1[3], or_15_out);
  // Binary_to_BCD_converter #(.binvalue(11)) binary_to_bcd_converter_6: pin names not known; wires that end beside it: binary_to_bcd_converter_6_p1, binary_to_bcd_converter_6_p2, binary_to_bcd_converter_6_p3
  FPSubtractor fpsubtractor_2 (.a(fpmultiplier_2_out), .b(inttofp_5_p2), .out(fpsubtractor_2_out));
  // Probe on fpsubtractor_2_out
  _7_Segment_Display u_7_segment_display_15 (.dp(fpcomparator_2_p1));  // open: g, f, a, b, e, d, c
  // BCD_to_7_Segment_decoder bcd_to_7_segment_decoder_14: pin names not known
  Controlled_Buffer #(.width(4)) controlled_buffer_14 (.in(binary_to_bcd_converter_5_p3), .en(or_14_out));  // open: out
  or or_14 (or_14_out, binary_to_bcd_converter_5_p3[0], binary_to_bcd_converter_5_p3[1], binary_to_bcd_converter_5_p3[2], binary_to_bcd_converter_5_p3[3], or_12_out);
  Divider #(.width(64)) divider_3 (
    .a(divider_4_out), .b(64'h3e8), .out(divider_3_out), .rem(divider_3_rem));  // open: upper
  // Probe on fpsubtractor_3_out
  FPSubtractor fpsubtractor_3 (.a(multiplexer_1_out), .b(inttofp_6_p2), .out(fpsubtractor_3_out));
  _7_Segment_Display u_7_segment_display_16 ();  // open: g, f, a, b, e, d, c, dp
  // BCD_to_7_Segment_decoder bcd_to_7_segment_decoder_15: pin names not known
  Controlled_Buffer #(.width(4)) controlled_buffer_15 (.in(binary_to_bcd_converter_6_p3), .en(or_15_out));  // open: out
  or or_15 (or_15_out, binary_to_bcd_converter_6_p3[0], binary_to_bcd_converter_6_p3[1], binary_to_bcd_converter_6_p3[2], binary_to_bcd_converter_6_p3[3]);
  FPMultiplier fpmultiplier_3 (.a(fpsubtractor_2_out), .b(inttofp_1_p2), .out(fpmultiplier_3_out));
  // FPToInt #(.mode("floor"), .width(11)) fptoint_4: pin names not known; wires that end beside it: fpmultiplier_3_out, fpmultiplier_3_out, binary_to_bcd_converter_6_p2
  _7_Segment_Display u_7_segment_display_17 (.dp(fpcomparator_2_p1));  // open: g, f, a, b, e, d, c
  _7_Segment_Display u_7_segment_display_18 (.dp(fpcomparator_2_p1));  // open: g, f, a, b, e, d, c
  // BCD_to_7_Segment_decoder bcd_to_7_segment_decoder_16: pin names not known
  // BCD_to_7_Segment_decoder bcd_to_7_segment_decoder_17: pin names not known
  Controlled_Buffer #(.width(4)) controlled_buffer_16 (.in(binary_to_bcd_converter_7_p1), .en(or_16_out));  // open: out
  or or_16 (or_16_out, binary_to_bcd_converter_7_p1[0], binary_to_bcd_converter_7_p1[1], binary_to_bcd_converter_7_p1[2], binary_to_bcd_converter_7_p1[3], or_14_out);
  Bit_Extender #(.in_width(64), .out_width(10)) bit_extender_4 (.in(divider_3_rem), .out(binary_to_bcd_converter_5_p2));
  // Probe on fpmultiplier_4_out
  FPMultiplier fpmultiplier_4 (.a(fpsubtractor_3_out), .b(fpmultiplier_5_out), .out(fpmultiplier_4_out));
  FPMultiplier fpmultiplier_5 (.a(inttofp_3_p2), .b(inttofp_3_p2), .out(fpmultiplier_5_out));
  Controlled_Buffer #(.width(4)) controlled_buffer_17 (.in(binary_to_bcd_converter_7_p2), .en(or_17_out));  // open: out
  or or_17 (or_17_out, binary_to_bcd_converter_7_p2[0], binary_to_bcd_converter_7_p2[1], binary_to_bcd_converter_7_p2[2], binary_to_bcd_converter_7_p2[3], or_16_out);
  // Binary_to_BCD_converter #(.binvalue(10)) binary_to_bcd_converter_7: pin names not known; wires that end beside it: binary_to_bcd_converter_7_p1, binary_to_bcd_converter_7_p2, binary_to_bcd_converter_7_p3, binary_to_bcd_converter_7_p4, binary_to_bcd_converter_7_p5
  _7_Segment_Display u_7_segment_display_19 (.dp(fpcomparator_2_p1));  // open: g, f, a, b, e, d, c
  // BCD_to_7_Segment_decoder bcd_to_7_segment_decoder_18: pin names not known
  Controlled_Buffer #(.width(4)) controlled_buffer_18 (.in(binary_to_bcd_converter_7_p4), .en(or_18_out));  // open: out
  or or_18 (or_18_out, binary_to_bcd_converter_7_p4[0], binary_to_bcd_converter_7_p4[1], binary_to_bcd_converter_7_p4[2], binary_to_bcd_converter_7_p4[3], or_17_out);
  Divider #(.width(64)) divider_4 (
    .a(divider_5_out), .b(64'h3e8), .out(divider_4_out), .rem(divider_4_rem));  // open: upper
  _7_Segment_Display u_7_segment_display_20 (.dp(fpcomparator_2_p1));  // open: g, f, a, b, e, d, c
  _7_Segment_Display u_7_segment_display_21 (.dp(fpcomparator_2_p1));  // open: g, f, a, b, e, d, c
  // BCD_to_7_Segment_decoder bcd_to_7_segment_decoder_19: pin names not known
  // BCD_to_7_Segment_decoder bcd_to_7_segment_decoder_20: pin names not known
  Controlled_Buffer #(.width(4)) controlled_buffer_19 (.in(binary_to_bcd_converter_7_p5), .en(or_19_out));  // open: out
  or or_19 (or_19_out, binary_to_bcd_converter_7_p5[0], binary_to_bcd_converter_7_p5[1], binary_to_bcd_converter_7_p5[2], binary_to_bcd_converter_7_p5[3], or_18_out);
  Bit_Extender #(.in_width(64), .out_width(10)) bit_extender_5 (.in(divider_4_rem), .out(binary_to_bcd_converter_7_p3));
  Controlled_Buffer #(.width(4)) controlled_buffer_20 (.in(binary_to_bcd_converter_8_p1), .en(or_20_out));  // open: out
  or or_20 (or_20_out, binary_to_bcd_converter_8_p1[0], binary_to_bcd_converter_8_p1[1], binary_to_bcd_converter_8_p1[2], binary_to_bcd_converter_8_p1[3], or_19_out);
  // Binary_to_BCD_converter #(.binvalue(10)) binary_to_bcd_converter_8: pin names not known; wires that end beside it: binary_to_bcd_converter_8_p1, binary_to_bcd_converter_8_p2, binary_to_bcd_converter_8_p3, binary_to_bcd_converter_8_p4
  _7_Segment_Display u_7_segment_display_22 (.dp(fpcomparator_2_p1));  // open: g, f, a, b, e, d, c
  // BCD_to_7_Segment_decoder bcd_to_7_segment_decoder_21: pin names not known
  Controlled_Buffer #(.width(4)) controlled_buffer_21 (.in(binary_to_bcd_converter_8_p3), .en(or_21_out));  // open: out
  or or_21 (or_21_out, binary_to_bcd_converter_8_p3[0], binary_to_bcd_converter_8_p3[1], binary_to_bcd_converter_8_p3[2], binary_to_bcd_converter_8_p3[3], or_20_out);
  Divider #(.width(64)) divider_5 (
    .a(divider_6_out), .b(64'h3e8), .out(divider_5_out), .rem(divider_5_rem));  // open: upper
  _7_Segment_Display u_7_segment_display_23 (.dp(fpcomparator_2_p1));  // open: g, f, a, b, e, d, c
  _7_Segment_Display u_7_segment_display_24 (.dp(fpcomparator_2_p1));  // open: g, f, a, b, e, d, c
  // BCD_to_7_Segment_decoder bcd_to_7_segment_decoder_22: pin names not known
  // BCD_to_7_Segment_decoder bcd_to_7_segment_decoder_23: pin names not known
  Controlled_Buffer #(.width(4)) controlled_buffer_22 (.in(binary_to_bcd_converter_8_p4), .en(or_22_out));  // open: out
  or or_22 (or_22_out, binary_to_bcd_converter_8_p4[0], binary_to_bcd_converter_8_p4[1], binary_to_bcd_converter_8_p4[2], binary_to_bcd_converter_8_p4[3], or_21_out);
  Bit_Extender #(.in_width(64), .out_width(10)) bit_extender_6 (.in(divider_5_rem), .out(binary_to_bcd_converter_8_p2));
  Controlled_Buffer #(.width(4)) controlled_buffer_23 (.in(binary_to_bcd_converter_9_p1), .en(or_23_out));  // open: out
  or or_23 (or_23_out, binary_to_bcd_converter_9_p1[0], binary_to_bcd_converter_9_p1[1], binary_to_bcd_converter_9_p1[2], binary_to_bcd_converter_9_p1[3], or_22_out);
  // Binary_to_BCD_converter #(.binvalue(10)) binary_to_bcd_converter_9: pin names not known; wires that end beside it: binary_to_bcd_converter_9_p1, binary_to_bcd_converter_9_p2, binary_to_bcd_converter_9_p3, binary_to_bcd_converter_9_p4
  _7_Segment_Display u_7_segment_display_25 (.dp(fpcomparator_2_p1));  // open: g, f, a, b, e, d, c
  // BCD_to_7_Segment_decoder bcd_to_7_segment_decoder_24: pin names not known
  Controlled_Buffer #(.width(4)) controlled_buffer_24 (.in(binary_to_bcd_converter_9_p3), .en(or_24_out));  // open: out
  or or_24 (or_24_out, binary_to_bcd_converter_9_p3[0], binary_to_bcd_converter_9_p3[1], binary_to_bcd_converter_9_p3[2], binary_to_bcd_converter_9_p3[3], or_23_out);
  Divider #(.width(64)) divider_6 (
    .a(multiplexer_2_out), .b(64'h3e8), .out(divider_6_out), .rem(divider_6_rem));  // open: upper
  _7_Segment_Display u_7_segment_display_26 (.dp(fpcomparator_2_p1));  // open: g, f, a, b, e, d, c
  _7_Segment_Display u_7_segment_display_27 (.dp(1'b1));  // open: g, f, a, b, e, d, c
  // BCD_to_7_Segment_decoder bcd_to_7_segment_decoder_25: pin names not known
  // BCD_to_7_Segment_decoder bcd_to_7_segment_decoder_26: pin names not known; wires that end beside it: bcd_to_7_segment_decoder_26_p1, bcd_to_7_segment_decoder_26_p1, or_3_out
  Controlled_Buffer #(.width(4)) controlled_buffer_25 (.in(binary_to_bcd_converter_9_p4), .en(or_25_out));  // open: out
  or or_25 (or_25_out, binary_to_bcd_converter_9_p4[0], binary_to_bcd_converter_9_p4[1], binary_to_bcd_converter_9_p4[2], binary_to_bcd_converter_9_p4[3], or_24_out);
  Bit_Extender #(.in_width(64), .out_width(10)) bit_extender_7 (.in(divider_6_rem), .out(binary_to_bcd_converter_9_p2));
endmodule

module SQRT (
  input  [31:0] S,
  output [31:0] RootOut
);

  wire comparator_1_eq, comparator_2_eq;
  wire [7:0] adder_1_out, adder_4_out, bit_extender_3_out, shifter_1_out, subtractor_1_out, subtractor_2_out,
       subtractor_3_out;
  wire [10:0] adder_2_out, adder_3_out, bit_extender_1_out, bit_extender_2_out, fpdivider_17_out_3,
       subtractor_4_out;
  wire [31:0] fpmultiplier_1_out, multiplexer_2_out;
  wire [31:31] fpdivider_17_out_2;
  wire [51:0] fpdivider_17_out;
  wire [63:0] fpadder_1_out, fpadder_2_out, fpadder_3_out, fpadder_4_out, fpadder_5_out, fpadder_6_out,
       fpadder_7_out, fpadder_8_out, fpdivider_1_out, fpdivider_2_out, fpdivider_3_out, fpdivider_4_out,
       fpdivider_5_out, fpdivider_6_out, fpdivider_7_out, fpdivider_8_out, fpdivider_9_out, fpdivider_10_out,
       fpdivider_11_out, fpdivider_12_out, fpdivider_13_out, fpdivider_14_out, fpdivider_15_out,
       fpdivider_16_out, fpmultiplier_2_out, inttofp_2_p2;

  // IntToFP #(.mode("unsigned"), .width(16)) inttofp_1: pin names not known; wires that end beside it: 16'h8, 32'h40000000, S, S
  Subtractor subtractor_1 (.a(S[30:23]), .b(8'h7f), .out(subtractor_1_out));  // open: bin, bout
  // Probe on subtractor_1_out
  // Probe on S[30:23]
  // Probe on S
  Shifter #(.shift("ar")) shifter_1 (.in(subtractor_1_out), .\dist (3'b001), .out(shifter_1_out));
  // Probe on shifter_1_out
  Comparator comparator_1 (.a(S[30:23]), .b({8{1'b0}}), .eq(comparator_1_eq));  // open: gt, lt
  Comparator comparator_2 (.a(S[30:23]), .b({8{1'b1}}), .eq(comparator_2_eq));  // open: gt, lt
  // Probe on RootOut
  // Probe on fpmultiplier_1_out
  FPMultiplier fpmultiplier_1 (.a(RootOut), .b(RootOut), .out(fpmultiplier_1_out));
  // Probe on S[30:23]
  // Probe on adder_1_out
  Adder adder_1 (.a(8'h7f), .b(shifter_1_out), .out(adder_1_out));  // open: cin, cout
  Subtractor subtractor_2 (.a(S[30:23]), .b(8'h7f), .out(subtractor_2_out));  // open: bin, bout
  Subtractor subtractor_3 (.a(adder_1_out), .b(8'h7f), .out(subtractor_3_out));  // open: bin, bout
  // Probe on subtractor_3_out
  Multiplexer #(.width(32)) multiplexer_1 (
    .in0(multiplexer_2_out), .in1({S[31], 31'h7f800000}), .out(RootOut), .sel(comparator_2_eq));
  assign bit_extender_1_out = {{3{subtractor_2_out[7]}}, subtractor_2_out};  // Bit_Extender bit_extender_1
  assign bit_extender_2_out = {{3{subtractor_3_out[7]}}, subtractor_3_out};  // Bit_Extender bit_extender_2
  // Probe on bit_extender_2_out
  Multiplexer #(.width(32)) multiplexer_2 (
    .in0({fpdivider_17_out_2[31], adder_4_out, fpdivider_17_out[51:29]}), .in1({S[31], {31{1'b0}}}),
    .out(multiplexer_2_out), .sel(comparator_1_eq));
  // Probe on {S[31], 31'h7f800000}
  // Probe on {S[31], adder_2_out, S[22:0], {29{1'b0}}}
  Adder #(.width(11)) adder_2 (.a(bit_extender_1_out), .b(11'h3ff), .out(adder_2_out));  // open: cin, cout
  Adder #(.width(11)) adder_3 (.a(bit_extender_2_out), .b(11'h3ff), .out(adder_3_out));  // open: cin, cout
  // Probe on {S[31], adder_3_out, S[22:0], {29{1'b0}}}
  // Probe on {S[31], adder_2_out, S[22:0], {29{1'b0}}}
  // IntToFP #(.fpwidth(64), .width(16)) inttofp_2: pin names not known; wires that end beside it: 16'h2, inttofp_2_p2
  // Probe on {S[31], adder_3_out, S[22:0], {29{1'b0}}}
  // Probe on fpdivider_1_out
  FPDivider #(.fpwidth(64)) fpdivider_1 (
    .a({S[31], adder_2_out, S[22:0], {29{1'b0}}}), .b({S[31], adder_3_out, S[22:0], {29{1'b0}}}),
    .out(fpdivider_1_out));
  FPDivider #(.fpwidth(64)) fpdivider_2 (
    .a({S[31], adder_2_out, S[22:0], {29{1'b0}}}), .b(fpadder_8_out), .out(fpdivider_2_out));
  FPDivider #(.fpwidth(64)) fpdivider_3 (
    .a({S[31], adder_2_out, S[22:0], {29{1'b0}}}), .b(fpdivider_11_out), .out(fpdivider_3_out));
  FPDivider #(.fpwidth(64)) fpdivider_4 (
    .a({S[31], adder_2_out, S[22:0], {29{1'b0}}}), .b(fpdivider_12_out), .out(fpdivider_4_out));
  FPDivider #(.fpwidth(64)) fpdivider_5 (
    .a({S[31], adder_2_out, S[22:0], {29{1'b0}}}), .b(fpdivider_13_out), .out(fpdivider_5_out));
  FPDivider #(.fpwidth(64)) fpdivider_6 (
    .a({S[31], adder_2_out, S[22:0], {29{1'b0}}}), .b(fpdivider_14_out), .out(fpdivider_6_out));
  FPDivider #(.fpwidth(64)) fpdivider_7 (
    .a({S[31], adder_2_out, S[22:0], {29{1'b0}}}), .b(fpdivider_15_out), .out(fpdivider_7_out));
  FPDivider #(.fpwidth(64)) fpdivider_8 (
    .a({S[31], adder_2_out, S[22:0], {29{1'b0}}}), .b(fpdivider_16_out), .out(fpdivider_8_out));
  // Probe on fpdivider_9_out
  FPDivider #(.fpwidth(64)) fpdivider_9 (.a(fpdivider_1_out), .b(inttofp_2_p2), .out(fpdivider_9_out));
  FPDivider #(.fpwidth(64)) fpdivider_10 (
    .a({S[31], adder_3_out, S[22:0], {29{1'b0}}}), .b(inttofp_2_p2), .out(fpdivider_10_out));
  // Probe on fpdivider_10_out
  FPAdder #(.fpwidth(64)) fpadder_1 (.a(fpdivider_2_out), .b(fpadder_8_out), .out(fpadder_1_out));
  FPAdder #(.fpwidth(64)) fpadder_2 (.a(fpdivider_3_out), .b(fpdivider_11_out), .out(fpadder_2_out));
  FPAdder #(.fpwidth(64)) fpadder_3 (.a(fpdivider_4_out), .b(fpdivider_12_out), .out(fpadder_3_out));
  FPAdder #(.fpwidth(64)) fpadder_4 (.a(fpdivider_5_out), .b(fpdivider_13_out), .out(fpadder_4_out));
  FPAdder #(.fpwidth(64)) fpadder_5 (.a(fpdivider_6_out), .b(fpdivider_14_out), .out(fpadder_5_out));
  FPAdder #(.fpwidth(64)) fpadder_6 (.a(fpdivider_7_out), .b(fpdivider_15_out), .out(fpadder_6_out));
  FPAdder #(.fpwidth(64)) fpadder_7 (.a(fpdivider_8_out), .b(fpdivider_16_out), .out(fpadder_7_out));
  // Probe on fpadder_8_out
  FPAdder #(.fpwidth(64)) fpadder_8 (.a(fpdivider_9_out), .b(fpdivider_10_out), .out(fpadder_8_out));
  // Probe on fpdivider_11_out
  FPDivider #(.fpwidth(64)) fpdivider_11 (.a(fpadder_1_out), .b(inttofp_2_p2), .out(fpdivider_11_out));
  // Probe on fpdivider_12_out
  FPDivider #(.fpwidth(64)) fpdivider_12 (.a(fpadder_2_out), .b(inttofp_2_p2), .out(fpdivider_12_out));
  // Probe on fpdivider_13_out
  FPDivider #(.fpwidth(64)) fpdivider_13 (.a(fpadder_3_out), .b(inttofp_2_p2), .out(fpdivider_13_out));
  // Probe on fpdivider_14_out
  FPDivider #(.fpwidth(64)) fpdivider_14 (.a(fpadder_4_out), .b(inttofp_2_p2), .out(fpdivider_14_out));
  // Probe on fpdivider_15_out
  FPDivider #(.fpwidth(64)) fpdivider_15 (.a(fpadder_5_out), .b(inttofp_2_p2), .out(fpdivider_15_out));
  // Probe on fpdivider_16_out
  FPDivider #(.fpwidth(64)) fpdivider_16 (.a(fpadder_6_out), .b(inttofp_2_p2), .out(fpdivider_16_out));
  // Probe on {fpdivider_17_out_2[31], fpdivider_17_out_3, fpdivider_17_out}
  FPDivider #(.fpwidth(64)) fpdivider_17 (
    .a(fpadder_7_out), .b(inttofp_2_p2), .out({fpdivider_17_out_2[31], fpdivider_17_out_3, fpdivider_17_out}));
  Subtractor #(.width(11)) subtractor_4 (
    .a(fpdivider_17_out_3), .b(11'h3ff), .out(subtractor_4_out));  // open: bin, bout
  // Probe on fpmultiplier_2_out
  FPMultiplier #(.fpwidth(64)) fpmultiplier_2 (
    .a({fpdivider_17_out_2[31], fpdivider_17_out_3, fpdivider_17_out}),
    .b({fpdivider_17_out_2[31], fpdivider_17_out_3, fpdivider_17_out}), .out(fpmultiplier_2_out));
  Bit_Extender #(.in_width(11), .out_width(8)) bit_extender_3 (.in(subtractor_4_out), .out(bit_extender_3_out));
  Adder adder_4 (.a(8'h7f), .b(bit_extender_3_out), .out(adder_4_out));  // open: cin, cout

  // Notes on the sheet:
  //   TODO: Startwert durch halbieren der Potenz
endmodule
