// Logisim project DoubleOutputTest.circ as structural Verilog: 2 circuits, main circuit main
module main (
);

  wire bcd_to_7_segment_decoder_1_p1, bcd_to_7_segment_decoder_2_p1, bcd_to_7_segment_decoder_3_p1, or_1_out,
       or_2_out, or_3_out, or_4_out, or_5_out, or_6_out;
  wire [2:0] controlled_buffer_3_out, controlled_buffer_4_out, controlled_buffer_6_out, undriven_2,
       undriven_4, undriven_6;
  wire [3:0] binary_to_bcd_converter_1_p2, binary_to_bcd_converter_1_p3, binary_to_bcd_converter_1_p4,
       binary_to_bcd_converter_2_p2, binary_to_bcd_converter_2_p3, binary_to_bcd_converter_2_p4,
       controlled_buffer_1_out, controlled_buffer_2_out, controlled_buffer_5_out, undriven, undriven_3,
       undriven_5;
  wire [31:0] fpadder_1_out, fpmultiplier_1_out, inttofp_1_p2, inttofp_2_p2;

  _7_Segment_Display u_7_segment_display_1 (
    .g(controlled_buffer_1_out[3]), .f(controlled_buffer_1_out[2]), .a(controlled_buffer_1_out[1]),
    .b(controlled_buffer_1_out[0]), .e(controlled_buffer_3_out[2]), .d(controlled_buffer_3_out[1]),
    .c(controlled_buffer_3_out[0]));  // open: dp
  // BCD_to_7_Segment_decoder bcd_to_7_segment_decoder_1: pin names not known; wires that end beside it: bcd_to_7_segment_decoder_1_p1
  // Probe on inttofp_1_p2
  // IntToFP #(.mode("unsigned"), .width(64)) inttofp_1: pin names not known; wires that end beside it: 64'hfffff, inttofp_1_p2
  FPMultiplier fpmultiplier_1 (.a(inttofp_1_p2), .b(inttofp_2_p2), .out(fpmultiplier_1_out));
  // IntToFP #(.mode("unsigned"), .width(64)) inttofp_2: pin names not known; wires that end beside it: 64'h1, inttofp_2_p2
  _7_Segment_Display u_7_segment_display_2 (
    .g(controlled_buffer_2_out[3]), .f(controlled_buffer_2_out[2]), .a(controlled_buffer_2_out[1]),
    .b(controlled_buffer_2_out[0]), .e(controlled_buffer_4_out[2]), .d(controlled_buffer_4_out[1]),
    .c(controlled_buffer_4_out[0]));  // open: dp
  assign controlled_buffer_1_out = or_1_out ? undriven : 4'bz;  // Controlled_Buffer controlled_buffer_1
  assign controlled_buffer_2_out = or_2_out ? undriven_3 : 4'bz;  // Controlled_Buffer controlled_buffer_2
  // BCD_to_7_Segment_decoder bcd_to_7_segment_decoder_2: pin names not known; wires that end beside it: bcd_to_7_segment_decoder_2_p1
  assign controlled_buffer_3_out = or_1_out ? undriven_2 : 3'bz;  // Controlled_Buffer controlled_buffer_3
  assign controlled_buffer_4_out = or_2_out ? undriven_4 : 3'bz;  // Controlled_Buffer controlled_buffer_4
  or or_1 (or_1_out, bcd_to_7_segment_decoder_1_p1, binary_to_bcd_converter_1_p2[0], binary_to_bcd_converter_1_p2[1], binary_to_bcd_converter_1_p2[2], binary_to_bcd_converter_1_p2[3]);
  // Binary_to_BCD_converter #(.binvalue(8)) binary_to_bcd_converter_1: pin names not known; wires that end beside it: 8'hf, binary_to_bcd_converter_1_p2, binary_to_bcd_converter_1_p3, binary_to_bcd_converter_1_p4
  // Probe on fpadder_1_out
  FPAdder fpadder_1 (.a(32'h40490fdb), .b(fpmultiplier_1_out), .out(fpadder_1_out));
  OutputFloat outputfloat_1 (.in_1(fpadder_1_out));
  // Probe on 32'h3f800000
  OutputFloat outputfloat_2 (.in_1(32'h3f800000));
  _7_Segment_Display u_7_segment_display_3 (
    .g(controlled_buffer_5_out[3]), .f(controlled_buffer_5_out[2]), .a(controlled_buffer_5_out[1]),
    .b(controlled_buffer_5_out[0]), .e(controlled_buffer_6_out[2]), .d(controlled_buffer_6_out[1]),
    .c(controlled_buffer_6_out[0]));  // open: dp
  assign controlled_buffer_5_out = or_3_out ? undriven_5 : 4'bz;  // Controlled_Buffer controlled_buffer_5
  // BCD_to_7_Segment_decoder bcd_to_7_segment_decoder_3: pin names not known; wires that end beside it: bcd_to_7_segment_decoder_3_p1
  assign controlled_buffer_6_out = or_3_out ? undriven_6 : 3'bz;  // Controlled_Buffer controlled_buffer_6
  or or_2 (or_2_out, bcd_to_7_segment_decoder_2_p1, binary_to_bcd_converter_1_p3[0], binary_to_bcd_converter_1_p3[1], binary_to_bcd_converter_1_p3[2], binary_to_bcd_converter_1_p3[3]);
  or or_3 (or_3_out, bcd_to_7_segment_decoder_3_p1, binary_to_bcd_converter_1_p4[0], binary_to_bcd_converter_1_p4[1], binary_to_bcd_converter_1_p4[2], binary_to_bcd_converter_1_p4[3]);
  _7_Segment_Display u_7_segment_display_4 ();  // open: g, f, a, b, e, d, c, dp
  _7_Segment_Display u_7_segment_display_5 ();  // open: g, f, a, b, e, d, c, dp
  // BCD_to_7_Segment_decoder bcd_to_7_segment_decoder_4: pin names not known
  // BCD_to_7_Segment_decoder bcd_to_7_segment_decoder_5: pin names not known
  Controlled_Buffer #(.width(4)) controlled_buffer_7 (.in(binary_to_bcd_converter_2_p2), .en(or_4_out));  // open: out
  or or_4 (or_4_out, binary_to_bcd_converter_2_p2[0], binary_to_bcd_converter_2_p2[1], binary_to_bcd_converter_2_p2[2], binary_to_bcd_converter_2_p2[3]);
  // Binary_to_BCD_converter #(.binvalue(8)) binary_to_bcd_converter_2: pin names not known; wires that end beside it: 8'ha, binary_to_bcd_converter_2_p2, binary_to_bcd_converter_2_p3, binary_to_bcd_converter_2_p4
  _7_Segment_Display u_7_segment_display_6 ();  // open: g, f, a, b, e, d, c, dp
  // BCD_to_7_Segment_decoder bcd_to_7_segment_decoder_6: pin names not known
  Controlled_Buffer #(.width(4)) controlled_buffer_8 (.in(binary_to_bcd_converter_2_p3), .en(or_5_out));  // open: out
  Controlled_Buffer #(.width(4)) controlled_buffer_9 (.in(binary_to_bcd_converter_2_p4), .en(or_6_out));  // open: out
  or or_5 (or_5_out, binary_to_bcd_converter_2_p3[0], binary_to_bcd_converter_2_p3[1], binary_to_bcd_converter_2_p3[2], binary_to_bcd_converter_2_p3[3], or_4_out);
  or or_6 (or_6_out, binary_to_bcd_converter_2_p4[0], binary_to_bcd_converter_2_p4[1], binary_to_bcd_converter_2_p4[2], binary_to_bcd_converter_2_p4[3], or_5_out);
endmodule

module OutputFloat (
  input  [31:0] in_1
);

  wire bcd_to_7_segment_decoder_26_p1, binary_to_bcd_converter_2_p1, binary_to_bcd_converter_4_p2,
       binary_to_bcd_converter_6_p2, fpcomparator_1_p3, fpcomparator_1_p4, fpcomparator_2_p1, inttofp_4_p2,
       or_1_out, or_2_out, or_3_out, or_4_out, or_5_out, or_6_out, or_7_out, or_8_out, or_9_out, or_10_out,
       or_11_out, or_12_out, or_13_out, or_14_out, or_15_out, or_16_out, or_17_out, or_18_out, or_19_out,
       or_20_out, or_21_out, or_22_out, or_23_out, or_24_out, or_25_out;
  wire [3:0] binary_to_bcd_converter_1_p2, binary_to_bcd_converter_1_p3, binary_to_bcd_converter_2_p2,
       binary_to_bcd_converter_3_p1, binary_to_bcd_converter_3_p4, binary_to_bcd_converter_3_p5,
       binary_to_bcd_converter_4_p1, binary_to_bcd_converter_4_p3, binary_to_bcd_converter_5_p1,
       binary_to_bcd_converter_5_p3, binary_to_bcd_converter_5_p4, binary_to_bcd_converter_6_p1,
       binary_to_bcd_converter_6_p3, binary_to_bcd_converter_7_p1, binary_to_bcd_converter_7_p3,
       binary_to_bcd_converter_8_p1, binary_to_bcd_converter_8_p2, binary_to_bcd_converter_8_p4,
       binary_to_bcd_converter_8_p5, binary_to_bcd_converter_9_p1, binary_to_bcd_converter_9_p3,
       binary_to_bcd_converter_9_p4, bit_extender_1_out, inttofp_2_p1, inttofp_5_p1;
  wire [9:0] binary_to_bcd_converter_1_p1, binary_to_bcd_converter_3_p2, binary_to_bcd_converter_5_p2,
       binary_to_bcd_converter_7_p2, binary_to_bcd_converter_8_p3, binary_to_bcd_converter_9_p2;
  wire [31:0] fpmultiplier_1_out, fpmultiplier_2_out, fpmultiplier_3_out, fpmultiplier_4_out,
       fpmultiplier_5_out, fpnegator_1_p2, fpsubtractor_1_out, fpsubtractor_2_out, fpsubtractor_3_out,
       inttofp_1_p2, inttofp_2_p2, inttofp_3_p2, inttofp_5_p2, inttofp_6_p2, multiplexer_1_out;
  wire [63:0] divider_1_out, divider_1_rem, divider_2_out, divider_2_rem, divider_3_out, divider_3_rem,
       divider_4_out, divider_4_rem, divider_5_out, divider_5_rem, divider_6_out, divider_6_rem,
       fptoint_2_p2, multiplexer_2_out;

  // Probe on in_1
  _7_Segment_Display u_7_segment_display_1 (.g(fpcomparator_1_p4));  // open: f, a, b, e, d, c, dp
  _7_Segment_Display u_7_segment_display_2 (.dp(fpcomparator_2_p1));  // open: g, f, a, b, e, d, c
  // BCD_to_7_Segment_decoder bcd_to_7_segment_decoder_1: pin names not known
  Controlled_Buffer #(.width(4)) controlled_buffer_1 (.in(bit_extender_1_out), .en(or_1_out));  // open: out
  Bit_Extender #(.in_width(64), .out_width(4)) bit_extender_1 (.in(divider_1_out), .out(bit_extender_1_out));
  // FPNegator fpnegator_1: pin names not known; wires that end beside it: in_1, fpnegator_1_p2
  // FPComparator fpcomparator_1: pin names not known; wires that end beside it: in_1, {32{1'b0}}, fpcomparator_1_p3, fpcomparator_1_p4
  // IntToFP #(.width(12)) inttofp_1: pin names not known; wires that end beside it: 12'h3e8, inttofp_1_p2
  or or_1 (or_1_out, bit_extender_1_out[0], bit_extender_1_out[1], bit_extender_1_out[2], bit_extender_1_out[3]);
  // Binary_to_BCD_converter #(.binvalue(10)) binary_to_bcd_converter_1: pin names not known; wires that end beside it: binary_to_bcd_converter_1_p1, binary_to_bcd_converter_1_p2, binary_to_bcd_converter_1_p3
  // Probe on multiplexer_1_out
  Multiplexer #(.width(32)) multiplexer_1 (
    .in0(fpnegator_1_p2), .in1(in_1), .out(multiplexer_1_out), .sel(fpcomparator_1_p3));
  _7_Segment_Display u_7_segment_display_3 ();  // open: g, f, a, b, e, d, c, dp
  // BCD_to_7_Segment_decoder bcd_to_7_segment_decoder_2: pin names not known
  // Binary_to_BCD_converter #(.binvalue(11)) binary_to_bcd_converter_2: pin names not known; wires that end beside it: binary_to_bcd_converter_2_p1, binary_to_bcd_converter_2_p2
  FPMultiplier fpmultiplier_1 (.a(fpsubtractor_3_out), .b(inttofp_1_p2), .out(fpmultiplier_1_out));
  _7_Segment_Display u_7_segment_display_4 (.dp(fpcomparator_2_p1));  // open: g, f, a, b, e, d, c
  _7_Segment_Display u_7_segment_display_5 (.dp(fpcomparator_2_p1));  // open: g, f, a, b, e, d, c
  // BCD_to_7_Segment_decoder bcd_to_7_segment_decoder_3: pin names not known
  // BCD_to_7_Segment_decoder bcd_to_7_segment_decoder_4: pin names not known
  Controlled_Buffer #(.width(4)) controlled_buffer_2 (.in(binary_to_bcd_converter_1_p2), .en(or_2_out));  // open: out
  Controlled_Buffer #(.width(4)) controlled_buffer_3 (.in(binary_to_bcd_converter_1_p3), .en(or_4_out));  // open: out
  or or_2 (or_2_out, binary_to_bcd_converter_1_p2[0], binary_to_bcd_converter_1_p2[1], binary_to_bcd_converter_1_p2[2], binary_to_bcd_converter_1_p2[3], or_1_out);
  Divider #(.width(64)) divider_1 (
    .a(divider_2_out), .b(64'h3e8), .out(divider_1_out), .rem(divider_1_rem));  // open: upper
  _7_Segment_Display u_7_segment_display_6 ();  // open: g, f, a, b, e, d, c, dp
  // BCD_to_7_Segment_decoder bcd_to_7_segment_decoder_5: pin names not known
  Controlled_Buffer #(.width(4)) controlled_buffer_4 (.in(binary_to_bcd_converter_2_p2), .en(or_3_out));  // open: out
  Controlled_Buffer #(.width(4)) controlled_buffer_5 (.in(inttofp_2_p1), .en(or_5_out));  // open: out
  or or_3 (or_3_out, binary_to_bcd_converter_2_p2[0], binary_to_bcd_converter_2_p2[1], binary_to_bcd_converter_2_p2[2], binary_to_bcd_converter_2_p2[3], or_5_out);
  // FPToInt #(.mode("floor"), .width(11)) fptoint_1: pin names not known; wires that end beside it: fpmultiplier_1_out, binary_to_bcd_converter_2_p1
  // IntToFP #(.width(11)) inttofp_2: pin names not known; wires that end beside it: inttofp_2_p1, inttofp_2_p2
  _7_Segment_Display u_7_segment_display_7 (.dp(fpcomparator_2_p1));  // open: g, f, a, b, e, d, c
  // BCD_to_7_Segment_decoder bcd_to_7_segment_decoder_6: pin names not known
  Controlled_Buffer #(.width(4)) controlled_buffer_6 (.in(binary_to_bcd_converter_3_p1), .en(or_7_out));  // open: out
  or or_4 (or_4_out, binary_to_bcd_converter_1_p3[0], binary_to_bcd_converter_1_p3[1], binary_to_bcd_converter_1_p3[2], binary_to_bcd_converter_1_p3[3], or_2_out);
  Bit_Extender #(.in_width(64), .out_width(10)) bit_extender_2 (.in(divider_1_rem), .out(binary_to_bcd_converter_1_p1));
  // IntToFP #(.width(12)) inttofp_3: pin names not known; wires that end beside it: 12'h3e8, inttofp_3_p2
  _7_Segment_Display u_7_segment_display_8 ();  // open: g, f, a, b, e, d, c, dp
  // BCD_to_7_Segment_decoder bcd_to_7_segment_decoder_7: pin names not known
  Controlled_Buffer #(.width(4)) controlled_buffer_7 (.in(binary_to_bcd_converter_4_p1), .en(or_6_out));  // open: out
  or or_5 (or_5_out, inttofp_2_p1[0], inttofp_2_p1[1], inttofp_2_p1[2], inttofp_2_p1[3], or_6_out);
  or or_6 (or_6_out, binary_to_bcd_converter_4_p1[0], binary_to_bcd_converter_4_p1[1], binary_to_bcd_converter_4_p1[2], binary_to_bcd_converter_4_p1[3], or_9_out);
  FPSubtractor fpsubtractor_1 (.a(fpmultiplier_1_out), .b(inttofp_2_p2), .out(fpsubtractor_1_out));
  or or_7 (or_7_out, binary_to_bcd_converter_3_p1[0], binary_to_bcd_converter_3_p1[1], binary_to_bcd_converter_3_p1[2], binary_to_bcd_converter_3_p1[3], or_4_out);
  // Binary_to_BCD_converter #(.binvalue(10)) binary_to_bcd_converter_3: pin names not known; wires that end beside it: binary_to_bcd_converter_3_p1, binary_to_bcd_converter_3_p2, {64{1'b1}}, binary_to_bcd_converter_3_p4, binary_to_bcd_converter_3_p5
  // IntToFP #(.mode("unsigned"), .width(64)) inttofp_4: pin names not known; wires that end beside it: 64'h7fffffffffffffff, inttofp_4_p2, multiplexer_1_out, inttofp_4_p2
  _7_Segment_Display u_7_segment_display_9 ();  // open: g, f, a, b, e, d, c, dp
  // BCD_to_7_Segment_decoder bcd_to_7_segment_decoder_8: pin names not known
  // Binary_to_BCD_converter #(.binvalue(11)) binary_to_bcd_converter_4: pin names not known; wires that end beside it: binary_to_bcd_converter_4_p1, binary_to_bcd_converter_4_p2, binary_to_bcd_converter_4_p3
  FPMultiplier fpmultiplier_2 (.a(fpsubtractor_1_out), .b(inttofp_1_p2), .out(fpmultiplier_2_out));
  _7_Segment_Display u_7_segment_display_10 (.dp(fpcomparator_2_p1));  // open: g, f, a, b, e, d, c
  _7_Segment_Display u_7_segment_display_11 (.dp(fpcomparator_2_p1));  // open: g, f, a, b, e, d, c
  // BCD_to_7_Segment_decoder bcd_to_7_segment_decoder_9: pin names not known
  // BCD_to_7_Segment_decoder bcd_to_7_segment_decoder_10: pin names not known
  Controlled_Buffer #(.width(4)) controlled_buffer_8 (.in(binary_to_bcd_converter_3_p4), .en(or_8_out));  // open: out
  Controlled_Buffer #(.width(4)) controlled_buffer_9 (.in(binary_to_bcd_converter_3_p5), .en(or_10_out));  // open: out
  or or_8 (or_8_out, binary_to_bcd_converter_3_p4[0], binary_to_bcd_converter_3_p4[1], binary_to_bcd_converter_3_p4[2], binary_to_bcd_converter_3_p4[3], or_7_out);
  Divider #(.width(64)) divider_2 (
    .a(divider_3_out), .b(64'h3e8), .out(divider_2_out), .rem(divider_2_rem));  // open: upper
  // FPToInt #(.mode("floor"), .width(64)) fptoint_2: pin names not known; wires that end beside it: multiplexer_1_out, fptoint_2_p2
  // FPComparator fpcomparator_2: pin names not known; wires that end beside it: fpcomparator_2_p1
  // Probe on inttofp_4_p2
  _7_Segment_Display u_7_segment_display_12 ();  // open: g, f, a, b, e, d, c, dp
  // BCD_to_7_Segment_decoder bcd_to_7_segment_decoder_11: pin names not known
  Controlled_Buffer #(.width(4)) controlled_buffer_10 (.in(binary_to_bcd_converter_4_p3), .en(or_9_out));  // open: out
  Controlled_Buffer #(.width(4)) controlled_buffer_11 (.in(inttofp_5_p1), .en(or_11_out));  // open: out
  or or_9 (or_9_out, binary_to_bcd_converter_4_p3[0], binary_to_bcd_converter_4_p3[1], binary_to_bcd_converter_4_p3[2], binary_to_bcd_converter_4_p3[3], or_11_out);
  // FPToInt #(.mode("floor"), .width(11)) fptoint_3: pin names not known; wires that end beside it: fpmultiplier_2_out, binary_to_bcd_converter_4_p2
  // IntToFP #(.width(11)) inttofp_5: pin names not known; wires that end beside it: inttofp_5_p1, inttofp_5_p2
  _7_Segment_Display u_7_segment_display_13 (.dp(fpcomparator_2_p1));  // open: g, f, a, b, e, d, c
  // BCD_to_7_Segment_decoder bcd_to_7_segment_decoder_12: pin names not known
  Controlled_Buffer #(.width(4)) controlled_buffer_12 (.in(binary_to_bcd_converter_5_p1), .en(or_13_out));  // open: out
  or or_10 (or_10_out, binary_to_bcd_converter_3_p5[0], binary_to_bcd_converter_3_p5[1], binary_to_bcd_converter_3_p5[2], binary_to_bcd_converter_3_p5[3], or_8_out);
  Bit_Extender #(.in_width(64), .out_width(10)) bit_extender_3 (.in(divider_2_rem), .out(binary_to_bcd_converter_3_p2));
  // Probe on fptoint_2_p2
  _7_Segment_Display u_7_segment_display_14 ();  // open: g, f, a, b, e, d, c, dp
  // BCD_to_7_Segment_decoder bcd_to_7_segment_decoder_13: pin names not known
  Controlled_Buffer #(.width(4)) controlled_buffer_13 (.in(binary_to_bcd_converter_6_p1), .en(or_12_out));  // open: out
  or or_11 (or_11_out, inttofp_5_p1[0], inttofp_5_p1[1], inttofp_5_p1[2], inttofp_5_p1[3], or_12_out);
  or or_12 (or_12_out, binary_to_bcd_converter_6_p1[0], binary_to_bcd_converter_6_p1[1], binary_to_bcd_converter_6_p1[2], binary_to_bcd_converter_6_p1[3], or_15_out);
  FPSubtractor fpsubtractor_2 (.a(fpmultiplier_2_out), .b(inttofp_5_p2), .out(fpsubtractor_2_out));
  or or_13 (or_13_out, binary_to_bcd_converter_5_p1[0], binary_to_bcd_converter_5_p1[1], binary_to_bcd_converter_5_p1[2], binary_to_bcd_converter_5_p1[3], or_10_out);
  // Binary_to_BCD_converter #(.binvalue(10)) binary_to_bcd_converter_5: pin names not known; wires that end beside it: binary_to_bcd_converter_5_p1, binary_to_bcd_converter_5_p2, binary_to_bcd_converter_5_p3, binary_to_bcd_converter_5_p4
  Multiplexer #(.width(64)) multiplexer_2 (
    .in0(fptoint_2_p2), .in1({64{1'b0}}), .out(multiplexer_2_out), .sel(fpcomparator_2_p1));
  // Probe on fpsubtractor_3_out
  FPSubtractor fpsubtractor_3 (.a(multiplexer_1_out), .b(inttofp_6_p2), .out(fpsubtractor_3_out));
  // IntToFP #(.width(64)) inttofp_6: pin names not known; wires that end beside it: fptoint_2_p2, inttofp_6_p2
  _7_Segment_Display u_7_segment_display_15 ();  // open: g, f, a, b, e, d, c, dp
  // BCD_to_7_Segment_decoder bcd_to_7_segment_decoder_14: pin names not known
  // Binary_to_BCD_converter #(.binvalue(11)) binary_to_bcd_converter_6: pin names not known; wires that end beside it: binary_to_bcd_converter_6_p1, binary_to_bcd_converter_6_p2, binary_to_bcd_converter_6_p3
  FPMultiplier fpmultiplier_3 (.a(fpsubtractor_2_out), .b(inttofp_1_p2), .out(fpmultiplier_3_out));
  _7_Segment_Display u_7_segment_display_16 (.dp(fpcomparator_2_p1));  // open: g, f, a, b, e, d, c
  _7_Segment_Display u_7_segment_display_17 (.dp(fpcomparator_2_p1));  // open: g, f, a, b, e, d, c
  // BCD_to_7_Segment_decoder bcd_to_7_segment_decoder_15: pin names not known
  // BCD_to_7_Segment_decoder bcd_to_7_segment_decoder_16: pin names not known
  Controlled_Buffer #(.width(4)) controlled_buffer_14 (.in(binary_to_bcd_converter_5_p3), .en(or_14_out));  // open: out
  Controlled_Buffer #(.width(4)) controlled_buffer_15 (.in(binary_to_bcd_converter_5_p4), .en(or_16_out));  // open: out
  or or_14 (or_14_out, binary_to_bcd_converter_5_p3[0], binary_to_bcd_converter_5_p3[1], binary_to_bcd_converter_5_p3[2], binary_to_bcd_converter_5_p3[3], or_13_out);
  Divider #(.width(64)) divider_3 (
    .a(divider_4_out), .b(64'h3e8), .out(divider_3_out), .rem(divider_3_rem));  // open: upper
  FPMultiplier fpmultiplier_4 (.a(inttofp_3_p2), .b(inttofp_3_p2), .out(fpmultiplier_4_out));
  Controlled_Buffer #(.width(4)) controlled_buffer_16 (.in(binary_to_bcd_converter_6_p3), .en(or_15_out));  // open: out
  or or_15 (or_15_out, binary_to_bcd_converter_6_p3[0], binary_to_bcd_converter_6_p3[1], binary_to_bcd_converter_6_p3[2], binary_to_bcd_converter_6_p3[3]);
  // FPToInt #(.mode("floor"), .width(11)) fptoint_4: pin names not known; wires that end beside it: fpmultiplier_3_out, binary_to_bcd_converter_6_p2
  _7_Segment_Display u_7_segment_display_18 (.dp(fpcomparator_2_p1));  // open: g, f, a, b, e, d, c
  // BCD_to_7_Segment_decoder bcd_to_7_segment_decoder_17: pin names not known
  Controlled_Buffer #(.width(4)) controlled_buffer_17 (.in(binary_to_bcd_converter_7_p1), .en(or_17_out));  // open: out
  or or_16 (or_16_out, binary_to_bcd_converter_5_p4[0], binary_to_bcd_converter_5_p4[1], binary_to_bcd_converter_5_p4[2], binary_to_bcd_converter_5_p4[3], or_14_out);
  Bit_Extender #(.in_width(64), .out_width(10)) bit_extender_4 (.in(divider_3_rem), .out(binary_to_bcd_converter_5_p2));
  // Probe on fpmultiplier_5_out
  FPMultiplier fpmultiplier_5 (.a(fpsubtractor_3_out), .b(fpmultiplier_4_out), .out(fpmultiplier_5_out));
  or or_17 (or_17_out, binary_to_bcd_converter_7_p1[0], binary_to_bcd_converter_7_p1[1], binary_to_bcd_converter_7_p1[2], binary_to_bcd_converter_7_p1[3], or_16_out);
  // Binary_to_BCD_converter #(.binvalue(10)) binary_to_bcd_converter_7: pin names not known; wires that end beside it: binary_to_bcd_converter_7_p1, binary_to_bcd_converter_7_p2, binary_to_bcd_converter_7_p3
  _7_Segment_Display u_7_segment_display_19 (.dp(fpcomparator_2_p1));  // open: g, f, a, b, e, d, c
  _7_Segment_Display u_7_segment_display_20 (.dp(fpcomparator_2_p1));  // open: g, f, a, b, e, d, c
  // BCD_to_7_Segment_decoder bcd_to_7_segment_decoder_18: pin names not known
  // BCD_to_7_Segment_decoder bcd_to_7_segment_decoder_19: pin names not known
  Controlled_Buffer #(.width(4)) controlled_buffer_18 (.in(binary_to_bcd_converter_7_p3), .en(or_18_out));  // open: out
  Controlled_Buffer #(.width(4)) controlled_buffer_19 (.in(binary_to_bcd_converter_8_p1), .en(or_19_out));  // open: out
  or or_18 (or_18_out, binary_to_bcd_converter_7_p3[0], binary_to_bcd_converter_7_p3[1], binary_to_bcd_converter_7_p3[2], binary_to_bcd_converter_7_p3[3], or_17_out);
  Divider #(.width(64)) divider_4 (
    .a(divider_5_out), .b(64'h3e8), .out(divider_4_out), .rem(divider_4_rem));  // open: upper
  _7_Segment_Display u_7_segment_display_21 (.dp(fpcomparator_2_p1));  // open: g, f, a, b, e, d, c
  // BCD_to_7_Segment_decoder bcd_to_7_segment_decoder_20: pin names not known
  Controlled_Buffer #(.width(4)) controlled_buffer_20 (.in(binary_to_bcd_converter_8_p2), .en(or_20_out));  // open: out
  or or_19 (or_19_out, binary_to_bcd_converter_8_p1[0], binary_to_bcd_converter_8_p1[1], binary_to_bcd_converter_8_p1[2], binary_to_bcd_converter_8_p1[3], or_18_out);
  Bit_Extender #(.in_width(64), .out_width(10)) bit_extender_5 (.in(divider_4_rem), .out(binary_to_bcd_converter_7_p2));
  or or_20 (or_20_out, binary_to_bcd_converter_8_p2[0], binary_to_bcd_converter_8_p2[1], binary_to_bcd_converter_8_p2[2], binary_to_bcd_converter_8_p2[3], or_19_out);
  // Binary_to_BCD_converter #(.binvalue(10)) binary_to_bcd_converter_8: pin names not known; wires that end beside it: binary_to_bcd_converter_8_p1, binary_to_bcd_converter_8_p2, binary_to_bcd_converter_8_p3, binary_to_bcd_converter_8_p4, binary_to_bcd_converter_8_p5
  _7_Segment_Display u_7_segment_display_22 (.dp(fpcomparator_2_p1));  // open: g, f, a, b, e, d, c
  _7_Segment_Display u_7_segment_display_23 (.dp(fpcomparator_2_p1));  // open: g, f, a, b, e, d, c
  // BCD_to_7_Segment_decoder bcd_to_7_segment_decoder_21: pin names not known
  // BCD_to_7_Segment_decoder bcd_to_7_segment_decoder_22: pin names not known
  Controlled_Buffer #(.width(4)) controlled_buffer_21 (.in(binary_to_bcd_converter_8_p4), .en(or_21_out));  // open: out
  Controlled_Buffer #(.width(4)) controlled_buffer_22 (.in(binary_to_bcd_converter_8_p5), .en(or_22_out));  // open: out
  or or_21 (or_21_out, binary_to_bcd_converter_8_p4[0], binary_to_bcd_converter_8_p4[1], binary_to_bcd_converter_8_p4[2], binary_to_bcd_converter_8_p4[3], or_20_out);
  Divider #(.width(64)) divider_5 (
    .a(divider_6_out), .b(64'h3e8), .out(divider_5_out), .rem(divider_5_rem));  // open: upper
  _7_Segment_Display u_7_segment_display_24 (.dp(fpcomparator_2_p1));  // open: g, f, a, b, e, d, c
  // BCD_to_7_Segment_decoder bcd_to_7_segment_decoder_23: pin names not known
  Controlled_Buffer #(.width(4)) controlled_buffer_23 (.in(binary_to_bcd_converter_9_p1), .en(or_23_out));  // open: out
  or or_22 (or_22_out, binary_to_bcd_converter_8_p5[0], binary_to_bcd_converter_8_p5[1], binary_to_bcd_converter_8_p5[2], binary_to_bcd_converter_8_p5[3], or_21_out);
  Bit_Extender #(.in_width(64), .out_width(10)) bit_extender_6 (.in(divider_5_rem), .out(binary_to_bcd_converter_8_p3));
  or or_23 (or_23_out, binary_to_bcd_converter_9_p1[0], binary_to_bcd_converter_9_p1[1], binary_to_bcd_converter_9_p1[2], binary_to_bcd_converter_9_p1[3], or_22_out);
  // Binary_to_BCD_converter #(.binvalue(10)) binary_to_bcd_converter_9: pin names not known; wires that end beside it: binary_to_bcd_converter_9_p1, binary_to_bcd_converter_9_p2, binary_to_bcd_converter_9_p3, binary_to_bcd_converter_9_p4
  _7_Segment_Display u_7_segment_display_25 (.dp(fpcomparator_2_p1));  // open: g, f, a, b, e, d, c
  _7_Segment_Display u_7_segment_display_26 (.dp(fpcomparator_2_p1));  // open: g, f, a, b, e, d, c
  // BCD_to_7_Segment_decoder bcd_to_7_segment_decoder_24: pin names not known
  // BCD_to_7_Segment_decoder bcd_to_7_segment_decoder_25: pin names not known
  Controlled_Buffer #(.width(4)) controlled_buffer_24 (.in(binary_to_bcd_converter_9_p3), .en(or_24_out));  // open: out
  Controlled_Buffer #(.width(4)) controlled_buffer_25 (.in(binary_to_bcd_converter_9_p4), .en(or_25_out));  // open: out
  or or_24 (or_24_out, binary_to_bcd_converter_9_p3[0], binary_to_bcd_converter_9_p3[1], binary_to_bcd_converter_9_p3[2], binary_to_bcd_converter_9_p3[3], or_23_out);
  Divider #(.width(64)) divider_6 (
    .a(multiplexer_2_out), .b(64'h3e8), .out(divider_6_out), .rem(divider_6_rem));  // open: upper
  _7_Segment_Display u_7_segment_display_27 (.dp(or_3_out));  // open: g, f, a, b, e, d, c
  // BCD_to_7_Segment_decoder bcd_to_7_segment_decoder_26: pin names not known; wires that end beside it: bcd_to_7_segment_decoder_26_p1, bcd_to_7_segment_decoder_26_p1, 1'b1
  or or_25 (or_25_out, binary_to_bcd_converter_9_p4[0], binary_to_bcd_converter_9_p4[1], binary_to_bcd_converter_9_p4[2], binary_to_bcd_converter_9_p4[3], or_24_out);
  Bit_Extender #(.in_width(64), .out_width(10)) bit_extender_7 (.in(divider_6_rem), .out(binary_to_bcd_converter_9_p2));
endmodule
