// Logisim project 8BitComputer.circ as structural Verilog: 12 circuits, main circuit main
module main (
  input  in_1,
  input  in_2
);

  wire alu_1_carryout, button_1_out, button_2_out, button_3_out, control_1_clr, control_1_counterenable,
       control_1_hlt, control_1_notain, control_1_notaout, control_1_notbin, control_1_notclr,
       control_1_notcounterout, control_1_notequationout, control_1_notflagsin, control_1_notinstructionin,
       control_1_notinstructionout, control_1_notjump, control_1_notmemoryin, control_1_notramout,
       control_1_outputin, control_1_ramin, control_1_subtract, dipswitch_1_sw1, dipswitch_1_sw2,
       dipswitch_1_sw3, dipswitch_1_sw4, dipswitch_1_sw5, dipswitch_1_sw6, dipswitch_1_sw7, dipswitch_1_sw8,
       dipswitch_2_sw1, dipswitch_2_sw2, dipswitch_2_sw3, dipswitch_2_sw4, myclock_1_clk, myclock_1_notclk,
       registerflags_1_carryflag, registerflags_1_zeroflag, registermemoryaddress_1_notprogrammingmode;
  wire [3:0] registerinstructions_1_instructionout4_7, registermemoryaddress_1_adressout;
  wire [7:0] alu_1_aluout, rammodule_1_busout, registera_1_aout, registerb_1_bout;

  Button button_1 (.out(button_1_out));
  Button button_2 (.out(button_2_out));
  DipSwitch dipswitch_1 (
    .sw1(dipswitch_1_sw1), .sw2(dipswitch_1_sw2), .sw3(dipswitch_1_sw3), .sw4(dipswitch_1_sw4),
    .sw5(dipswitch_1_sw5), .sw6(dipswitch_1_sw6), .sw7(dipswitch_1_sw7), .sw8(dipswitch_1_sw8));
  MyClock myclock_1 (
    .NotCLK(myclock_1_notclk), .CLK(myclock_1_clk), .CLKSwitch(in_1), .CLKPush(button_1_out),
    .HLT(control_1_hlt));
  RegisterMemoryAddress registermemoryaddress_1 (
    .AdressOut(registermemoryaddress_1_adressout),
    .NotProgrammingMode(registermemoryaddress_1_notprogrammingmode), .CLK(myclock_1_clk),
    .CLR(control_1_clr), .NotMemoryIn(control_1_notmemoryin), .Dip0In(dipswitch_2_sw4),
    .Dip1In(dipswitch_2_sw3), .Dip2In(dipswitch_2_sw2), .Dip3In(dipswitch_2_sw1),
    .NotProgrammingSwitch(in_2), .BusIn(rammodule_1_busout));
  DipSwitch #(.number(4)) dipswitch_2 (
    .sw1(dipswitch_2_sw1), .sw2(dipswitch_2_sw2), .sw3(dipswitch_2_sw3), .sw4(dipswitch_2_sw4));
  RAMModule rammodule_1 (
    .BusOut(rammodule_1_busout), .ClockPush(button_2_out), .RAMIn(control_1_ramin), .CLK(myclock_1_clk),
    .ProgMode(registermemoryaddress_1_notprogrammingmode), .Dip0In(dipswitch_1_sw8),
    .Dip1In(dipswitch_1_sw7), .Dip2In(dipswitch_1_sw6), .Dip3In(dipswitch_1_sw5), .Dip4In(dipswitch_1_sw4),
    .Dip5In(dipswitch_1_sw3), .Dip6In(dipswitch_1_sw2), .Dip7In(dipswitch_1_sw1), .BusIn(rammodule_1_busout),
    .AddressIn(registermemoryaddress_1_adressout), .NotRAMOut(control_1_notramout));
  RegisterInstructions registerinstructions_1 (
    .BusOut(rammodule_1_busout), .InstructionOut4_7(registerinstructions_1_instructionout4_7),
    .BusIn(rammodule_1_busout), .CLK(myclock_1_clk), .CLR(control_1_clr),
    .NotInstructionIn(control_1_notinstructionin), .NotInstructionOut(control_1_notinstructionout));
  Button button_3 (.out(button_3_out));
  LedBar ledbar_1 (
    .led0(rammodule_1_busout[7]), .led1(rammodule_1_busout[6]), .led2(rammodule_1_busout[5]),
    .led3(rammodule_1_busout[4]), .led4(rammodule_1_busout[3]), .led5(rammodule_1_busout[2]),
    .led6(rammodule_1_busout[1]), .led7(rammodule_1_busout[0]));
  ProgramCounter programcounter_1 (
    .BusOut(rammodule_1_busout), .BusIn(rammodule_1_busout), .NotJump(control_1_notjump),
    .CLK(myclock_1_clk), .NotCLR(control_1_notclr), .CounterEnable(control_1_counterenable),
    .NotCounterOut(control_1_notcounterout));
  RegisterOutput registeroutput_1 (
    .BusIn(rammodule_1_busout), .OutputIn(control_1_outputin), .CLK(myclock_1_clk), .NotCLR(control_1_notclr));
  RegisterA registera_1 (
    .AOut(registera_1_aout), .BusOut(rammodule_1_busout), .BusIn(rammodule_1_busout), .CLK(myclock_1_clk),
    .CLR(control_1_clr), .NotAIn(control_1_notain), .NotAOut(control_1_notaout));
  ALU alu_1 (
    .BusOut(rammodule_1_busout), .ALUOut(alu_1_aluout), .CarryOut(alu_1_carryout), .AIn(registera_1_aout),
    .BIn(registerb_1_bout), .Subtract(control_1_subtract), .NotEOut(control_1_notequationout));
  RegisterB registerb_1 (
    .BOut(registerb_1_bout), .BusOut(rammodule_1_busout), .BusIn(rammodule_1_busout), .CLK(myclock_1_clk),
    .CLR(control_1_clr), .NotBIn(control_1_notbin), .NotBOut(1'b1));
  Control control_1 (
    .HLT(control_1_hlt), .NotMemoryIn(control_1_notmemoryin), .RAMIn(control_1_ramin),
    .NotRAMOut(control_1_notramout), .NotInstructionOut(control_1_notinstructionout),
    .NotInstructionIn(control_1_notinstructionin), .NotAIn(control_1_notain), .NotAOut(control_1_notaout),
    .NotEquationOut(control_1_notequationout), .Subtract(control_1_subtract), .NotBIn(control_1_notbin),
    .OutputIn(control_1_outputin), .CounterEnable(control_1_counterenable),
    .NotCounterOut(control_1_notcounterout), .NotJump(control_1_notjump), .NotFlagsIn(control_1_notflagsin),
    .CLR(control_1_clr), .NotCLR(control_1_notclr), .NotCLK(myclock_1_notclk), .PushReset(button_3_out),
    .InstructionIn(registerinstructions_1_instructionout4_7), .CarryFlag(registerflags_1_carryflag),
    .ZeroFlag(registerflags_1_zeroflag));
  RegisterFlags registerflags_1 (
    .ZeroFlag(registerflags_1_zeroflag), .CarryFlag(registerflags_1_carryflag), .CarryIn(alu_1_carryout),
    .CLK(myclock_1_clk), .CLR(control_1_clr), .NotFlagsIn(control_1_notflagsin), .ALUIn(alu_1_aluout));
endmodule

module MyClock (
  input  CLKSwitch,
  input  CLKPush,
  input  HLT,
  output NotCLK,
  output CLK
);

  wire and_1_out, and_2_out, clock_1_out, not_1_out, not_2_out, or_1_out;

  Clock clock_1 (.out(clock_1_out));
  not not_1 (not_1_out, CLKSwitch);
  and and_1 (and_1_out, clock_1_out, CLKSwitch);
  LED led_1 (.in(CLKSwitch));
  LED led_2 (.in(not_1_out));
  and and_2 (and_2_out, not_1_out, CLKPush);
  or or_1 (or_1_out, and_1_out, and_2_out);
  not not_2 (not_2_out, HLT);
  and and_3 (CLK, or_1_out, not_2_out);
  not not_3 (NotCLK, CLK);
  LED led_3 (.in(CLK));
endmodule

module RegisterA (
  input  [7:0] BusIn,
  input  CLK,
  input  CLR,
  input  NotAIn,
  input  NotAOut,
  output [7:0] AOut,
  output [7:0] BusOut
);

  wire not_1_out, not_2_out;

  Register register_1 (.D(BusIn), .en(not_1_out), .clk(CLK), .Q(AOut), .clr(CLR));
  not not_1 (not_1_out, NotAIn);
  LED led_1 (.in(AOut[0]));
  LED led_2 (.in(AOut[1]));
  LED led_3 (.in(AOut[2]));
  LED led_4 (.in(AOut[3]));
  LED led_5 (.in(AOut[4]));
  LED led_6 (.in(AOut[5]));
  LED led_7 (.in(AOut[6]));
  LED led_8 (.in(AOut[7]));
  assign BusOut = not_2_out ? AOut : 8'bz;  // Controlled_Buffer controlled_buffer_1
  not not_2 (not_2_out, NotAOut);
endmodule

module RegisterB (
  input  [7:0] BusIn,
  input  CLK,
  input  CLR,
  input  NotBIn,
  input  NotBOut,
  output [7:0] BOut,
  output [7:0] BusOut
);

  wire not_1_out, not_2_out;

  Register register_1 (.D(BusIn), .en(not_1_out), .clk(CLK), .Q(BOut), .clr(CLR));
  not not_1 (not_1_out, NotBIn);
  assign BusOut = not_2_out ? BOut : 8'bz;  // Controlled_Buffer controlled_buffer_1
  not not_2 (not_2_out, NotBOut);
  LED led_1 (.in(BOut[0]));
  LED led_2 (.in(BOut[1]));
  LED led_3 (.in(BOut[2]));
  LED led_4 (.in(BOut[3]));
  LED led_5 (.in(BOut[4]));
  LED led_6 (.in(BOut[5]));
  LED led_7 (.in(BOut[6]));
  LED led_8 (.in(BOut[7]));
endmodule

module RegisterInstructions (
  input  [7:0] BusIn,
  input  CLK,
  input  CLR,
  input  NotInstructionIn,
  input  NotInstructionOut,
  output [3:0] InstructionOut4_7,
  output [7:0] BusOut
);

  wire not_1_out, not_2_out;
  wire [3:0] register_1_q;

  Register register_1 (.D(BusIn), .en(not_1_out), .clk(CLK), .Q({InstructionOut4_7, register_1_q}), .clr(CLR));
  not not_1 (not_1_out, NotInstructionIn);
  LED led_1 (.in(register_1_q[0]));
  LED led_2 (.in(register_1_q[1]));
  LED led_3 (.in(register_1_q[2]));
  LED led_4 (.in(register_1_q[3]));
  LED led_5 (.in(InstructionOut4_7[0]));
  LED led_6 (.in(InstructionOut4_7[1]));
  LED led_7 (.in(InstructionOut4_7[2]));
  LED led_8 (.in(InstructionOut4_7[3]));
  assign BusOut = not_2_out ? {4'b0000, register_1_q} : 8'bz;  // Controlled_Buffer controlled_buffer_1
  not not_2 (not_2_out, NotInstructionOut);
endmodule

module ALU (
  input  [7:0] AIn,
  input  [7:0] BIn,
  input  Subtract,
  input  NotEOut,
  output [7:0] BusOut,
  output [7:0] ALUOut,
  output CarryOut
);

  wire not_1_out;
  wire [7:0] xor_1_out;

  xor xor_1 (xor_1_out[0], BIn[0], Subtract);
  xor xor_2 (xor_1_out[1], BIn[1], Subtract);
  xor xor_3 (xor_1_out[2], BIn[2], Subtract);
  xor xor_4 (xor_1_out[3], BIn[3], Subtract);
  xor xor_5 (xor_1_out[4], BIn[4], Subtract);
  xor xor_6 (xor_1_out[5], BIn[5], Subtract);
  xor xor_7 (xor_1_out[6], BIn[6], Subtract);
  xor xor_8 (xor_1_out[7], BIn[7], Subtract);
  Adder adder_1 (.a(AIn), .b(xor_1_out), .out(ALUOut), .cin(Subtract), .cout(CarryOut));
  assign BusOut = not_1_out ? ALUOut : 8'bz;  // Controlled_Buffer controlled_buffer_1
  not not_1 (not_1_out, NotEOut);
  LED led_1 (.in(ALUOut[0]));
  LED led_2 (.in(ALUOut[1]));
  LED led_3 (.in(ALUOut[2]));
  LED led_4 (.in(ALUOut[3]));
  LED led_5 (.in(ALUOut[4]));
  LED led_6 (.in(ALUOut[5]));
  LED led_7 (.in(ALUOut[6]));
  LED led_8 (.in(ALUOut[7]));
endmodule

module RegisterFlags (
  input  [7:0] ALUIn,
  input  CarryIn,
  input  CLK,
  input  CLR,
  input  NotFlagsIn,
  output ZeroFlag,
  output CarryFlag
);

  wire and_1_out, and_3_out, nor_1_out, nor_2_out, nor_3_out, nor_4_out, not_1_out;
  wire [0:0] and_2_out;

  nor nor_1 (nor_1_out, ALUIn[0], ALUIn[1]);
  nor nor_2 (nor_2_out, ALUIn[2], ALUIn[3]);
  nor nor_3 (nor_3_out, ALUIn[4], ALUIn[5]);
  nor nor_4 (nor_4_out, ALUIn[6], ALUIn[7]);
  and and_1 (and_1_out, nor_1_out, nor_2_out);
  and and_2 (and_2_out[0], and_1_out, and_3_out);
  and and_3 (and_3_out, nor_3_out, nor_4_out);
  not not_1 (not_1_out, NotFlagsIn);
  Register #(.width(2)) register_1 (
    .D({CarryIn, and_2_out[0]}), .en(not_1_out), .clk(CLK), .Q({CarryFlag, ZeroFlag}), .clr(CLR));
  LED led_1 (.in(ZeroFlag));
  LED led_2 (.in(CarryFlag));
endmodule

module RegisterMemoryAddress (
  input  [7:0] BusIn,
  input  CLK,
  input  CLR,
  input  NotMemoryIn,
  input  Dip0In,
  input  Dip1In,
  input  Dip2In,
  input  Dip3In,
  input  NotProgrammingSwitch,
  output [3:0] AdressOut,
  output NotProgrammingMode
);

  wire not_1_out, not_2_out;
  wire [3:0] register_1_q;

  DipSwitch #(.number(4)) dipswitch_1 ();  // open: sw1, sw2, sw3, sw4
  not not_1 (not_1_out, NotProgrammingSwitch);
  LED led_1 (.in(not_1_out));
  LED led_2 (.in(NotProgrammingSwitch));
  Register #(.width(4)) register_1 (.D(BusIn[3:0]), .en(not_2_out), .clk(CLK), .Q(register_1_q), .clr(CLR));
  not not_2 (not_2_out, NotMemoryIn);
  LED led_3 (.in(AdressOut[0]));
  LED led_4 (.in(AdressOut[1]));
  LED led_5 (.in(AdressOut[2]));
  LED led_6 (.in(AdressOut[3]));
  Multiplexer #(.width(4)) multiplexer_1 (
    .in0({Dip3In, Dip2In, Dip1In, Dip0In}), .in1(register_1_q), .out(AdressOut), .sel(NotProgrammingSwitch));

  assign NotProgrammingMode = NotProgrammingSwitch;
endmodule

module RAMModule (
  input  [3:0] AddressIn,
  input  NotRAMOut,
  input  ClockPush,
  input  RAMIn,
  input  CLK,
  input  ProgMode,
  input  Dip0In,
  input  Dip1In,
  input  Dip2In,
  input  Dip3In,
  input  Dip4In,
  input  Dip5In,
  input  Dip6In,
  input  Dip7In,
  input  [7:0] BusIn,
  output [7:0] BusOut
);

  wire multiplexer_1_out, nand_1_out, not_1_out, not_2_out, not_3_out;
  wire [7:0] multiplexer_2_out, ram_1_dout;

  not not_1 (not_1_out, ClockPush);
  nand nand_1 (nand_1_out, RAMIn, CLK);
  not not_2 (not_2_out, multiplexer_1_out);
  Multiplexer multiplexer_1 (.in0(not_1_out), .in1(nand_1_out), .out(multiplexer_1_out), .sel(ProgMode));
  Multiplexer #(.width(8)) multiplexer_2 (
    .in0({Dip7In, Dip6In, Dip5In, Dip4In, Dip3In, Dip2In, Dip1In, Dip0In}), .in1(BusIn),
    .out(multiplexer_2_out), .sel(ProgMode));
  RAM #(.addrWidth(4), .trigger("high")) ram_1 (
    .addr(AddressIn), .we(not_2_out), .oe(1'b1), .din(multiplexer_2_out), .dout(ram_1_dout));  // open: clk
  not not_3 (not_3_out, NotRAMOut);
  assign BusOut = not_3_out ? ram_1_dout : 8'bz;  // Controlled_Buffer controlled_buffer_1
  LED led_1 (.in(ram_1_dout[0]));
  LED led_2 (.in(ram_1_dout[1]));
  LED led_3 (.in(ram_1_dout[2]));
  LED led_4 (.in(ram_1_dout[3]));
  LED led_5 (.in(ram_1_dout[4]));
  LED led_6 (.in(ram_1_dout[5]));
  LED led_7 (.in(ram_1_dout[6]));
  LED led_8 (.in(ram_1_dout[7]));
endmodule

module RegisterOutput (
  input  [7:0] BusIn,
  input  OutputIn,
  input  CLK,
  input  NotCLR
);

  wire and_1_out, not_1_out;
  wire [7:0] register_1_q;

  Register register_1 (.D(BusIn), .en(1'b1), .clk(and_1_out), .Q(register_1_q), .clr(not_1_out));
  and and_1 (and_1_out, OutputIn, CLK);
  not not_1 (not_1_out, NotCLR);
  _7_Segment_Display u_7_segment_display_1 ();  // open: g, f, a, b, e, d, c, dp
  // BCD_to_7_Segment_decoder bcd_to_7_segment_decoder_1: pin names not known
  // Binary_to_BCD_converter #(.binvalue(8)) binary_to_bcd_converter_1: pin names not known; wires that end beside it: register_1_q
  _7_Segment_Display u_7_segment_display_2 ();  // open: g, f, a, b, e, d, c, dp
  _7_Segment_Display u_7_segment_display_3 ();  // open: g, f, a, b, e, d, c, dp
  // BCD_to_7_Segment_decoder bcd_to_7_segment_decoder_2: pin names not known
  // BCD_to_7_Segment_decoder bcd_to_7_segment_decoder_3: pin names not known
endmodule

module ProgramCounter (
  input  [7:0] BusIn,
  input  NotJump,
  input  CLK,
  input  NotCLR,
  input  CounterEnable,
  input  NotCounterOut,
  output [7:0] BusOut
);

  wire not_1_out, not_2_out, not_3_out;
  wire [3:0] counter_1_q;

  not not_1 (not_1_out, NotJump);
  not not_2 (not_2_out, NotCLR);
  Counter #(.max('hf), .width(4)) counter_1 (
    .clr(not_2_out), .load(not_1_out), .up(1'b1), .count(CounterEnable), .clk(CLK), .D(BusIn[3:0]),
    .Q(counter_1_q));  // open: carry
  LED led_1 (.in(counter_1_q[0]));
  LED led_2 (.in(counter_1_q[1]));
  LED led_3 (.in(counter_1_q[2]));
  LED led_4 (.in(counter_1_q[3]));
  assign BusOut = not_3_out ? {4'b0000, counter_1_q} : 8'bz;  // Controlled_Buffer controlled_buffer_1
  not not_3 (not_3_out, NotCounterOut);
  _7_Segment_Display u_7_segment_display_1 ();  // open: g, f, a, b, e, d, c, dp
  // BCD_to_7_Segment_decoder bcd_to_7_segment_decoder_1: pin names not known
  // Binary_to_BCD_converter #(.binvalue(4)) binary_to_bcd_converter_1: pin names not known; wires that end beside it: counter_1_q
  _7_Segment_Display u_7_segment_display_2 ();  // open: g, f, a, b, e, d, c, dp
  // BCD_to_7_Segment_decoder bcd_to_7_segment_decoder_2: pin names not known
endmodule

module Control (
  input  [3:0] InstructionIn,
  input  NotCLK,
  input  CarryFlag,
  input  ZeroFlag,
  input  PushReset,
  output HLT,
  output NotMemoryIn,
  output RAMIn,
  output NotRAMOut,
  output NotInstructionOut,
  output NotInstructionIn,
  output NotAIn,
  output NotAOut,
  output NotEquationOut,
  output Subtract,
  output NotBIn,
  output OutputIn,
  output CLR,
  output CounterEnable,
  output NotCLR,
  output NotCounterOut,
  output NotJump,
  output NotFlagsIn
);

  wire decoder_1_out0, decoder_1_out1, decoder_1_out2, decoder_1_out3, decoder_1_out4, decoder_1_out5,
       nand_1_out, not_1_out;
  wire [2:0] counter_1_q_2;
  wire [3:3] counter_1_q;
  wire [14:0] rom_1_data;

  Counter #(.max('hf), .width(4)) counter_1 (
    .clr(not_1_out), .load(1'b0), .up(1'b1), .count(1'b1), .clk(NotCLK), .Q({counter_1_q[3], counter_1_q_2}));  // open: D, carry
  not not_1 (not_1_out, nand_1_out);
  LED led_1 (.in(decoder_1_out0));
  LED led_2 (.in(decoder_1_out1));
  LED led_3 (.in(decoder_1_out2));
  nand nand_1 (nand_1_out, decoder_1_out5, NotCLR);
  LED led_4 (.in(decoder_1_out3));
  LED led_5 (.in(decoder_1_out4));
  not not_2 (NotCLR, PushReset);
  _7_Segment_Display u_7_segment_display_1 ();  // open: g, f, a, b, e, d, c, dp
  // BCD_to_7_Segment_decoder bcd_to_7_segment_decoder_1: pin names not known; wires that end beside it: {counter_1_q[3], counter_1_q_2}
  Decoder #(.select(3)) decoder_1 (
    .out0(decoder_1_out0), .out1(decoder_1_out1), .out2(decoder_1_out2), .out3(decoder_1_out3),
    .out4(decoder_1_out4), .out5(decoder_1_out5), .sel(counter_1_q_2), .en(1'b1));  // open: out6, out7
  not not_3 (CLR, NotCLR);
  LED led_6 (.in(counter_1_q_2[0]));
  LED led_7 (.in(counter_1_q_2[1]));
  LED led_8 (.in(counter_1_q_2[2]));
  ROM #(.addrWidth(9), .dataWidth(16)) rom_1 (
    .addr({ZeroFlag, CarryFlag, InstructionIn, counter_1_q_2}),
    .data({HLT, rom_1_data[14], RAMIn, rom_1_data[12:7], Subtract, rom_1_data[5], OutputIn, CounterEnable, rom_1_data[2:0]}));
  LED led_9 (.in(HLT));
  LED led_10 (.in(rom_1_data[14]));
  LED led_11 (.in(RAMIn));
  LED led_12 (.in(rom_1_data[12]));
  LED led_13 (.in(rom_1_data[11]));
  LED led_14 (.in(rom_1_data[10]));
  LED led_15 (.in(rom_1_data[9]));
  LED led_16 (.in(rom_1_data[8]));
  LED led_17 (.in(rom_1_data[7]));
  LED led_18 (.in(Subtract));
  LED led_19 (.in(rom_1_data[5]));
  LED led_20 (.in(OutputIn));
  LED led_21 (.in(CounterEnable));
  LED led_22 (.in(rom_1_data[2]));
  LED led_23 (.in(rom_1_data[1]));
  LED led_24 (.in(rom_1_data[0]));
  not not_4 (NotMemoryIn, rom_1_data[14]);
  not not_5 (NotRAMOut, rom_1_data[12]);
  not not_6 (NotInstructionOut, rom_1_data[11]);
  not not_7 (NotInstructionIn, rom_1_data[10]);
  not not_8 (NotAIn, rom_1_data[9]);
  not not_9 (NotAOut, rom_1_data[8]);
  not not_10 (NotEquationOut, rom_1_data[7]);
  not not_11 (NotBIn, rom_1_data[5]);
  not not_12 (NotCounterOut, rom_1_data[2]);
  not not_13 (NotJump, rom_1_data[1]);
  not not_14 (NotFlagsIn, rom_1_data[0]);

  // Notes on the sheet:
  //   contents of rom_1 (hex, n*v repeats v):
  //   4004 1408 6*0 4004 1408 4800 1200 4*0 4004 1408 4800 1020 281 0 0 0 4004 1408 4800 1020 2c1 0 0 0
  //   4004 1408 4800 2100 4*0 4004 1408 a00 5*0 4004 1408 802 5*0 4004 1408 6*0 4004 1408 6*0 4004 1408
  //   6*0 4004 1408 6*0 4004 1408 6*0 4004 1408 6*0 4004 1408 6*0 4004 1408 110 5*0 4004 1408 8000 5*0
  //   4004 1408 6*0 4004 1408 4800 1200 4*0 4004 1408 4800 1020 281 0 0 0 4004 1408 4800 1020 2c1 0 0 0
  //   4004 1408 4800 2100 4*0 4004 1408 a00 5*0 4004 1408 802 5*0 4004 1408 802 5*0 4004 1408 6*0 4004
  //   1408 6*0 4004 1408 6*0 4004 1408 6*0 4004 1408 6*0 4004 1408 6*0 4004 1408 110 5*0 4004 1408 8000
  //   5*0 4004 1408 6*0 4004 1408 4800 1200 4*0 4004 1408 4800 1020 281 0 0 0 4004 1408 4800 1020 2c1 0 0
  //   0 4004 1408 4800 2100 4*0 4004 1408 a00 5*0 4004 1408 802 5*0 4004 1408 6*0 4004 1408 802 5*0 4004
  //   1408 6*0 4004 1408 6*0 4004 1408 6*0 4004 1408 6*0 4004 1408 6*0 4004 1408 110 5*0 4004 1408 8000
  //   5*0 4004 1408 6*0 4004 1408 4800 1200 4*0 4004 1408 4800 1020 281 0 0 0 4004 1408 4800 1020 2c1 0 0
  //   0 4004 1408 4800 2100 4*0 4004 1408 a00 5*0 4004 1408 802 5*0 4004 1408 802 5*0 4004 1408 802 5*0
  //   4004 1408 6*0 4004 1408 6*0 4004 1408 6*0 4004 1408 6*0 4004 1408 6*0 4004 1408 110 5*0 4004 1408
  //   8000
endmodule
